// Logisim project MIPS-ROMney-2017.circ as structural Verilog
module SYSTEM2 (
  input  [7:0] in_1,
  input  On_Off,
  input  in_3,
  input  _0,
  input  _1,
  input  _2,
  input  _3,
  input  _4,
  input  _5,
  input  _6,
  input  _7,
  input  _8,
  input  _9,
  output [7:0] out_14,
  output [3:0] out_15,
  output [3:0] out_16,
  output [3:0] out_17,
  output [7:0] out_18,
  output [7:0] out_19,
  output [7:0] out_20,
  output [7:0] out_21,
  output [3:0] out_22,
  output [7:0] out_23,
  output [7:0] out_24,
  output [7:0] out_25,
  output [7:0] out_26,
  output [3:0] out_27,
  output [3:0] out_28,
  output [3:0] out_29,
  output [3:0] out_30,
  output [7:0] out_31,
  output [7:0] out_32,
  output [7:0] out_33,
  output [7:0] out_34,
  output [7:0] out_35,
  output [7:0] out_36,
  output [7:0] out_37,
  output [7:0] out_38,
  output [7:0] out_39,
  output [7:0] out_40,
  output [7:0] out_41,
  output [7:0] out_42
);

  wire and_1_out, and_2_out, and_3_out, and_4_out, and_5_out, and_6_out, and_7_out, and_8_out, and_10_out,
       and_11_out, and_12_out, and_13_out, and_14_out, and_15_out, and_16_out, and_17_out, and_18_out,
       and_19_out, and_20_out, button_1_out, clock_1_out, decoder_1_out0, decoder_1_out1, decoder_1_out2,
       decoder_1_out19, decoder_1_out20, decoder_1_out21, decoder_1_out22, decoder_1_out23, decoder_1_out24,
       decoder_1_out25, decoder_1_out26, decoder_1_out27, decoder_1_out28, decoder_1_out29, decoder_1_out30,
       decoder_1_out31, decoder_2_out19, decoder_2_out20, decoder_2_out21, decoder_2_out22, decoder_2_out23,
       decoder_2_out24, decoder_2_out25, decoder_2_out26, decoder_2_out27, decoder_2_out28, decoder_2_out29,
       decoder_2_out30, decoder_2_out31, decoder_3_out19, decoder_3_out20, decoder_3_out21, decoder_3_out22,
       decoder_3_out23, decoder_3_out24, decoder_3_out25, decoder_3_out26, decoder_3_out27, decoder_3_out28,
       decoder_3_out29, decoder_3_out30, decoder_3_out31, decoder_4_out19, decoder_4_out20, decoder_4_out21,
       decoder_4_out22, decoder_4_out23, decoder_4_out24, decoder_4_out25, decoder_4_out26, decoder_4_out27,
       decoder_4_out28, decoder_4_out29, decoder_4_out30, decoder_4_out31, decoder_5_out19, decoder_5_out20,
       decoder_5_out21, decoder_5_out22, decoder_5_out23, decoder_5_out24, decoder_5_out25, decoder_5_out26,
       decoder_5_out27, decoder_5_out28, decoder_5_out29, decoder_5_out30, decoder_5_out31, decoder_6_out19,
       decoder_6_out20, decoder_6_out21, decoder_6_out22, decoder_6_out23, decoder_6_out24, decoder_6_out25,
       decoder_6_out26, decoder_6_out27, decoder_6_out28, decoder_6_out29, decoder_6_out30, decoder_6_out31,
       decoder_7_out19, decoder_7_out20, decoder_7_out21, decoder_7_out22, decoder_7_out23, decoder_7_out24,
       decoder_7_out25, decoder_7_out26, decoder_7_out27, decoder_7_out28, decoder_7_out29, decoder_7_out30,
       decoder_7_out31, decoder_8_out20, decoder_8_out21, decoder_8_out22, decoder_8_out23, decoder_8_out24,
       decoder_8_out25, decoder_8_out26, decoder_8_out27, decoder_8_out28, decoder_8_out29, decoder_8_out30,
       decoder_8_out31, decoder_9_out19, decoder_9_out20, decoder_9_out21, decoder_9_out22, decoder_9_out23,
       decoder_9_out24, decoder_9_out25, decoder_9_out26, decoder_9_out27, decoder_9_out28, decoder_9_out29,
       decoder_9_out30, decoder_9_out31, digi1_1_a, digi1_1_b, digi1_1_c, digi1_1_d, digi1_1_e, digi1_1_f,
       digi1_1_g, digi2_1_a, digi2_1_b, digi2_1_c, digi2_1_d, digi2_1_e, digi2_1_f, digi2_1_g, digi3_1_a,
       digi3_1_b, digi3_1_c, digi3_1_d, digi3_1_e, digi3_1_f, digi3_1_g, Llock_out, not_1_out, not_2_out,
       not_3_out, not_4_out, not_5_out, not_6_out, not_7_out, not_8_out, not_9_out, not_10_out, or_1_out,
       or_2_out, or_3_out, or_4_out, or_5_out, or_7_out, or_8_out, or_9_out, or_10_out, or_11_out, or_13_out,
       or_14_out, or_15_out, or_16_out, or_17_out, or_18_out, or_19_out, or_20_out, or_21_out, or_22_out,
       or_23_out, or_24_out, or_25_out, or_26_out, or_27_out, or_28_out, or_29_out, or_30_out, or_31_out,
       or_32_out, or_33_out, or_34_out, or_35_out, or_36_out, or_37_out, or_38_out, or_39_out, or_40_out,
       or_41_out, or_42_out, or_43_out, or_44_out, or_45_out, or_46_out, or_47_out, or_48_out, or_49_out,
       or_50_out, or_51_out, or_52_out, or_53_out, Rlock_out, rwbit_1_out_3, voteromny2017_1_out_2;
  wire [0:0] not_11_out;
  wire [1:0] and_9_out;
  wire [2:0] alu_1_out_6;
  wire [3:0] inc_1_out_3, multiplexer_35_out, multiplexer_39_out;
  wire [7:0] alu_1_out_5, alupicker_1_out_4, d1_1_out_3, multiplexer_5_out, multiplexer_8_out,
       multiplexer_13_out, multiplexer_16_out, multiplexer_17_out, multiplexer_25_out, multiplexer_47_out,
       multiplexer_48_out, multiplexer_49_out, multiplexer_50_out, multiplexer_52_out, numpad_1_out_11;
  wire [8:0] cun_1_out_5;
  wire [13:12] multiplexer_9_out;
  wire [31:0] multiplexer_1_out, multiplexer_2_out, multiplexer_3_out, multiplexer_4_out,
       voteromny2017_1_out_3, voteromny2017_1_out_7, voteromny2017_1_out_11, voteromny2017_1_out_15;

  Button button_1 (.out(button_1_out));
  buf or_1 (or_1_out, clock_1_out);  // OR_Gate
  VoteRomny2017 voteromny2017_1 (
    .in_1(button_1_out), .out_2(voteromny2017_1_out_2), .out_3(voteromny2017_1_out_3[7:0]),
    .out_4(voteromny2017_1_out_3[15:8]), .out_5(voteromny2017_1_out_3[23:16]),
    .out_6(voteromny2017_1_out_3[31:24]), .out_7(voteromny2017_1_out_7[7:0]),
    .out_8(voteromny2017_1_out_7[15:8]), .out_9(voteromny2017_1_out_7[23:16]),
    .out_10(voteromny2017_1_out_7[31:24]), .out_11(voteromny2017_1_out_11[7:0]),
    .out_12(voteromny2017_1_out_11[15:8]), .out_13(voteromny2017_1_out_11[23:16]),
    .out_14(voteromny2017_1_out_11[31:24]), .out_15(voteromny2017_1_out_15[7:0]),
    .out_16(voteromny2017_1_out_15[15:8]), .out_17(voteromny2017_1_out_15[23:16]),
    .out_18(voteromny2017_1_out_15[31:24]));
  or or_2 (or_2_out, On_Off, voteromny2017_1_out_2);
  Multiplexer #(.width(32), .enable("false")) multiplexer_1 (
    .in0(voteromny2017_1_out_3), .in1({32{1'b0}}), .out(multiplexer_1_out), .sel(On_Off));
  Multiplexer #(.width(32), .enable("false")) multiplexer_2 (
    .in0(voteromny2017_1_out_7), .in1({32{1'b0}}), .out(multiplexer_2_out), .sel(On_Off));
  Multiplexer #(.width(32), .enable("false")) multiplexer_3 (
    .in0(voteromny2017_1_out_11), .in1({32{1'b0}}), .out(multiplexer_3_out), .sel(On_Off));
  Multiplexer #(.width(32), .enable("false")) multiplexer_4 (
    .in0(voteromny2017_1_out_15), .in1({32{1'b0}}), .out(multiplexer_4_out), .sel(On_Off));
  digi1 digi1_1 (
    .i8(out_31[7]), .i7(out_31[6]), .i6(out_31[5]), .i5(out_31[4]), .i4(out_31[3]), .i3(out_31[2]),
    .i2(out_31[1]), .i1(out_31[0]), .A(digi1_1_a), .B(digi1_1_b), .C(digi1_1_c), .D(digi1_1_d),
    .E(digi1_1_e), .F(digi1_1_f), .G(digi1_1_g));
  _7_Segment_Display u_7_segment_display_1 (
    .g(digi1_1_g), .f(digi1_1_f), .a(digi1_1_a), .b(digi1_1_b), .e(digi1_1_e), .d(digi1_1_d), .c(digi1_1_c));  // open: dp
  RAM ram_1 (
    .in_1(out_22), .in_2(out_14), .R_W_R_0_W_1(or_4_out), .in_4(clock_1_out), .out_22(out_26),
    .in_6(multiplexer_1_out[7:0]), .in_5(or_2_out), .in_7(multiplexer_1_out[15:8]),
    .in_8(multiplexer_1_out[23:16]), .in_9(multiplexer_1_out[31:24]), .in_10(multiplexer_2_out[7:0]),
    .in_11(multiplexer_2_out[15:8]), .in_12(multiplexer_2_out[23:16]), .in_13(multiplexer_2_out[31:24]),
    .in_14(multiplexer_3_out[7:0]), .in_15(multiplexer_3_out[15:8]), .in_16(multiplexer_3_out[23:16]),
    .in_17(multiplexer_3_out[31:24]), .in_18(multiplexer_4_out[7:0]), .in_19(multiplexer_4_out[15:8]),
    .in_20(multiplexer_4_out[23:16]), .in_21(multiplexer_4_out[31:24]));
  _7_Segment_Display u_7_segment_display_2 (
    .g(digi2_1_g), .f(digi2_1_f), .a(digi2_1_a), .b(digi2_1_b), .e(digi2_1_e), .d(digi2_1_d), .c(digi2_1_c));  // open: dp
  Multiplexer #(.width(8), .enable("false")) multiplexer_5 (
    .in1({8{1'b0}}), .out(multiplexer_5_out), .sel(On_Off));  // open: in0
  Multiplexer #(.width(8), .enable("false")) multiplexer_6 (.in1({8{1'b0}}), .out(out_40), .sel(On_Off));  // open: in0
  buf or_3 (or_3_out, clock_1_out);  // OR_Gate
  or or_4 (or_4_out, in_3, rwbit_1_out_3);
  digi2 digi2_1 (
    .i8(out_31[7]), .i7(out_31[6]), .i6(out_31[5]), .i5(out_31[4]), .i4(out_31[3]), .i3(out_31[2]),
    .i2(out_31[1]), .i1(out_31[0]), .A(digi2_1_a), .B(digi2_1_b), .C(digi2_1_c), .D(digi2_1_d),
    .E(digi2_1_e), .F(digi2_1_f), .G(digi2_1_g));
  NUMPAD numpad_1 (
    ._0(_0), ._1(_1), ._2(_2), ._3(_3), ._4(_4), ._5(_5), ._6(_6), ._7(_7), ._8(_8), ._9(_9),
    .out_11(numpad_1_out_11));
  Multiplexer #(.width(8), .enable("false")) multiplexer_7 (.in1(in_1), .sel(in_3));  // open: in0, out
  Multiplexer #(.width(8), .enable("false")) multiplexer_8 (
    .in0(out_26), .out(multiplexer_8_out), .sel(rwbit_1_out_3));  // open: in1
  RWbit rwbit_1 (.out_3(rwbit_1_out_3), .clock_bit(or_3_out), .in_2(multiplexer_9_out[12]));
  Multiplexer #(.enable("false")) multiplexer_9 (.in1(1'b0), .out(multiplexer_9_out[12]), .sel(On_Off));  // open: in0
  dispbyte dispbyte_1 (.clock_bit(clock_1_out), .in_2(out_32), .out_3(out_31));
  digi3 digi3_1 (
    .i8(out_31[7]), .i7(out_31[6]), .i6(out_31[5]), .i5(out_31[4]), .i4(out_31[3]), .i3(out_31[2]),
    .i2(out_31[1]), .i1(out_31[0]), .A(digi3_1_a), .B(digi3_1_b), .C(digi3_1_c), .D(digi3_1_d),
    .E(digi3_1_e), .F(digi3_1_f), .G(digi3_1_g));
  _7_Segment_Display u_7_segment_display_3 (
    .g(digi3_1_g), .f(digi3_1_f), .a(digi3_1_a), .b(digi3_1_b), .e(digi3_1_e), .d(digi3_1_d), .c(digi3_1_c));  // open: dp
  numpadbuffer numpadbuffer_1 (.clock_bit(clock_1_out), .in_2(numpad_1_out_11), .out_3(out_33));
  buf or_5 (or_5_out, clock_1_out);  // OR_Gate
  Multiplexer #(.width(8), .enable("false")) multiplexer_10 (
    .in1(out_14), .out(multiplexer_8_out), .sel(rwbit_1_out_3));  // open: in0
  Multiplexer #(.width(8), .enable("false")) multiplexer_11 (
    .in1({8{1'b0}}), .out(multiplexer_8_out), .sel(On_Off));  // open: in0
  Multiplexer #(.width(8), .enable("false")) multiplexer_12 (
    .in1(multiplexer_13_out), .out(out_14), .sel(not_2_out));  // open: in0
  Multiplexer #(.width(8), .enable("false")) multiplexer_13 (
    .in0(out_20), .out(multiplexer_13_out), .sel(rwbit_1_out_3));  // open: in1
  Multiplexer #(.width(8), .enable("false")) multiplexer_14 (.in1(out_20), .out(out_14));  // open: in0, sel
  DRn drn_1 (.clock_bit(or_5_out), .in_2(multiplexer_8_out), .out_3(out_20));
  ARn arn_1 (.clock_bit(or_3_out), .in_2(out_27), .out_3(out_22));
  Multiplexer #(.width(4), .enable("false")) multiplexer_15 (.in1(4'b0000), .out(out_22), .sel(On_Off));  // open: in0
  and and_1 (and_1_out, decoder_3_out21, out_25[4]);
  or or_6 (and_9_out[1], cun_1_out_5[5], cun_1_out_5[7], cun_1_out_5[3], decoder_4_out21);
  not not_1 (not_1_out, out_25[4]);
  and and_2 (and_2_out, decoder_3_out21, not_1_out);
  Multiplexer #(.width(8), .enable("false")) multiplexer_16 (
    .in1(out_34), .out(multiplexer_16_out), .sel(and_9_out[1]));  // open: in0
  buf or_7 (or_7_out, and_1_out);  // OR_Gate
  Multiplexer #(.width(8), .enable("false")) multiplexer_17 (
    .in1(out_34), .out(multiplexer_17_out), .sel(and_9_out[1]));  // open: in0
  not not_2 (not_2_out, multiplexer_9_out[13]);
  Multiplexer #(.width(8), .enable("false")) multiplexer_18 (
    .in1(out_33), .out(out_14), .sel(multiplexer_9_out[13]));  // open: in0
  not not_3 (not_3_out, out_25[3]);
  and and_3 (and_3_out, not_3_out, decoder_3_out22);
  buf or_8 (or_8_out, and_2_out);  // OR_Gate
  Multiplexer #(.width(8), .enable("false")) multiplexer_19 (
    .in1(multiplexer_16_out), .out(multiplexer_5_out), .sel(or_9_out));  // open: in0
  or or_9 (or_9_out, decoder_4_out21, and_13_out, and_5_out);
  Multiplexer #(.width(8), .enable("false")) multiplexer_20 (
    .in1(multiplexer_17_out), .out(out_40), .sel(or_10_out));  // open: in0
  or or_10 (or_10_out, or_11_out, and_6_out);
  or or_11 (or_11_out, and_10_out, and_9_out[0], and_14_out);
  and and_4 (and_4_out, out_25[3], decoder_3_out22);
  Multiplexer #(.width(8), .enable("false")) multiplexer_21 (
    .in1(out_34), .out(multiplexer_5_out), .sel(or_8_out));  // open: in0
  Multiplexer #(.width(8), .enable("false")) multiplexer_22 (.in1(out_34), .out(out_40), .sel(or_7_out));  // open: in0
  buf or_12 (multiplexer_9_out[12], or_13_out);  // OR_Gate
  and and_5 (and_5_out, decoder_6_out21, not_4_out);
  and and_6 (and_6_out, decoder_6_out21, out_25[4]);
  D0 d0_1 (.clock_bit(or_1_out), .in_2(multiplexer_5_out), .out_3(out_38));
  D1 d1_1 (.clock_bit(or_1_out), .in_2(out_40), .out_3(d1_1_out_3));
  Multiplexer #(.width(4), .enable("false")) multiplexer_23 (.in1(out_29), .out(out_27), .sel(or_17_out));  // open: in0
  Multiplexer #(.width(8), .enable("false")) multiplexer_24 (
    .in1(out_34), .out(out_32), .sel(decoder_1_out19));  // open: in0
  or or_13 (or_13_out, decoder_5_out21, decoder_5_out20);
  not not_4 (not_4_out, out_25[4]);
  or or_14 (or_14_out, or_19_out, and_8_out, not_5_out, out_25[3]);
  Multiplexer #(.width(8), .enable("false")) multiplexer_25 (
    .in1(out_38), .out(multiplexer_25_out), .sel(or_14_out));  // open: in0
  Multiplexer #(.width(8), .enable("false")) multiplexer_26 (
    .in1(d1_1_out_3), .out(out_39), .sel(or_15_out));  // open: in0
  or or_15 (or_15_out, or_19_out, and_7_out, and_9_out[0], out_25[3]);
  Multiplexer #(.width(8), .enable("false")) multiplexer_27 (.in1(out_19), .out(out_14), .sel(or_16_out));  // open: in0
  buf or_16 (or_16_out, decoder_5_out21);  // OR_Gate
  or or_17 (or_17_out, decoder_1_out1, or_23_out);
  not not_5 (not_5_out, and_9_out[0]);
  alupicker alupicker_1 (.out_5(out_41), .out_4(alupicker_1_out_4), .in_2(out_38), .in_1(and_9_out), .in_3(out_39));
  buf or_18 (or_18_out, clock_1_out);  // OR_Gate
  Multiplexer #(.width(4), .enable("false")) multiplexer_28 (.in1(4'b0000), .out(out_30), .sel(On_Off));  // open: in0
  or or_19 (or_19_out, or_30_out, or_26_out);
  Multiplexer #(.width(8), .enable("false")) multiplexer_29 (
    .in1(multiplexer_25_out), .out(out_34), .sel(cun_1_out_5[0]));  // open: in0
  Clock clock_1 (.out(clock_1_out));
  Multiplexer #(.width(8), .enable("false")) multiplexer_30 (.in1(out_34), .out(out_23), .sel(or_21_out));  // open: in0
  MAR mar_1 (.out_3(out_29), .clock_bit(or_18_out), .in_2(out_30));
  Multiplexer #(.width(8), .enable("false")) multiplexer_31 (.in1({8{1'b0}}), .out(out_23), .sel(On_Off));  // open: in0
  MBR mbr_1 (.clock_bit(or_20_out), .in_2(out_23), .out_3(out_19));
  buf or_20 (or_20_out, clock_1_out);  // OR_Gate
  Multiplexer #(.width(8), .enable("false")) multiplexer_32 (.in1(out_14), .out(out_23), .sel(or_22_out));  // open: in0
  or or_21 (or_21_out, decoder_1_out19, decoder_5_out20);
  Multiplexer #(.width(4), .enable("false")) multiplexer_33 (
    .in1(multiplexer_39_out), .out(out_30), .sel(or_23_out));  // open: in0
  Multiplexer #(.width(8), .enable("false")) multiplexer_34 (
    .in1(out_39), .out(out_34), .sel(cun_1_out_5[0]));  // open: in0
  Multiplexer #(.width(4), .enable("false")) multiplexer_35 (
    .in1(4'b0000), .out(multiplexer_35_out), .sel(On_Off));  // open: in0
  or or_22 (or_22_out, decoder_3_out20, multiplexer_9_out[13], decoder_1_out1);
  Multiplexer #(.width(4), .enable("false")) multiplexer_36 (
    .in1(multiplexer_39_out), .out(out_30), .sel(or_47_out));  // open: in0
  or or_23 (or_23_out, decoder_5_out20, or_24_out, decoder_3_out21, decoder_5_out19, decoder_1_out0);
  or or_24 (or_24_out, decoder_3_out20, decoder_3_out19);
  Multiplexer #(.width(4), .enable("false")) multiplexer_37 (
    .in0(inc_1_out_3), .in1(multiplexer_35_out), .out(out_17), .sel(or_44_out));
  Multiplexer #(.width(8), .enable("false")) multiplexer_38 (.in1(out_19), .out(out_34), .sel(or_25_out));  // open: in0
  or or_25 (or_25_out, decoder_3_out21, decoder_3_out22, decoder_8_out20);
  or or_26 (or_26_out, decoder_9_out19, decoder_9_out20);
  buf or_27 (or_27_out, clock_1_out);  // OR_Gate
  Multiplexer #(.width(4), .enable("false")) multiplexer_39 (
    .in1(out_16), .out(multiplexer_39_out), .sel(or_28_out));  // open: in0
  or or_28 (or_28_out, decoder_1_out0, or_47_out);
  and and_7 (and_7_out, decoder_5_out20, out_25[3]);
  and and_8 (and_8_out, decoder_5_out20, not_6_out);
  or or_29 (or_29_out, or_47_out, or_52_out);
  PC pc_1 (.clock_bit(or_27_out), .in_2(out_17), .out_3(out_16));
  or or_30 (or_30_out, decoder_2_out19, decoder_2_out20);
  or Rlock (Rlock_out, decoder_9_out19, decoder_2_out19, decoder_4_out19, decoder_6_out19, and_12_out);
  not not_6 (not_6_out, out_25[3]);
  buf or_31 (or_31_out, Rlock_out);  // OR_Gate
  Multiplexer #(.select(2), .width(8), .enable("false")) multiplexer_40 (
    .in1(multiplexer_25_out), .in2(out_39), .out(out_41), .sel(out_25[5:4]));  // open: in0, in3
  Multiplexer #(.select(2), .width(8), .enable("false")) multiplexer_41 (
    .in1(out_39), .in2(multiplexer_25_out), .out(alupicker_1_out_4), .sel(out_25[5:4]));  // open: in0, in3
  INC inc_1 (.in_1(out_16), .in_2(or_29_out), .out_3(inc_1_out_3));
  buf or_32 (or_32_out, clock_1_out);  // OR_Gate
  Multiplexer #(.width(8), .enable("false")) multiplexer_42 (
    .in1(out_19), .out(out_21), .sel(decoder_1_out2));  // open: in0
  or or_33 (or_33_out, or_49_out, or_47_out, or_45_out);
  Multiplexer #(.width(4), .enable("false")) multiplexer_43 (
    .in0(out_25[3:0]), .out(multiplexer_39_out), .sel(or_34_out));  // open: in1
  or or_34 (or_34_out, or_47_out, decoder_1_out0);
  or Llock (Llock_out, decoder_9_out20, decoder_2_out20, decoder_4_out20, decoder_6_out20, and_11_out);
  buf or_35 (or_35_out, Llock_out);  // OR_Gate
  Multiplexer #(.width(8), .enable("false")) multiplexer_44 (
    .in1(alupicker_1_out_4), .out(out_34), .sel(or_35_out));  // open: in0
  Multiplexer #(.width(8), .enable("false")) multiplexer_45 (.in1(out_41), .out(out_34), .sel(or_31_out));  // open: in0
  or or_36 (or_36_out, cun_1_out_5[1], cun_1_out_5[5], cun_1_out_5[8]);
  Multiplexer #(.width(8), .enable("false")) multiplexer_46 (.in1({8{1'b0}}), .out(out_21), .sel(On_Off));  // open: in0
  CUn cun_1 (
    .out_5(cun_1_out_5), .in_1(out_25), .in_2(clock_1_out), .out_6(out_15), .in_4(or_37_out),
    .resetter(or_39_out));
  IR ir_1 (.out_4(out_25), .in_3(or_33_out), .clock_bit(or_32_out), .in_1(out_21));
  or or_37 (or_37_out, or_45_out, or_47_out, or_38_out, or_49_out);
  or or_38 (or_38_out, On_Off, decoder_7_out19);
  Multiplexer #(.width(8), .enable("false")) multiplexer_47 (
    .in1(out_34), .out(multiplexer_47_out), .sel(Rlock_out));  // open: in0
  Multiplexer #(.width(8), .enable("false")) multiplexer_48 (
    .in0(multiplexer_50_out), .in1({8{1'b0}}), .out(multiplexer_48_out), .sel(On_Off));
  Multiplexer #(.width(8), .enable("false")) multiplexer_49 (
    .in0(multiplexer_47_out), .in1({8{1'b0}}), .out(multiplexer_49_out), .sel(On_Off));
  and and_9 (and_9_out[0], out_25[5], cun_1_out_5[5]);
  or or_39 (or_39_out, or_47_out, or_40_out, or_49_out);
  or or_40 (or_40_out, On_Off, or_45_out);
  Multiplexer #(.width(8), .enable("false")) multiplexer_50 (
    .in1(out_34), .out(multiplexer_50_out), .sel(Llock_out));  // open: in0
  buf or_41 (or_41_out, clock_1_out);  // OR_Gate
  buf or_42 (or_42_out, clock_1_out);  // OR_Gate
  and and_10 (and_10_out, cun_1_out_5[4], out_25[4]);
  or or_43 (or_43_out, decoder_4_out21, decoder_6_out21);
  L l_1 (.clock_bit(or_41_out), .in_2(multiplexer_48_out), .out_3(out_35));
  R r_1 (.clock_bit(or_42_out), .in_2(multiplexer_49_out), .out_3(out_42));
  or or_44 (or_44_out, On_Off, or_51_out, or_53_out);
  or or_45 (or_45_out, decoder_7_out20, decoder_7_out21, decoder_7_out22, decoder_7_out23, decoder_7_out24, decoder_7_out25, decoder_7_out26, decoder_7_out27, decoder_7_out28, decoder_7_out29, decoder_7_out30, decoder_7_out31);
  and and_11 (and_11_out, decoder_5_out20, not_7_out);
  and and_12 (and_12_out, decoder_5_out20, out_25[4]);
  ALU alu_1 (
    .in_1(out_35), ._0_add_1_subtract(or_36_out), .in_3(clock_1_out), .in_4(out_42), .out_5(alu_1_out_5),
    .out_6(alu_1_out_6));
  not not_7 (not_7_out, out_25[4]);
  Multiplexer #(.width(8), .enable("false")) multiplexer_51 (.in1(out_37), .out(out_34), .sel(or_43_out));  // open: in0
  buf or_46 (or_46_out, clock_1_out);  // OR_Gate
  Multiplexer #(.width(8), .enable("false")) multiplexer_52 (
    .in0(alu_1_out_5), .in1({8{1'b0}}), .out(multiplexer_52_out), .sel(On_Off));
  Decoder #(.select(5)) decoder_1 (
    .out0(decoder_1_out0), .out1(decoder_1_out1), .out2(decoder_1_out2), .out19(decoder_1_out19),
    .out20(decoder_1_out20), .out21(decoder_1_out21), .out22(decoder_1_out22), .out23(decoder_1_out23),
    .out24(decoder_1_out24), .out25(decoder_1_out25), .out26(decoder_1_out26), .out27(decoder_1_out27),
    .out28(decoder_1_out28), .out29(decoder_1_out29), .out30(decoder_1_out30), .out31(decoder_1_out31),
    .sel({cun_1_out_5[0], out_15}));  // open: out3, out4, out5, out6, out7, out8, out9, out10, out11, out12, out13, out14, out15, out16, out17, out18, en
  Decoder #(.select(5)) decoder_2 (
    .out19(decoder_2_out19), .out20(decoder_2_out20), .out21(decoder_2_out21), .out22(decoder_2_out22),
    .out23(decoder_2_out23), .out24(decoder_2_out24), .out25(decoder_2_out25), .out26(decoder_2_out26),
    .out27(decoder_2_out27), .out28(decoder_2_out28), .out29(decoder_2_out29), .out30(decoder_2_out30),
    .out31(decoder_2_out31), .sel({cun_1_out_5[1], out_15}));  // open: out0, out1, out2, out3, out4, out5, out6, out7, out8, out9, out10, out11, out12, out13, out14, out15, out16, out17, out18, en
  Decoder #(.select(5)) decoder_3 (
    .out19(decoder_3_out19), .out20(decoder_3_out20), .out21(decoder_3_out21), .out22(decoder_3_out22),
    .out23(decoder_3_out23), .out24(decoder_3_out24), .out25(decoder_3_out25), .out26(decoder_3_out26),
    .out27(decoder_3_out27), .out28(decoder_3_out28), .out29(decoder_3_out29), .out30(decoder_3_out30),
    .out31(decoder_3_out31), .sel({cun_1_out_5[2], out_15}));  // open: out0, out1, out2, out3, out4, out5, out6, out7, out8, out9, out10, out11, out12, out13, out14, out15, out16, out17, out18, en
  Decoder #(.select(5)) decoder_4 (
    .out19(decoder_4_out19), .out20(decoder_4_out20), .out21(decoder_4_out21), .out22(decoder_4_out22),
    .out23(decoder_4_out23), .out24(decoder_4_out24), .out25(decoder_4_out25), .out26(decoder_4_out26),
    .out27(decoder_4_out27), .out28(decoder_4_out28), .out29(decoder_4_out29), .out30(decoder_4_out30),
    .out31(decoder_4_out31), .sel({cun_1_out_5[3], out_15}));  // open: out0, out1, out2, out3, out4, out5, out6, out7, out8, out9, out10, out11, out12, out13, out14, out15, out16, out17, out18, en
  Decoder #(.select(5)) decoder_5 (
    .out19(decoder_5_out19), .out20(decoder_5_out20), .out21(decoder_5_out21), .out22(decoder_5_out22),
    .out23(decoder_5_out23), .out24(decoder_5_out24), .out25(decoder_5_out25), .out26(decoder_5_out26),
    .out27(decoder_5_out27), .out28(decoder_5_out28), .out29(decoder_5_out29), .out30(decoder_5_out30),
    .out31(decoder_5_out31), .sel({cun_1_out_5[4], out_15}));  // open: out0, out1, out2, out3, out4, out5, out6, out7, out8, out9, out10, out11, out12, out13, out14, out15, out16, out17, out18, en
  Decoder #(.select(5)) decoder_6 (
    .out19(decoder_6_out19), .out20(decoder_6_out20), .out21(decoder_6_out21), .out22(decoder_6_out22),
    .out23(decoder_6_out23), .out24(decoder_6_out24), .out25(decoder_6_out25), .out26(decoder_6_out26),
    .out27(decoder_6_out27), .out28(decoder_6_out28), .out29(decoder_6_out29), .out30(decoder_6_out30),
    .out31(decoder_6_out31), .sel({cun_1_out_5[5], out_15}));  // open: out0, out1, out2, out3, out4, out5, out6, out7, out8, out9, out10, out11, out12, out13, out14, out15, out16, out17, out18, en
  Decoder #(.select(5)) decoder_7 (
    .out19(decoder_7_out19), .out20(decoder_7_out20), .out21(decoder_7_out21), .out22(decoder_7_out22),
    .out23(decoder_7_out23), .out24(decoder_7_out24), .out25(decoder_7_out25), .out26(decoder_7_out26),
    .out27(decoder_7_out27), .out28(decoder_7_out28), .out29(decoder_7_out29), .out30(decoder_7_out30),
    .out31(decoder_7_out31), .sel({cun_1_out_5[6], out_15}));  // open: out0, out1, out2, out3, out4, out5, out6, out7, out8, out9, out10, out11, out12, out13, out14, out15, out16, out17, out18, en
  Decoder #(.select(5)) decoder_8 (
    .out19(multiplexer_9_out[13]), .out20(decoder_8_out20), .out21(decoder_8_out21), .out22(decoder_8_out22),
    .out23(decoder_8_out23), .out24(decoder_8_out24), .out25(decoder_8_out25), .out26(decoder_8_out26),
    .out27(decoder_8_out27), .out28(decoder_8_out28), .out29(decoder_8_out29), .out30(decoder_8_out30),
    .out31(decoder_8_out31), .sel({cun_1_out_5[7], out_15}));  // open: out0, out1, out2, out3, out4, out5, out6, out7, out8, out9, out10, out11, out12, out13, out14, out15, out16, out17, out18, en
  A a_1 (.clock_bit(or_46_out), .in_2(multiplexer_52_out), .out_3(out_37));
  Decoder #(.select(5)) decoder_9 (
    .out19(decoder_9_out19), .out20(decoder_9_out20), .out21(decoder_9_out21), .out22(decoder_9_out22),
    .out23(decoder_9_out23), .out24(decoder_9_out24), .out25(decoder_9_out25), .out26(decoder_9_out26),
    .out27(decoder_9_out27), .out28(decoder_9_out28), .out29(decoder_9_out29), .out30(decoder_9_out30),
    .out31(decoder_9_out31), .sel({cun_1_out_5[8], out_15}));  // open: out0, out1, out2, out3, out4, out5, out6, out7, out8, out9, out10, out11, out12, out13, out14, out15, out16, out17, out18, en
  and and_13 (and_13_out, not_8_out, cun_1_out_5[7]);
  not not_8 (not_8_out, out_25[3]);
  and and_14 (and_14_out, cun_1_out_5[7], out_25[3]);
  or or_47 (or_47_out, decoder_1_out20, or_48_out);
  or or_48 (or_48_out, decoder_3_out22, decoder_4_out22, or_50_out);
  or or_49 (or_49_out, or_52_out, or_51_out);
  and and_15 (and_15_out, decoder_2_out22, not_9_out);
  not not_9 (not_9_out, alu_1_out_6[0]);
  or or_50 (or_50_out, decoder_5_out22, decoder_6_out22, decoder_8_out21);
  or or_51 (or_51_out, and_15_out, and_16_out);
  and and_16 (and_16_out, decoder_9_out22, alu_1_out_6[0]);
  or or_52 (or_52_out, and_17_out, and_18_out);
  and and_17 (and_17_out, decoder_2_out22, alu_1_out_6[0]);
  and and_18 (and_18_out, decoder_9_out22, not_10_out);
  not not_10 (not_10_out, alu_1_out_6[0]);
  Multiplexer #(.select(2), .width(4), .enable("false")) multiplexer_53 (
    .in1(out_25[3:0]), .in2(out_25[3:0]), .out(multiplexer_35_out), .sel({alu_1_out_6[0], not_11_out[0]}));  // open: in0, in3
  not not_11 (not_11_out[0], alu_1_out_6[0]);
  and and_19 (and_19_out, alu_1_out_6[0], cun_1_out_5[8], decoder_9_out21);
  and and_20 (and_20_out, not_11_out[0], cun_1_out_5[1], decoder_2_out21);
  or or_53 (or_53_out, and_20_out, and_19_out);

  assign out_18 = out_14;
  assign out_24 = out_14;
  assign out_28 = out_27;

  // Notes on the sheet:
  //   ROM
  //   write mode
  //   01
  //   10
  //   we only do PC to MAR
  //   incrementor
  //   LOAD D1 or D0
  //   STORE
  //   REMOVE
endmodule

module CUn (
  input  [7:0] in_1,
  input  in_2,
  input  resetter,
  input  in_4,
  output [8:0] out_5,
  output [3:0] out_6
);

  wire not_2_out, not_3_out, not_4_out, not_5_out, not_6_out, not_7_out, not_8_out, not_9_out, OP00_out,
       OP01_out, OP10_out, OP11_out, or_1_out, xor_1_out, xor_2_out;
  wire [3:0] cuincrementor_1_out_3, multiplexer_1_out, not_1_out;

  assign not_1_out = ~4'b1111;  // NOT_Gate not_1, 4 bits wide
  Multiplexer #(.width(4), .enable("false")) multiplexer_1 (
    .in0(cuincrementor_1_out_3), .in1(not_1_out), .out(multiplexer_1_out), .sel(resetter));
  or or_1 (or_1_out, in_1[5], in_1[4]);
  not not_2 (not_2_out, or_1_out);
  and OP11 (OP11_out, in_1[7], in_1[6]);
  xor xor_1 (xor_1_out, in_1[7], in_1[6]);
  not not_3 (not_3_out, in_1[7]);
  and OP00 (OP00_out, not_3_out, not_4_out);
  not not_4 (not_4_out, in_1[6]);
  xor xor_2 (xor_2_out, in_1[5], in_1[4]);
  not not_5 (not_5_out, xor_2_out);
  not not_6 (not_6_out, not_5_out);
  not not_7 (not_7_out, in_1[5]);
  D_Flip_Flop #(.trigger("falling")) d_ff_1 (
    .D(multiplexer_1_out[0]), .clk(in_2), .Q(out_6[0]));  // open: Qn, preset, reset
  D_Flip_Flop #(.trigger("falling")) d_ff_2 (
    .D(multiplexer_1_out[1]), .clk(in_2), .Q(out_6[1]));  // open: Qn, preset, reset
  D_Flip_Flop #(.trigger("falling")) d_ff_3 (
    .D(multiplexer_1_out[2]), .clk(in_2), .Q(out_6[2]));  // open: Qn, preset, reset
  D_Flip_Flop #(.trigger("falling")) d_ff_4 (
    .D(multiplexer_1_out[3]), .clk(in_2), .Q(out_6[3]));  // open: Qn, preset, reset
  cuincrementor cuincrementor_1 (.in_1(out_6), .in_2(in_4), .out_3(cuincrementor_1_out_3));
  not not_8 (not_8_out, not_2_out);
  not not_9 (not_9_out, in_1[5]);
  and OP10 (OP10_out, in_1[7], xor_1_out);
  and OP01 (OP01_out, xor_1_out, in_1[6]);
  and and_1 (out_5[8], not_6_out, OP00_out);
  and and_2 (out_5[0], not_2_out, OP11_out);
  and and_3 (out_5[1], not_8_out, OP11_out);
  and and_4 (out_5[2], in_1[5], OP10_out);
  and and_5 (out_5[3], not_9_out, OP10_out);
  and and_6 (out_5[4], in_1[5], OP01_out);
  and and_7 (out_5[5], not_9_out, OP01_out);
  and and_8 (out_5[6], not_7_out, not_5_out, OP00_out);
  and and_9 (out_5[7], in_1[5], not_5_out, OP00_out);

  // Notes on the sheet:
  //   PRT
  //   BNQ
  //   LOAD
  //   ADD
  //   STORE
  //   SUB
  //   STOP
  //   INP
  //   BEQ
  //   WE NEED A DONE BIT to increment the PC
endmodule

module cuincrementor (
  input  [3:0] in_1,
  input  in_2,
  output [3:0] out_3
);

  wire not_1_out, onebitadder_1_cout, onebitadder_2_cout, onebitadder_3_p3, onebitadder_3_p6;

  not not_1 (not_1_out, in_2);
  onebitadder onebitadder_1 (.A(in_1[0]), .B(not_1_out), .Sum(out_3[0]), .Cout(onebitadder_1_cout));  // open: Cin
  onebitadder onebitadder_2 (
    .Cin(onebitadder_1_cout), .A(in_1[1]), .Sum(out_3[1]), .Cout(onebitadder_2_cout));  // open: B
  // onebitadder onebitadder_3: pin names not known; wires that end beside it: onebitadder_2_cout, in_1[2], onebitadder_3_p3, onebitadder_3_p3, out_3[2], onebitadder_3_p6
  onebitadder onebitadder_4 (.Cin(onebitadder_3_p6), .A(in_1[3]), .Sum(out_3[3]));  // open: B, Cout
endmodule

module RAM (
  input  [3:0] in_1,
  input  [7:0] in_2,
  input  R_W_R_0_W_1,
  input  in_4,
  input  in_5,
  input  [7:0] in_6,
  input  [7:0] in_7,
  input  [7:0] in_8,
  input  [7:0] in_9,
  input  [7:0] in_10,
  input  [7:0] in_11,
  input  [7:0] in_12,
  input  [7:0] in_13,
  input  [7:0] in_14,
  input  [7:0] in_15,
  input  [7:0] in_16,
  input  [7:0] in_17,
  input  [7:0] in_18,
  input  [7:0] in_19,
  input  [7:0] in_20,
  input  [7:0] in_21,
  output [7:0] out_22
);

  wire a0_out, a1_out, a2_out, a3_out, a4_out, a5_out, a6_out, a7_out, a8_out, a9_out, a10_out, a11_out,
       a12_out, a13_out, a14_out, a15_out, not_1_out, not_2_out, not_3_out, not_4_out, not_5_out, not_6_out,
       not_7_out, not_8_out, not_9_out, not_10_out, not_11_out, not_12_out, not_13_out, not_14_out,
       not_15_out, not_16_out, not_17_out, not_18_out, not_19_out, not_20_out, not_21_out, not_22_out,
       not_23_out, not_24_out, not_25_out, not_26_out, not_27_out, not_28_out, not_29_out, not_30_out,
       not_31_out, not_32_out, or_1_out, or_2_out, or_3_out, or_4_out, or_5_out, or_6_out, or_7_out,
       or_8_out, or_9_out, or_10_out, or_11_out, or_12_out, or_13_out, or_14_out, or_15_out, or_16_out,
       or_17_out, or_18_out;
  wire [7:0] byte_1_out_5, byte_2_out_5, byte_3_out_5, byte_4_out_5, byte_5_out_5, byte_6_out_5,
       byte_7_out_5, byte_8_out_5, byte_9_out_5, byte_10_out_5, byte_11_out_5, byte_12_out_5, byte_13_out_5,
       byte_14_out_5, byte_15_out_5, byte_16_out_5, multiplexer_1_out, multiplexer_2_out, multiplexer_3_out,
       multiplexer_4_out, multiplexer_5_out, multiplexer_6_out, multiplexer_7_out, multiplexer_8_out,
       multiplexer_9_out, multiplexer_10_out, multiplexer_11_out, multiplexer_12_out, multiplexer_13_out,
       multiplexer_14_out, multiplexer_15_out, multiplexer_16_out;

  ExactlyOne xor_1[7:0] (
    .out(out_22), .in0(byte_1_out_5), .in1(byte_2_out_5), .in2(byte_3_out_5), .in3(byte_4_out_5),
    .in4(byte_5_out_5), .in5(byte_6_out_5), .in6(byte_7_out_5), .in7(byte_8_out_5), .in8(byte_9_out_5),
    .in9(byte_10_out_5), .in10(byte_11_out_5), .in11(byte_12_out_5), .in12(byte_13_out_5),
    .in13(byte_14_out_5), .in14(byte_15_out_5), .in15(byte_16_out_5));
  or or_1 (or_1_out, in_4, in_5);
  or or_2 (or_2_out, in_5, a0_out);
  or or_3 (or_3_out, R_W_R_0_W_1, in_5);
  Byte byte_1 (
    .in_4(multiplexer_1_out), .out_5(byte_1_out_5), .clock_bit(or_1_out), .address(or_2_out), .in_1(or_3_out));
  Multiplexer #(.width(8), .enable("false")) multiplexer_1 (
    .in0(in_2), .in1(in_6), .out(multiplexer_1_out), .sel(in_5));
  not not_1 (not_1_out, in_1[2]);
  not not_2 (not_2_out, in_1[3]);
  not not_3 (not_3_out, in_1[0]);
  not not_4 (not_4_out, in_1[2]);
  not not_5 (not_5_out, in_1[1]);
  not not_6 (not_6_out, in_1[3]);
  and a0 (a0_out, not_2_out, not_4_out, not_5_out, not_3_out);
  and a1 (a1_out, not_6_out, not_1_out, not_7_out, in_1[0]);
  or or_4 (or_4_out, in_5, a1_out);
  Byte byte_2 (
    .in_4(multiplexer_2_out), .out_5(byte_2_out_5), .clock_bit(or_1_out), .address(or_4_out), .in_1(or_3_out));
  Multiplexer #(.width(8), .enable("false")) multiplexer_2 (
    .in0(in_2), .in1(in_7), .out(multiplexer_2_out), .sel(in_5));
  not not_7 (not_7_out, in_1[1]);
  not not_8 (not_8_out, in_1[3]);
  not not_9 (not_9_out, in_1[2]);
  not not_10 (not_10_out, in_1[3]);
  not not_11 (not_11_out, in_1[0]);
  and a2 (a2_out, not_10_out, not_9_out, in_1[1], not_11_out);
  or or_5 (or_5_out, in_5, a2_out);
  Byte byte_3 (
    .in_4(multiplexer_3_out), .out_5(byte_3_out_5), .clock_bit(or_1_out), .address(or_5_out), .in_1(or_3_out));
  Multiplexer #(.width(8), .enable("false")) multiplexer_3 (
    .in0(in_2), .in1(in_8), .out(multiplexer_3_out), .sel(in_5));
  not not_12 (not_12_out, in_1[3]);
  not not_13 (not_13_out, in_1[1]);
  not not_14 (not_14_out, in_1[2]);
  and a4 (a4_out, not_12_out, in_1[2], not_13_out, not_16_out);
  and a3 (a3_out, not_8_out, not_14_out, in_1[1], in_1[0]);
  or or_6 (or_6_out, in_5, a3_out);
  Byte byte_4 (
    .in_4(multiplexer_4_out), .out_5(byte_4_out_5), .clock_bit(or_1_out), .address(or_6_out), .in_1(or_3_out));
  Multiplexer #(.width(8), .enable("false")) multiplexer_4 (
    .in0(in_2), .in1(in_9), .out(multiplexer_4_out), .sel(in_5));
  not not_15 (not_15_out, in_1[3]);
  not not_16 (not_16_out, in_1[0]);
  not not_17 (not_17_out, in_1[3]);
  not not_18 (not_18_out, in_1[1]);
  and a5 (a5_out, not_15_out, in_1[2], not_18_out, in_1[0]);
  or or_7 (or_7_out, in_5, a4_out);
  Byte byte_5 (
    .in_4(multiplexer_5_out), .out_5(byte_5_out_5), .clock_bit(or_1_out), .address(or_7_out), .in_1(or_3_out));
  Multiplexer #(.width(8), .enable("false")) multiplexer_5 (
    .in0(in_2), .in1(in_10), .out(multiplexer_5_out), .sel(in_5));
  not not_19 (not_19_out, in_1[3]);
  not not_20 (not_20_out, in_1[0]);
  and a6 (a6_out, not_17_out, in_1[2], in_1[1], not_20_out);
  and a7 (a7_out, not_19_out, in_1[2], in_1[1], in_1[0]);
  or or_8 (or_8_out, in_5, a5_out);
  Byte byte_6 (
    .in_4(multiplexer_6_out), .out_5(byte_6_out_5), .clock_bit(or_1_out), .address(or_8_out), .in_1(or_3_out));
  Multiplexer #(.width(8), .enable("false")) multiplexer_6 (
    .in0(in_2), .in1(in_11), .out(multiplexer_6_out), .sel(in_5));
  not not_21 (not_21_out, in_1[1]);
  not not_22 (not_22_out, in_1[2]);
  not not_23 (not_23_out, in_1[2]);
  not not_24 (not_24_out, in_1[0]);
  and a8 (a8_out, in_1[3], not_22_out, not_21_out, not_24_out);
  and a9 (a9_out, in_1[3], not_23_out, not_26_out, in_1[0]);
  or or_9 (or_9_out, in_5, a6_out);
  Byte byte_7 (
    .in_4(multiplexer_7_out), .out_5(byte_7_out_5), .clock_bit(or_1_out), .address(or_9_out), .in_1(or_3_out));
  Multiplexer #(.width(8), .enable("false")) multiplexer_7 (
    .in0(in_2), .in1(in_12), .out(multiplexer_7_out), .sel(in_5));
  not not_25 (not_25_out, in_1[2]);
  not not_26 (not_26_out, in_1[1]);
  not not_27 (not_27_out, in_1[0]);
  and a10 (a10_out, in_1[3], not_25_out, in_1[1], not_27_out);
  or or_10 (or_10_out, in_5, a7_out);
  Byte byte_8 (
    .in_4(multiplexer_8_out), .out_5(byte_8_out_5), .clock_bit(or_1_out), .address(or_10_out), .in_1(or_3_out));
  Multiplexer #(.width(8), .enable("false")) multiplexer_8 (
    .in0(in_2), .in1(in_13), .out(multiplexer_8_out), .sel(in_5));
  not not_28 (not_28_out, in_1[2]);
  not not_29 (not_29_out, in_1[1]);
  and a12 (a12_out, in_1[3], in_1[2], not_29_out, not_31_out);
  and a11 (a11_out, in_1[3], not_28_out, in_1[1], in_1[0]);
  or or_11 (or_11_out, in_5, a8_out);
  Byte byte_9 (
    .in_4(multiplexer_9_out), .out_5(byte_9_out_5), .clock_bit(or_1_out), .address(or_11_out), .in_1(or_3_out));
  Multiplexer #(.width(8), .enable("false")) multiplexer_9 (
    .in0(in_2), .in1(in_14), .out(multiplexer_9_out), .sel(in_5));
  not not_30 (not_30_out, in_1[1]);
  not not_31 (not_31_out, in_1[0]);
  and a13 (a13_out, in_1[3], in_1[2], not_30_out, in_1[0]);
  or or_12 (or_12_out, in_5, a9_out);
  Byte byte_10 (
    .in_4(multiplexer_10_out), .out_5(byte_10_out_5), .clock_bit(or_1_out), .address(or_12_out),
    .in_1(or_3_out));
  Multiplexer #(.width(8), .enable("false")) multiplexer_10 (
    .in0(in_2), .in1(in_15), .out(multiplexer_10_out), .sel(in_5));
  not not_32 (not_32_out, in_1[0]);
  and a14 (a14_out, in_1[3], in_1[2], in_1[1], not_32_out);
  and a15 (a15_out, in_1[3], in_1[2], in_1[1], in_1[0]);
  or or_13 (or_13_out, in_5, a10_out);
  Byte byte_11 (
    .in_4(multiplexer_11_out), .out_5(byte_11_out_5), .clock_bit(or_1_out), .address(or_13_out),
    .in_1(or_3_out));
  Multiplexer #(.width(8), .enable("false")) multiplexer_11 (
    .in0(in_2), .in1(in_16), .out(multiplexer_11_out), .sel(in_5));
  or or_14 (or_14_out, in_5, a11_out);
  Byte byte_12 (
    .in_4(multiplexer_12_out), .out_5(byte_12_out_5), .clock_bit(or_1_out), .address(or_14_out),
    .in_1(or_3_out));
  Multiplexer #(.width(8), .enable("false")) multiplexer_12 (
    .in0(in_2), .in1(in_17), .out(multiplexer_12_out), .sel(in_5));
  or or_15 (or_15_out, in_5, a12_out);
  Byte byte_13 (
    .in_4(multiplexer_13_out), .out_5(byte_13_out_5), .clock_bit(or_1_out), .address(or_15_out),
    .in_1(or_3_out));
  Multiplexer #(.width(8), .enable("false")) multiplexer_13 (
    .in0(in_2), .in1(in_18), .out(multiplexer_13_out), .sel(in_5));
  or or_16 (or_16_out, in_5, a13_out);
  Byte byte_14 (
    .in_4(multiplexer_14_out), .out_5(byte_14_out_5), .clock_bit(or_1_out), .address(or_16_out),
    .in_1(or_3_out));
  Multiplexer #(.width(8), .enable("false")) multiplexer_14 (
    .in0(in_2), .in1(in_19), .out(multiplexer_14_out), .sel(in_5));
  or or_17 (or_17_out, in_5, a14_out);
  Byte byte_15 (
    .in_4(multiplexer_15_out), .out_5(byte_15_out_5), .clock_bit(or_1_out), .address(or_17_out),
    .in_1(or_3_out));
  Multiplexer #(.width(8), .enable("false")) multiplexer_15 (
    .in0(in_2), .in1(in_20), .out(multiplexer_15_out), .sel(in_5));
  or or_18 (or_18_out, in_5, a15_out);
  Byte byte_16 (
    .in_4(multiplexer_16_out), .out_5(byte_16_out_5), .clock_bit(or_1_out), .address(or_18_out),
    .in_1(or_3_out));
  Multiplexer #(.width(8), .enable("false")) multiplexer_16 (
    .in0(in_2), .in1(in_21), .out(multiplexer_16_out), .sel(in_5));

  // Notes on the sheet:
  //   CLOCK
endmodule

module ARn (
  input  clock_bit,
  input  [3:0] in_2,
  output [3:0] out_3
);

  wire and_1_out, and_2_out, and_3_out, and_4_out, and_5_out, and_6_out, and_7_out, and_8_out, not_1_out,
       not_2_out, not_3_out, not_4_out, s_r_ff_1_q, s_r_ff_2_q, s_r_ff_3_q, s_r_ff_4_q;

  not not_1 (not_1_out, in_2[0]);
  not not_2 (not_2_out, in_2[1]);
  not not_3 (not_3_out, in_2[2]);
  not not_4 (not_4_out, in_2[3]);
  and and_1 (and_1_out, 1'b1, 1'b1, in_2[0]);
  and and_2 (and_2_out, not_1_out, 1'b1, 1'b1);
  and and_3 (and_3_out, 1'b1, 1'b1, in_2[1]);
  and and_4 (and_4_out, not_2_out, 1'b1, 1'b1);
  and and_5 (and_5_out, 1'b1, 1'b1, in_2[2]);
  and and_6 (and_6_out, not_3_out, 1'b1, 1'b1);
  and and_7 (and_7_out, 1'b1, 1'b1, in_2[3]);
  and and_8 (and_8_out, not_4_out, 1'b1, 1'b1);
  S_R_Flip_Flop #(.trigger("falling")) s_r_ff_1 (
    .S(and_1_out), .R(and_2_out), .clk(clock_bit), .Q(s_r_ff_1_q));  // open: reset, Qn, preset
  S_R_Flip_Flop #(.trigger("falling")) s_r_ff_2 (
    .S(and_3_out), .R(and_4_out), .clk(clock_bit), .Q(s_r_ff_2_q));  // open: reset, Qn, preset
  S_R_Flip_Flop #(.trigger("falling")) s_r_ff_3 (
    .S(and_5_out), .R(and_6_out), .clk(clock_bit), .Q(s_r_ff_3_q));  // open: reset, Qn, preset
  S_R_Flip_Flop #(.trigger("falling")) s_r_ff_4 (
    .S(and_7_out), .R(and_8_out), .clk(clock_bit), .Q(s_r_ff_4_q));  // open: reset, Qn, preset
  and and_9 (out_3[0], s_r_ff_1_q, 1'b1, 1'b1);
  and and_10 (out_3[1], s_r_ff_2_q, 1'b1, 1'b1);
  and and_11 (out_3[2], s_r_ff_3_q, 1'b1, 1'b1);
  and and_12 (out_3[3], s_r_ff_4_q, 1'b1, 1'b1);

  // Notes on the sheet:
  //   address
  //   R/W, 1=W 0=R
endmodule

module AR (
  input  clock_bit,
  input  [3:0] in_2,
  output [3:0] out_3
);

  wire and_1_out, and_2_out, and_3_out, and_4_out, and_5_out, and_6_out, and_7_out, and_8_out, not_1_out,
       not_2_out, not_3_out, not_4_out, s_r_ff_1_q, s_r_ff_2_q, s_r_ff_3_q, s_r_ff_4_q;

  not not_1 (not_1_out, in_2[0]);
  not not_2 (not_2_out, in_2[1]);
  not not_3 (not_3_out, in_2[2]);
  not not_4 (not_4_out, in_2[3]);
  and and_1 (and_1_out, 1'b1, 1'b1, in_2[0]);
  and and_2 (and_2_out, not_1_out, 1'b1, 1'b1);
  and and_3 (and_3_out, 1'b1, 1'b1, in_2[1]);
  and and_4 (and_4_out, not_2_out, 1'b1, 1'b1);
  and and_5 (and_5_out, 1'b1, 1'b1, in_2[2]);
  and and_6 (and_6_out, not_3_out, 1'b1, 1'b1);
  and and_7 (and_7_out, 1'b1, 1'b1, in_2[3]);
  and and_8 (and_8_out, not_4_out, 1'b1, 1'b1);
  S_R_Flip_Flop #(.trigger("falling")) s_r_ff_1 (
    .S(and_1_out), .R(and_2_out), .clk(clock_bit), .Q(s_r_ff_1_q));  // open: reset, Qn, preset
  S_R_Flip_Flop #(.trigger("falling")) s_r_ff_2 (
    .S(and_3_out), .R(and_4_out), .clk(clock_bit), .Q(s_r_ff_2_q));  // open: reset, Qn, preset
  S_R_Flip_Flop #(.trigger("falling")) s_r_ff_3 (
    .S(and_5_out), .R(and_6_out), .clk(clock_bit), .Q(s_r_ff_3_q));  // open: reset, Qn, preset
  S_R_Flip_Flop #(.trigger("falling")) s_r_ff_4 (
    .S(and_7_out), .R(and_8_out), .clk(clock_bit), .Q(s_r_ff_4_q));  // open: reset, Qn, preset
  and and_9 (out_3[0], s_r_ff_1_q, 1'b1, 1'b1);
  and and_10 (out_3[1], s_r_ff_2_q, 1'b1, 1'b1);
  and and_11 (out_3[2], s_r_ff_3_q, 1'b1, 1'b1);
  and and_12 (out_3[3], s_r_ff_4_q, 1'b1, 1'b1);

  // Notes on the sheet:
  //   address
  //   R/W, 1=W 0=R
endmodule

module Byte (
  input  in_1,
  input  clock_bit,
  input  address,
  input  [7:0] in_4,
  output [7:0] out_5
);

  wire and_1_out, and_2_out, and_3_out, and_4_out, and_5_out, and_6_out, and_7_out, and_8_out, and_9_out,
       and_10_out, and_11_out, and_12_out, and_13_out, and_14_out, and_15_out, and_16_out, not_1_out,
       not_2_out, not_3_out, not_4_out, not_5_out, not_6_out, not_7_out, not_8_out, not_9_out, s_r_ff_1_q,
       s_r_ff_2_q, s_r_ff_3_q, s_r_ff_4_q, s_r_ff_5_q, s_r_ff_6_q, s_r_ff_7_q, s_r_ff_8_q;

  not not_1 (not_1_out, in_4[0]);
  not not_2 (not_2_out, in_4[1]);
  not not_3 (not_3_out, in_4[2]);
  not not_4 (not_4_out, in_4[3]);
  not not_5 (not_5_out, in_4[4]);
  not not_6 (not_6_out, in_4[5]);
  not not_7 (not_7_out, in_4[6]);
  not not_8 (not_8_out, in_4[7]);
  and and_1 (and_1_out, address, in_1, in_4[0]);
  and and_2 (and_2_out, not_1_out, in_1, address);
  and and_3 (and_3_out, address, in_1, in_4[1]);
  and and_4 (and_4_out, not_2_out, in_1, address);
  and and_5 (and_5_out, address, in_1, in_4[2]);
  and and_6 (and_6_out, not_3_out, in_1, address);
  and and_7 (and_7_out, address, in_1, in_4[3]);
  and and_8 (and_8_out, not_4_out, in_1, address);
  and and_9 (and_9_out, address, in_1, in_4[4]);
  and and_10 (and_10_out, not_5_out, in_1, address);
  and and_11 (and_11_out, address, in_1, in_4[5]);
  and and_12 (and_12_out, not_6_out, in_1, address);
  and and_13 (and_13_out, address, in_1, in_4[6]);
  and and_14 (and_14_out, not_7_out, in_1, address);
  and and_15 (and_15_out, address, in_1, in_4[7]);
  and and_16 (and_16_out, not_8_out, in_1, address);
  S_R_Flip_Flop #(.trigger("falling")) s_r_ff_1 (
    .S(and_1_out), .R(and_2_out), .clk(clock_bit), .Q(s_r_ff_1_q));  // open: reset, Qn, preset
  S_R_Flip_Flop #(.trigger("falling")) s_r_ff_2 (
    .S(and_3_out), .R(and_4_out), .clk(clock_bit), .Q(s_r_ff_2_q));  // open: reset, Qn, preset
  S_R_Flip_Flop #(.trigger("falling")) s_r_ff_3 (
    .S(and_5_out), .R(and_6_out), .clk(clock_bit), .Q(s_r_ff_3_q));  // open: reset, Qn, preset
  S_R_Flip_Flop #(.trigger("falling")) s_r_ff_4 (
    .S(and_7_out), .R(and_8_out), .clk(clock_bit), .Q(s_r_ff_4_q));  // open: reset, Qn, preset
  S_R_Flip_Flop #(.trigger("falling")) s_r_ff_5 (
    .S(and_9_out), .R(and_10_out), .clk(clock_bit), .Q(s_r_ff_5_q));  // open: reset, Qn, preset
  S_R_Flip_Flop #(.trigger("falling")) s_r_ff_6 (
    .S(and_11_out), .R(and_12_out), .clk(clock_bit), .Q(s_r_ff_6_q));  // open: reset, Qn, preset
  S_R_Flip_Flop #(.trigger("falling")) s_r_ff_7 (
    .S(and_13_out), .R(and_14_out), .clk(clock_bit), .Q(s_r_ff_7_q));  // open: reset, Qn, preset
  S_R_Flip_Flop #(.trigger("falling")) s_r_ff_8 (
    .S(and_15_out), .R(and_16_out), .clk(clock_bit), .Q(s_r_ff_8_q));  // open: reset, Qn, preset
  not not_9 (not_9_out, in_1);
  and and_17 (out_5[0], s_r_ff_1_q, not_9_out, address);
  and and_18 (out_5[1], s_r_ff_2_q, not_9_out, address);
  and and_19 (out_5[2], s_r_ff_3_q, not_9_out, address);
  and and_20 (out_5[3], s_r_ff_4_q, not_9_out, address);
  and and_21 (out_5[4], s_r_ff_5_q, not_9_out, address);
  and and_22 (out_5[5], s_r_ff_6_q, not_9_out, address);
  and and_23 (out_5[6], s_r_ff_7_q, not_9_out, address);
  and and_24 (out_5[7], s_r_ff_8_q, not_9_out, address);

  // Notes on the sheet:
  //   R/W, 1=W 0=R
endmodule

module DRn (
  input  clock_bit,
  input  [7:0] in_2,
  output [7:0] out_3
);

  wire and_1_out, and_2_out, and_3_out, and_4_out, and_5_out, and_6_out, and_7_out, and_8_out, and_9_out,
       and_10_out, and_11_out, and_12_out, and_13_out, and_14_out, and_15_out, and_16_out, not_1_out,
       not_2_out, not_3_out, not_4_out, not_5_out, not_6_out, not_7_out, not_8_out, s_r_ff_1_q, s_r_ff_2_q,
       s_r_ff_3_q, s_r_ff_4_q, s_r_ff_5_q, s_r_ff_6_q, s_r_ff_7_q, s_r_ff_8_q;

  not not_1 (not_1_out, in_2[0]);
  not not_2 (not_2_out, in_2[1]);
  not not_3 (not_3_out, in_2[2]);
  not not_4 (not_4_out, in_2[3]);
  not not_5 (not_5_out, in_2[4]);
  not not_6 (not_6_out, in_2[5]);
  not not_7 (not_7_out, in_2[6]);
  not not_8 (not_8_out, in_2[7]);
  and and_1 (and_1_out, 1'b1, 1'b1, in_2[0]);
  and and_2 (and_2_out, not_1_out, 1'b1, 1'b1);
  and and_3 (and_3_out, 1'b1, 1'b1, in_2[1]);
  and and_4 (and_4_out, not_2_out, 1'b1, 1'b1);
  and and_5 (and_5_out, 1'b1, 1'b1, in_2[2]);
  and and_6 (and_6_out, not_3_out, 1'b1, 1'b1);
  and and_7 (and_7_out, 1'b1, 1'b1, in_2[3]);
  and and_8 (and_8_out, not_4_out, 1'b1, 1'b1);
  and and_9 (and_9_out, 1'b1, 1'b1, in_2[4]);
  and and_10 (and_10_out, not_5_out, 1'b1, 1'b1);
  and and_11 (and_11_out, 1'b1, 1'b1, in_2[5]);
  and and_12 (and_12_out, not_6_out, 1'b1, 1'b1);
  and and_13 (and_13_out, 1'b1, 1'b1, in_2[6]);
  and and_14 (and_14_out, not_7_out, 1'b1, 1'b1);
  and and_15 (and_15_out, 1'b1, 1'b1, in_2[7]);
  and and_16 (and_16_out, not_8_out, 1'b1, 1'b1);
  S_R_Flip_Flop s_r_ff_1 (.S(and_1_out), .R(and_2_out), .clk(clock_bit), .Q(s_r_ff_1_q));  // open: reset, Qn, preset
  S_R_Flip_Flop s_r_ff_2 (.S(and_3_out), .R(and_4_out), .clk(clock_bit), .Q(s_r_ff_2_q));  // open: reset, Qn, preset
  S_R_Flip_Flop s_r_ff_3 (.S(and_5_out), .R(and_6_out), .clk(clock_bit), .Q(s_r_ff_3_q));  // open: reset, Qn, preset
  S_R_Flip_Flop s_r_ff_4 (.S(and_7_out), .R(and_8_out), .clk(clock_bit), .Q(s_r_ff_4_q));  // open: reset, Qn, preset
  S_R_Flip_Flop s_r_ff_5 (.S(and_9_out), .R(and_10_out), .clk(clock_bit), .Q(s_r_ff_5_q));  // open: reset, Qn, preset
  S_R_Flip_Flop s_r_ff_6 (.S(and_11_out), .R(and_12_out), .clk(clock_bit), .Q(s_r_ff_6_q));  // open: reset, Qn, preset
  S_R_Flip_Flop s_r_ff_7 (.S(and_13_out), .R(and_14_out), .clk(clock_bit), .Q(s_r_ff_7_q));  // open: reset, Qn, preset
  S_R_Flip_Flop s_r_ff_8 (.S(and_15_out), .R(and_16_out), .clk(clock_bit), .Q(s_r_ff_8_q));  // open: reset, Qn, preset
  and and_17 (out_3[0], s_r_ff_1_q, 1'b1, 1'b1);
  and and_18 (out_3[1], s_r_ff_2_q, 1'b1, 1'b1);
  and and_19 (out_3[2], s_r_ff_3_q, 1'b1, 1'b1);
  and and_20 (out_3[3], s_r_ff_4_q, 1'b1, 1'b1);
  and and_21 (out_3[4], s_r_ff_5_q, 1'b1, 1'b1);
  and and_22 (out_3[5], s_r_ff_6_q, 1'b1, 1'b1);
  and and_23 (out_3[6], s_r_ff_7_q, 1'b1, 1'b1);
  and and_24 (out_3[7], s_r_ff_8_q, 1'b1, 1'b1);

  // Notes on the sheet:
  //   address
  //   R/W, 1=W 0=R
endmodule

module DR (
  input  clock_bit,
  input  [7:0] in_2,
  output [7:0] out_3
);

  wire and_1_out, and_2_out, and_3_out, and_4_out, and_5_out, and_6_out, and_7_out, and_8_out, and_9_out,
       and_10_out, and_11_out, and_12_out, and_13_out, and_14_out, and_15_out, and_16_out, not_1_out,
       not_2_out, not_3_out, not_4_out, not_5_out, not_6_out, not_7_out, not_8_out, s_r_ff_1_q, s_r_ff_2_q,
       s_r_ff_3_q, s_r_ff_4_q, s_r_ff_5_q, s_r_ff_6_q, s_r_ff_7_q, s_r_ff_8_q;

  not not_1 (not_1_out, in_2[0]);
  not not_2 (not_2_out, in_2[1]);
  not not_3 (not_3_out, in_2[2]);
  not not_4 (not_4_out, in_2[3]);
  not not_5 (not_5_out, in_2[4]);
  not not_6 (not_6_out, in_2[5]);
  not not_7 (not_7_out, in_2[6]);
  not not_8 (not_8_out, in_2[7]);
  and and_1 (and_1_out, 1'b1, 1'b1, in_2[0]);
  and and_2 (and_2_out, not_1_out, 1'b1, 1'b1);
  and and_3 (and_3_out, 1'b1, 1'b1, in_2[1]);
  and and_4 (and_4_out, not_2_out, 1'b1, 1'b1);
  and and_5 (and_5_out, 1'b1, 1'b1, in_2[2]);
  and and_6 (and_6_out, not_3_out, 1'b1, 1'b1);
  and and_7 (and_7_out, 1'b1, 1'b1, in_2[3]);
  and and_8 (and_8_out, not_4_out, 1'b1, 1'b1);
  and and_9 (and_9_out, 1'b1, 1'b1, in_2[4]);
  and and_10 (and_10_out, not_5_out, 1'b1, 1'b1);
  and and_11 (and_11_out, 1'b1, 1'b1, in_2[5]);
  and and_12 (and_12_out, not_6_out, 1'b1, 1'b1);
  and and_13 (and_13_out, 1'b1, 1'b1, in_2[6]);
  and and_14 (and_14_out, not_7_out, 1'b1, 1'b1);
  and and_15 (and_15_out, 1'b1, 1'b1, in_2[7]);
  and and_16 (and_16_out, not_8_out, 1'b1, 1'b1);
  S_R_Flip_Flop #(.trigger("falling")) s_r_ff_1 (
    .S(and_1_out), .R(and_2_out), .clk(clock_bit), .Q(s_r_ff_1_q));  // open: reset, Qn, preset
  S_R_Flip_Flop #(.trigger("falling")) s_r_ff_2 (
    .S(and_3_out), .R(and_4_out), .clk(clock_bit), .Q(s_r_ff_2_q));  // open: reset, Qn, preset
  S_R_Flip_Flop #(.trigger("falling")) s_r_ff_3 (
    .S(and_5_out), .R(and_6_out), .clk(clock_bit), .Q(s_r_ff_3_q));  // open: reset, Qn, preset
  S_R_Flip_Flop #(.trigger("falling")) s_r_ff_4 (
    .S(and_7_out), .R(and_8_out), .clk(clock_bit), .Q(s_r_ff_4_q));  // open: reset, Qn, preset
  S_R_Flip_Flop #(.trigger("falling")) s_r_ff_5 (
    .S(and_9_out), .R(and_10_out), .clk(clock_bit), .Q(s_r_ff_5_q));  // open: reset, Qn, preset
  S_R_Flip_Flop #(.trigger("falling")) s_r_ff_6 (
    .S(and_11_out), .R(and_12_out), .clk(clock_bit), .Q(s_r_ff_6_q));  // open: reset, Qn, preset
  S_R_Flip_Flop #(.trigger("falling")) s_r_ff_7 (
    .S(and_13_out), .R(and_14_out), .clk(clock_bit), .Q(s_r_ff_7_q));  // open: reset, Qn, preset
  S_R_Flip_Flop #(.trigger("falling")) s_r_ff_8 (
    .S(and_15_out), .R(and_16_out), .clk(clock_bit), .Q(s_r_ff_8_q));  // open: reset, Qn, preset
  and and_17 (out_3[0], s_r_ff_1_q, 1'b1, 1'b1, clock_bit);
  and and_18 (out_3[1], s_r_ff_2_q, 1'b1, 1'b1, clock_bit);
  and and_19 (out_3[2], s_r_ff_3_q, 1'b1, 1'b1, clock_bit);
  and and_20 (out_3[3], s_r_ff_4_q, 1'b1, 1'b1, clock_bit);
  and and_21 (out_3[4], s_r_ff_5_q, 1'b1, 1'b1, clock_bit);
  and and_22 (out_3[5], s_r_ff_6_q, 1'b1, 1'b1, clock_bit);
  and and_23 (out_3[6], s_r_ff_7_q, 1'b1, 1'b1, clock_bit);
  and and_24 (out_3[7], s_r_ff_8_q, 1'b1, 1'b1, clock_bit);

  // Notes on the sheet:
  //   address
  //   R/W, 1=W 0=R
endmodule

module Mode (
  input  in_1,
  input  in_2,
  output out_3
);

  D_Flip_Flop d_ff_1 (.D(in_2), .clk(in_1), .Q(out_3));  // open: Qn, preset, reset
endmodule

module MBR (
  input  clock_bit,
  input  [7:0] in_2,
  output [7:0] out_3
);

  wire and_1_out, and_2_out, and_3_out, and_4_out, and_5_out, and_6_out, and_7_out, and_8_out, and_9_out,
       and_10_out, and_11_out, and_12_out, and_13_out, and_14_out, and_15_out, and_16_out, not_1_out,
       not_2_out, not_3_out, not_4_out, not_5_out, not_6_out, not_7_out, not_8_out, s_r_ff_1_q, s_r_ff_2_q,
       s_r_ff_3_q, s_r_ff_4_q, s_r_ff_5_q, s_r_ff_6_q, s_r_ff_7_q, s_r_ff_8_q;

  not not_1 (not_1_out, in_2[0]);
  not not_2 (not_2_out, in_2[1]);
  not not_3 (not_3_out, in_2[2]);
  not not_4 (not_4_out, in_2[3]);
  not not_5 (not_5_out, in_2[4]);
  not not_6 (not_6_out, in_2[5]);
  not not_7 (not_7_out, in_2[6]);
  not not_8 (not_8_out, in_2[7]);
  and and_1 (and_1_out, 1'b1, 1'b1, in_2[0]);
  and and_2 (and_2_out, not_1_out, 1'b1, 1'b1);
  and and_3 (and_3_out, 1'b1, 1'b1, in_2[1]);
  and and_4 (and_4_out, not_2_out, 1'b1, 1'b1);
  and and_5 (and_5_out, 1'b1, 1'b1, in_2[2]);
  and and_6 (and_6_out, not_3_out, 1'b1, 1'b1);
  and and_7 (and_7_out, 1'b1, 1'b1, in_2[3]);
  and and_8 (and_8_out, not_4_out, 1'b1, 1'b1);
  and and_9 (and_9_out, 1'b1, 1'b1, in_2[4]);
  and and_10 (and_10_out, not_5_out, 1'b1, 1'b1);
  and and_11 (and_11_out, 1'b1, 1'b1, in_2[5]);
  and and_12 (and_12_out, not_6_out, 1'b1, 1'b1);
  and and_13 (and_13_out, 1'b1, 1'b1, in_2[6]);
  and and_14 (and_14_out, not_7_out, 1'b1, 1'b1);
  and and_15 (and_15_out, 1'b1, 1'b1, in_2[7]);
  and and_16 (and_16_out, not_8_out, 1'b1, 1'b1);
  S_R_Flip_Flop #(.trigger("falling")) s_r_ff_1 (
    .S(and_1_out), .R(and_2_out), .clk(clock_bit), .Q(s_r_ff_1_q));  // open: reset, Qn, preset
  S_R_Flip_Flop #(.trigger("falling")) s_r_ff_2 (
    .S(and_3_out), .R(and_4_out), .clk(clock_bit), .Q(s_r_ff_2_q));  // open: reset, Qn, preset
  S_R_Flip_Flop #(.trigger("falling")) s_r_ff_3 (
    .S(and_5_out), .R(and_6_out), .clk(clock_bit), .Q(s_r_ff_3_q));  // open: reset, Qn, preset
  S_R_Flip_Flop #(.trigger("falling")) s_r_ff_4 (
    .S(and_7_out), .R(and_8_out), .clk(clock_bit), .Q(s_r_ff_4_q));  // open: reset, Qn, preset
  S_R_Flip_Flop #(.trigger("falling")) s_r_ff_5 (
    .S(and_9_out), .R(and_10_out), .clk(clock_bit), .Q(s_r_ff_5_q));  // open: reset, Qn, preset
  S_R_Flip_Flop #(.trigger("falling")) s_r_ff_6 (
    .S(and_11_out), .R(and_12_out), .clk(clock_bit), .Q(s_r_ff_6_q));  // open: reset, Qn, preset
  S_R_Flip_Flop #(.trigger("falling")) s_r_ff_7 (
    .S(and_13_out), .R(and_14_out), .clk(clock_bit), .Q(s_r_ff_7_q));  // open: reset, Qn, preset
  S_R_Flip_Flop #(.trigger("falling")) s_r_ff_8 (
    .S(and_15_out), .R(and_16_out), .clk(clock_bit), .Q(s_r_ff_8_q));  // open: reset, Qn, preset
  and and_17 (out_3[0], s_r_ff_1_q, 1'b1, 1'b1);
  and and_18 (out_3[1], s_r_ff_2_q, 1'b1, 1'b1);
  and and_19 (out_3[2], s_r_ff_3_q, 1'b1, 1'b1);
  and and_20 (out_3[3], s_r_ff_4_q, 1'b1, 1'b1);
  and and_21 (out_3[4], s_r_ff_5_q, 1'b1, 1'b1);
  and and_22 (out_3[5], s_r_ff_6_q, 1'b1, 1'b1);
  and and_23 (out_3[6], s_r_ff_7_q, 1'b1, 1'b1);
  and and_24 (out_3[7], s_r_ff_8_q, 1'b1, 1'b1);

  // Notes on the sheet:
  //   address
  //   R/W, 1=W 0=R
endmodule

module MAR (
  input  clock_bit,
  input  [3:0] in_2,
  output [3:0] out_3
);

  wire and_1_out, and_2_out, and_3_out, and_4_out, and_5_out, and_6_out, and_7_out, and_8_out, not_1_out,
       not_2_out, not_3_out, not_4_out, s_r_ff_1_q, s_r_ff_2_q, s_r_ff_3_q, s_r_ff_4_q;

  not not_1 (not_1_out, in_2[0]);
  not not_2 (not_2_out, in_2[1]);
  not not_3 (not_3_out, in_2[2]);
  not not_4 (not_4_out, in_2[3]);
  and and_1 (and_1_out, 1'b1, 1'b1, in_2[0]);
  and and_2 (and_2_out, not_1_out, 1'b1, 1'b1);
  and and_3 (and_3_out, 1'b1, 1'b1, in_2[1]);
  and and_4 (and_4_out, not_2_out, 1'b1, 1'b1);
  and and_5 (and_5_out, 1'b1, 1'b1, in_2[2]);
  and and_6 (and_6_out, not_3_out, 1'b1, 1'b1);
  and and_7 (and_7_out, 1'b1, 1'b1, in_2[3]);
  and and_8 (and_8_out, not_4_out, 1'b1, 1'b1);
  S_R_Flip_Flop s_r_ff_1 (.S(and_1_out), .R(and_2_out), .clk(clock_bit), .Q(s_r_ff_1_q));  // open: reset, Qn, preset
  S_R_Flip_Flop s_r_ff_2 (.S(and_3_out), .R(and_4_out), .clk(clock_bit), .Q(s_r_ff_2_q));  // open: reset, Qn, preset
  S_R_Flip_Flop s_r_ff_3 (.S(and_5_out), .R(and_6_out), .clk(clock_bit), .Q(s_r_ff_3_q));  // open: reset, Qn, preset
  S_R_Flip_Flop s_r_ff_4 (.S(and_7_out), .R(and_8_out), .clk(clock_bit), .Q(s_r_ff_4_q));  // open: reset, Qn, preset
  and and_9 (out_3[0], s_r_ff_1_q, 1'b1, 1'b1);
  and and_10 (out_3[1], s_r_ff_2_q, 1'b1, 1'b1);
  and and_11 (out_3[2], s_r_ff_3_q, 1'b1, 1'b1);
  and and_12 (out_3[3], s_r_ff_4_q, 1'b1, 1'b1);

  // Notes on the sheet:
  //   address
  //   R/W, 1=W 0=R
endmodule

module VoteRomny2017 (
  input  in_1,
  output out_2,
  output [7:0] out_3,
  output [7:0] out_4,
  output [7:0] out_5,
  output [7:0] out_6,
  output [7:0] out_7,
  output [7:0] out_8,
  output [7:0] out_9,
  output [7:0] out_10,
  output [7:0] out_11,
  output [7:0] out_12,
  output [7:0] out_13,
  output [7:0] out_14,
  output [7:0] out_15,
  output [7:0] out_16,
  output [7:0] out_17,
  output [7:0] out_18
);


  assign out_2 = in_1;
  assign out_3 = 8'h30;
  assign out_4 = 8'h1b;
  assign out_5 = 8'h48;
  assign out_6 = 8'h60;
  assign out_7 = 8'haf;
  assign out_8 = 8'hbe;
  assign out_9 = 8'h88;
  assign out_10 = 8'h6f;
  assign out_11 = 8'hbd;
  assign out_12 = 8'ha0;
  assign out_13 = 8'hd2;
  assign out_14 = 8'haf;
  assign out_15 = 8'hc0;
  assign out_16 = 8'h1;
  assign out_17 = 8'hf;
  assign out_18 = {8{1'b0}};

  // Notes on the sheet:
  //   Multiplier valuein RAM 
endmodule

module PC (
  input  clock_bit,
  input  [3:0] in_2,
  output [3:0] out_3
);

  wire and_1_out, and_2_out, and_3_out, and_4_out, and_5_out, and_6_out, and_7_out, and_8_out, not_1_out,
       not_2_out, not_3_out, not_4_out, s_r_ff_1_q, s_r_ff_2_q, s_r_ff_3_q, s_r_ff_4_q;

  not not_1 (not_1_out, in_2[0]);
  not not_2 (not_2_out, in_2[1]);
  not not_3 (not_3_out, in_2[2]);
  not not_4 (not_4_out, in_2[3]);
  and and_1 (and_1_out, 1'b1, 1'b1, in_2[0]);
  and and_2 (and_2_out, not_1_out, 1'b1, 1'b1);
  and and_3 (and_3_out, 1'b1, 1'b1, in_2[1]);
  and and_4 (and_4_out, not_2_out, 1'b1, 1'b1);
  and and_5 (and_5_out, 1'b1, 1'b1, in_2[2]);
  and and_6 (and_6_out, not_3_out, 1'b1, 1'b1);
  and and_7 (and_7_out, 1'b1, 1'b1, in_2[3]);
  and and_8 (and_8_out, not_4_out, 1'b1, 1'b1);
  S_R_Flip_Flop s_r_ff_1 (.S(and_1_out), .R(and_2_out), .clk(clock_bit), .Q(s_r_ff_1_q));  // open: reset, Qn, preset
  S_R_Flip_Flop s_r_ff_2 (.S(and_3_out), .R(and_4_out), .clk(clock_bit), .Q(s_r_ff_2_q));  // open: reset, Qn, preset
  S_R_Flip_Flop s_r_ff_3 (.S(and_5_out), .R(and_6_out), .clk(clock_bit), .Q(s_r_ff_3_q));  // open: reset, Qn, preset
  S_R_Flip_Flop s_r_ff_4 (.S(and_7_out), .R(and_8_out), .clk(clock_bit), .Q(s_r_ff_4_q));  // open: reset, Qn, preset
  and and_9 (out_3[0], s_r_ff_1_q, 1'b1, 1'b1);
  and and_10 (out_3[1], s_r_ff_2_q, 1'b1, 1'b1);
  and and_11 (out_3[2], s_r_ff_3_q, 1'b1, 1'b1);
  and and_12 (out_3[3], s_r_ff_4_q, 1'b1, 1'b1);

  // Notes on the sheet:
  //   address
  //   R/W, 1=W 0=R
endmodule

module INC (
  input  [3:0] in_1,
  input  in_2,
  output [3:0] out_3
);

  wire onebitadder_1_cout, onebitadder_2_cout, onebitadder_3_p3, onebitadder_3_p6;

  onebitadder onebitadder_1 (.A(in_1[0]), .B(in_2), .Sum(out_3[0]), .Cout(onebitadder_1_cout));  // open: Cin
  onebitadder onebitadder_2 (
    .Cin(onebitadder_1_cout), .A(in_1[1]), .Sum(out_3[1]), .Cout(onebitadder_2_cout));  // open: B
  // onebitadder onebitadder_3: pin names not known; wires that end beside it: onebitadder_2_cout, in_1[2], onebitadder_3_p3, onebitadder_3_p3, out_3[2], onebitadder_3_p6
  onebitadder onebitadder_4 (.Cin(onebitadder_3_p6), .A(in_1[3]), .Sum(out_3[3]));  // open: B, Cout
endmodule

module IR (
  input  [7:0] in_1,
  input  clock_bit,
  input  in_3,
  output [7:0] out_4
);

  wire and_1_out, and_2_out, and_3_out, and_4_out, and_5_out, and_6_out, and_7_out, and_8_out, and_9_out,
       and_10_out, and_11_out, and_12_out, and_13_out, and_14_out, and_15_out, and_16_out, not_2_out,
       not_3_out, not_4_out, not_5_out, not_6_out, not_7_out, not_8_out, not_9_out, s_r_ff_1_q, s_r_ff_2_q,
       s_r_ff_3_q, s_r_ff_4_q, s_r_ff_5_q, s_r_ff_6_q, s_r_ff_7_q, s_r_ff_8_q;
  wire [7:0] multiplexer_1_out, not_1_out;

  assign not_1_out = ~{8{1'b1}};  // NOT_Gate not_1, 8 bits wide
  Multiplexer #(.width(8), .enable("false")) multiplexer_1 (
    .in0(in_1), .in1(not_1_out), .out(multiplexer_1_out), .sel(in_3));
  not not_2 (not_2_out, multiplexer_1_out[0]);
  not not_3 (not_3_out, multiplexer_1_out[1]);
  not not_4 (not_4_out, multiplexer_1_out[2]);
  not not_5 (not_5_out, multiplexer_1_out[3]);
  not not_6 (not_6_out, multiplexer_1_out[4]);
  not not_7 (not_7_out, multiplexer_1_out[5]);
  not not_8 (not_8_out, multiplexer_1_out[6]);
  not not_9 (not_9_out, multiplexer_1_out[7]);
  and and_1 (and_1_out, 1'b1, 1'b1, multiplexer_1_out[0]);
  and and_2 (and_2_out, not_2_out, 1'b1, 1'b1);
  and and_3 (and_3_out, 1'b1, 1'b1, multiplexer_1_out[1]);
  and and_4 (and_4_out, not_3_out, 1'b1, 1'b1);
  and and_5 (and_5_out, 1'b1, 1'b1, multiplexer_1_out[2]);
  and and_6 (and_6_out, not_4_out, 1'b1, 1'b1);
  and and_7 (and_7_out, 1'b1, 1'b1, multiplexer_1_out[3]);
  and and_8 (and_8_out, not_5_out, 1'b1, 1'b1);
  and and_9 (and_9_out, 1'b1, 1'b1, multiplexer_1_out[4]);
  and and_10 (and_10_out, not_6_out, 1'b1, 1'b1);
  and and_11 (and_11_out, 1'b1, 1'b1, multiplexer_1_out[5]);
  and and_12 (and_12_out, not_7_out, 1'b1, 1'b1);
  and and_13 (and_13_out, 1'b1, 1'b1, multiplexer_1_out[6]);
  and and_14 (and_14_out, not_8_out, 1'b1, 1'b1);
  and and_15 (and_15_out, 1'b1, 1'b1, multiplexer_1_out[7]);
  and and_16 (and_16_out, not_9_out, 1'b1, 1'b1);
  S_R_Flip_Flop s_r_ff_1 (.S(and_1_out), .R(and_2_out), .clk(clock_bit), .Q(s_r_ff_1_q));  // open: reset, Qn, preset
  S_R_Flip_Flop s_r_ff_2 (.S(and_3_out), .R(and_4_out), .clk(clock_bit), .Q(s_r_ff_2_q));  // open: reset, Qn, preset
  S_R_Flip_Flop s_r_ff_3 (.S(and_5_out), .R(and_6_out), .clk(clock_bit), .Q(s_r_ff_3_q));  // open: reset, Qn, preset
  S_R_Flip_Flop s_r_ff_4 (.S(and_7_out), .R(and_8_out), .clk(clock_bit), .Q(s_r_ff_4_q));  // open: reset, Qn, preset
  S_R_Flip_Flop s_r_ff_5 (.S(and_9_out), .R(and_10_out), .clk(clock_bit), .Q(s_r_ff_5_q));  // open: reset, Qn, preset
  S_R_Flip_Flop s_r_ff_6 (.S(and_11_out), .R(and_12_out), .clk(clock_bit), .Q(s_r_ff_6_q));  // open: reset, Qn, preset
  S_R_Flip_Flop s_r_ff_7 (.S(and_13_out), .R(and_14_out), .clk(clock_bit), .Q(s_r_ff_7_q));  // open: reset, Qn, preset
  S_R_Flip_Flop s_r_ff_8 (.S(and_15_out), .R(and_16_out), .clk(clock_bit), .Q(s_r_ff_8_q));  // open: reset, Qn, preset
  and and_17 (out_4[0], s_r_ff_1_q, 1'b1, 1'b1);
  and and_18 (out_4[1], s_r_ff_2_q, 1'b1, 1'b1);
  and and_19 (out_4[2], s_r_ff_3_q, 1'b1, 1'b1);
  and and_20 (out_4[3], s_r_ff_4_q, 1'b1, 1'b1);
  and and_21 (out_4[4], s_r_ff_5_q, 1'b1, 1'b1);
  and and_22 (out_4[5], s_r_ff_6_q, 1'b1, 1'b1);
  and and_23 (out_4[6], s_r_ff_7_q, 1'b1, 1'b1);
  and and_24 (out_4[7], s_r_ff_8_q, 1'b1, 1'b1);

  // Notes on the sheet:
  //   address
  //   R/W, 1=W 0=R
endmodule

module ALU (
  input  [7:0] in_1,
  input  _0_add_1_subtract,
  input  in_3,
  input  [7:0] in_4,
  output [7:0] out_5,
  output [2:0] out_6
);

  wire and_1_out, and_2_out, and_3_out, not_1_out, not_2_out, not_4_out, not_5_out, not_6_out, not_7_out,
       not_8_out, not_9_out, not_10_out, not_11_out, not_12_out, not_13_out, onebitadder_1_cout,
       onebitadder_2_cout, onebitadder_3_cout, onebitadder_4_cout, onebitadder_5_cout, onebitadder_6_cout,
       onebitadder_7_cout, onebitadder_8_cout, xnor_1_out, xnor_2_out, xnor_3_out, xor_1_out;
  wire [2:0] and_4_out;
  wire [7:0] eightbitinc_1_out_2, multiplexer_1_out, not_3_out;

  // Probe on in_4
  // Probe on in_1
  Multiplexer #(.width(8), .enable("false")) multiplexer_1 (
    .in0(in_1), .in1(eightbitinc_1_out_2), .out(multiplexer_1_out), .sel(_0_add_1_subtract));
  not not_1 (not_1_out, multiplexer_1_out[7]);
  not not_2 (not_2_out, in_4[7]);
  assign not_3_out = ~in_1;  // NOT_Gate not_3, 8 bits wide
  xnor xnor_1 (xnor_1_out, not_1_out, not_4_out);
  xnor xnor_2 (xnor_2_out, not_2_out, not_1_out);
  eightbitINC eightbitinc_1 (.in_1(not_3_out), .out_2(eightbitinc_1_out_2));
  and and_1 (and_1_out, multiplexer_1_out[0], multiplexer_1_out[1], multiplexer_1_out[2], multiplexer_1_out[3], multiplexer_1_out[4], multiplexer_1_out[5], multiplexer_1_out[6], multiplexer_1_out[7]);
  onebitadder onebitadder_1 (
    .A(in_4[0]), .B(multiplexer_1_out[0]), .Sum(out_5[0]), .Cout(onebitadder_1_cout));  // open: Cin
  onebitadder onebitadder_2 (
    .Cin(onebitadder_1_cout), .A(in_4[1]), .B(multiplexer_1_out[1]), .Sum(out_5[1]), .Cout(onebitadder_2_cout));
  onebitadder onebitadder_3 (
    .Cin(onebitadder_2_cout), .A(in_4[2]), .B(multiplexer_1_out[2]), .Sum(out_5[2]), .Cout(onebitadder_3_cout));
  onebitadder onebitadder_4 (
    .Cin(onebitadder_3_cout), .A(in_4[3]), .B(multiplexer_1_out[3]), .Sum(out_5[3]), .Cout(onebitadder_4_cout));
  onebitadder onebitadder_5 (
    .Cin(onebitadder_4_cout), .A(in_4[4]), .B(multiplexer_1_out[4]), .Sum(out_5[4]), .Cout(onebitadder_5_cout));
  onebitadder onebitadder_6 (
    .Cin(onebitadder_5_cout), .A(in_4[5]), .B(multiplexer_1_out[5]), .Sum(out_5[5]), .Cout(onebitadder_6_cout));
  onebitadder onebitadder_7 (
    .Cin(onebitadder_6_cout), .A(in_4[6]), .B(multiplexer_1_out[6]), .Sum(out_5[6]), .Cout(onebitadder_7_cout));
  onebitadder onebitadder_8 (
    .Cin(onebitadder_7_cout), .A(in_4[7]), .B(multiplexer_1_out[7]), .Sum(out_5[7]), .Cout(onebitadder_8_cout));
  and and_2 (and_2_out, xnor_1_out, not_2_out);
  not not_4 (not_4_out, _0_add_1_subtract);
  xnor xnor_3 (xnor_3_out, not_4_out, xnor_2_out);
  not not_5 (not_5_out, out_5[7]);
  xor xor_1 (xor_1_out, not_5_out, and_2_out);
  // Probe on out_5
  and and_3 (and_3_out, xor_1_out, xnor_3_out);
  not not_6 (not_6_out, out_5[0]);
  or or_1 (and_4_out[2], and_1_out, and_3_out);
  not not_7 (not_7_out, out_5[1]);
  not not_8 (not_8_out, out_5[2]);
  not not_9 (not_9_out, out_5[3]);
  not not_10 (not_10_out, out_5[4]);
  not not_11 (not_11_out, out_5[5]);
  not not_12 (not_12_out, out_5[6]);
  not not_13 (not_13_out, out_5[7]);
  and and_4 (and_4_out[0], not_13_out, not_12_out, not_11_out, not_10_out, not_9_out, not_8_out, not_7_out, not_6_out);
  StatusRegister statusregister_1 (.in_1(in_3), .in_2({and_4_out[2], out_5[7], and_4_out[0]}), .out_3(out_6));

  // Notes on the sheet:
  //   CHECKS ELIGIBILITY OF OVERFLOW
  //   (1 = can overflow, 0 = cannot overflow)
  //   COMPARES EXPECTED SIGN WITH ACTUAL SIGN
  //   (1 = expected and actual don't match, 0 = expected and actual match)
  //   overflow, negative, 0
endmodule

module alupicker (
  input  [1:0] in_1,
  input  [7:0] in_2,
  input  [7:0] in_3,
  output [7:0] out_4,
  output [7:0] out_5
);

  Multiplexer #(.select(2), .width(8), .enable("false")) multiplexer_1 (
    .in2(in_3), .in3(in_2), .out(out_4), .sel(in_1));  // open: in0, in1
  Multiplexer #(.select(2), .width(8), .enable("false")) multiplexer_2 (
    .in2(in_2), .in3(in_3), .out(out_5), .sel(in_1));  // open: in0, in1

  // Notes on the sheet:
  //   cubit, regibit,tick
endmodule

module INC4bit (
  input  [3:0] in_1,
  output [3:0] out_2
);

  wire onebitadder_1_cout, onebitadder_2_cout, onebitadder_3_p3, onebitadder_3_p6;

  onebitadder onebitadder_1 (.A(in_1[0]), .B(1'b1), .Sum(out_2[0]), .Cout(onebitadder_1_cout));  // open: Cin
  onebitadder onebitadder_2 (
    .Cin(onebitadder_1_cout), .A(in_1[1]), .Sum(out_2[1]), .Cout(onebitadder_2_cout));  // open: B
  // onebitadder onebitadder_3: pin names not known; wires that end beside it: onebitadder_2_cout, in_1[2], onebitadder_3_p3, onebitadder_3_p3, out_2[2], onebitadder_3_p6
  onebitadder onebitadder_4 (.Cin(onebitadder_3_p6), .A(in_1[3]), .Sum(out_2[3]));  // open: B, Cout
endmodule

module eightbitINC (
  input  [7:0] in_1,
  output [7:0] out_2
);

  wire onebitadder_1_cout, onebitadder_2_cout, onebitadder_3_cout, onebitadder_4_cout, onebitadder_5_cout,
       onebitadder_6_cout, onebitadder_7_cout;

  onebitadder onebitadder_1 (.A(in_1[0]), .B(1'b1), .Sum(out_2[0]), .Cout(onebitadder_1_cout));  // open: Cin
  onebitadder onebitadder_2 (
    .Cin(onebitadder_1_cout), .A(in_1[1]), .Sum(out_2[1]), .Cout(onebitadder_2_cout));  // open: B
  onebitadder onebitadder_3 (
    .Cin(onebitadder_2_cout), .A(in_1[2]), .Sum(out_2[2]), .Cout(onebitadder_3_cout));  // open: B
  onebitadder onebitadder_4 (
    .Cin(onebitadder_3_cout), .A(in_1[3]), .Sum(out_2[3]), .Cout(onebitadder_4_cout));  // open: B
  onebitadder onebitadder_5 (
    .Cin(onebitadder_4_cout), .A(in_1[4]), .Sum(out_2[4]), .Cout(onebitadder_5_cout));  // open: B
  onebitadder onebitadder_6 (
    .Cin(onebitadder_5_cout), .A(in_1[5]), .Sum(out_2[5]), .Cout(onebitadder_6_cout));  // open: B
  onebitadder onebitadder_7 (
    .Cin(onebitadder_6_cout), .A(in_1[6]), .Sum(out_2[6]), .Cout(onebitadder_7_cout));  // open: B
  onebitadder onebitadder_8 (.Cin(onebitadder_7_cout), .A(in_1[7]), .Sum(out_2[7]));  // open: B, Cout
endmodule

module onebitadder (
  input  Cin,
  input  A,
  input  B,
  output Sum,
  output Cout
);

  wire and_1_out, and_2_out, and_3_out, and_4_out, and_5_out, not_1_out, or_1_out;

  and and_1 (and_1_out, Cin, A, B);
  or or_1 (or_1_out, Cin, A, B);
  not not_1 (not_1_out, Cout);
  and and_2 (and_2_out, Cin, A);
  and and_3 (and_3_out, B, Cin);
  and and_4 (and_4_out, A, B);
  and and_5 (and_5_out, or_1_out, not_1_out);
  or or_2 (Cout, and_2_out, and_3_out, and_4_out);
  or or_3 (Sum, and_1_out, and_5_out);
endmodule

module L (
  input  clock_bit,
  input  [7:0] in_2,
  output [7:0] out_3
);

  wire and_1_out, and_2_out, and_3_out, and_4_out, and_5_out, and_6_out, and_7_out, and_8_out, and_9_out,
       and_10_out, and_11_out, and_12_out, and_13_out, and_14_out, and_15_out, and_16_out, not_1_out,
       not_2_out, not_3_out, not_4_out, not_5_out, not_6_out, not_7_out, not_8_out, s_r_ff_1_q, s_r_ff_2_q,
       s_r_ff_3_q, s_r_ff_4_q, s_r_ff_5_q, s_r_ff_6_q, s_r_ff_7_q, s_r_ff_8_q;

  not not_1 (not_1_out, in_2[0]);
  not not_2 (not_2_out, in_2[1]);
  not not_3 (not_3_out, in_2[2]);
  not not_4 (not_4_out, in_2[3]);
  not not_5 (not_5_out, in_2[4]);
  not not_6 (not_6_out, in_2[5]);
  not not_7 (not_7_out, in_2[6]);
  not not_8 (not_8_out, in_2[7]);
  and and_1 (and_1_out, 1'b1, 1'b1, in_2[0]);
  and and_2 (and_2_out, not_1_out, 1'b1, 1'b1);
  and and_3 (and_3_out, 1'b1, 1'b1, in_2[1]);
  and and_4 (and_4_out, not_2_out, 1'b1, 1'b1);
  and and_5 (and_5_out, 1'b1, 1'b1, in_2[2]);
  and and_6 (and_6_out, not_3_out, 1'b1, 1'b1);
  and and_7 (and_7_out, 1'b1, 1'b1, in_2[3]);
  and and_8 (and_8_out, not_4_out, 1'b1, 1'b1);
  and and_9 (and_9_out, 1'b1, 1'b1, in_2[4]);
  and and_10 (and_10_out, not_5_out, 1'b1, 1'b1);
  and and_11 (and_11_out, 1'b1, 1'b1, in_2[5]);
  and and_12 (and_12_out, not_6_out, 1'b1, 1'b1);
  and and_13 (and_13_out, 1'b1, 1'b1, in_2[6]);
  and and_14 (and_14_out, not_7_out, 1'b1, 1'b1);
  and and_15 (and_15_out, 1'b1, 1'b1, in_2[7]);
  and and_16 (and_16_out, not_8_out, 1'b1, 1'b1);
  S_R_Flip_Flop s_r_ff_1 (.S(and_1_out), .R(and_2_out), .clk(clock_bit), .Q(s_r_ff_1_q));  // open: reset, Qn, preset
  S_R_Flip_Flop s_r_ff_2 (.S(and_3_out), .R(and_4_out), .clk(clock_bit), .Q(s_r_ff_2_q));  // open: reset, Qn, preset
  S_R_Flip_Flop s_r_ff_3 (.S(and_5_out), .R(and_6_out), .clk(clock_bit), .Q(s_r_ff_3_q));  // open: reset, Qn, preset
  S_R_Flip_Flop s_r_ff_4 (.S(and_7_out), .R(and_8_out), .clk(clock_bit), .Q(s_r_ff_4_q));  // open: reset, Qn, preset
  S_R_Flip_Flop s_r_ff_5 (.S(and_9_out), .R(and_10_out), .clk(clock_bit), .Q(s_r_ff_5_q));  // open: reset, Qn, preset
  S_R_Flip_Flop s_r_ff_6 (.S(and_11_out), .R(and_12_out), .clk(clock_bit), .Q(s_r_ff_6_q));  // open: reset, Qn, preset
  S_R_Flip_Flop s_r_ff_7 (.S(and_13_out), .R(and_14_out), .clk(clock_bit), .Q(s_r_ff_7_q));  // open: reset, Qn, preset
  S_R_Flip_Flop s_r_ff_8 (.S(and_15_out), .R(and_16_out), .clk(clock_bit), .Q(s_r_ff_8_q));  // open: reset, Qn, preset
  and and_17 (out_3[0], s_r_ff_1_q, 1'b1, 1'b1);
  and and_18 (out_3[1], s_r_ff_2_q, 1'b1, 1'b1);
  and and_19 (out_3[2], s_r_ff_3_q, 1'b1, 1'b1);
  and and_20 (out_3[3], s_r_ff_4_q, 1'b1, 1'b1);
  and and_21 (out_3[4], s_r_ff_5_q, 1'b1, 1'b1);
  and and_22 (out_3[5], s_r_ff_6_q, 1'b1, 1'b1);
  and and_23 (out_3[6], s_r_ff_7_q, 1'b1, 1'b1);
  and and_24 (out_3[7], s_r_ff_8_q, 1'b1, 1'b1);

  // Notes on the sheet:
  //   address
  //   R/W, 1=W 0=R
endmodule

module R (
  input  clock_bit,
  input  [7:0] in_2,
  output [7:0] out_3
);

  wire and_1_out, and_2_out, and_3_out, and_4_out, and_5_out, and_6_out, and_7_out, and_8_out, and_9_out,
       and_10_out, and_11_out, and_12_out, and_13_out, and_14_out, and_15_out, and_16_out, not_1_out,
       not_2_out, not_3_out, not_4_out, not_5_out, not_6_out, not_7_out, not_8_out, s_r_ff_1_q, s_r_ff_2_q,
       s_r_ff_3_q, s_r_ff_4_q, s_r_ff_5_q, s_r_ff_6_q, s_r_ff_7_q, s_r_ff_8_q;

  not not_1 (not_1_out, in_2[0]);
  not not_2 (not_2_out, in_2[1]);
  not not_3 (not_3_out, in_2[2]);
  not not_4 (not_4_out, in_2[3]);
  not not_5 (not_5_out, in_2[4]);
  not not_6 (not_6_out, in_2[5]);
  not not_7 (not_7_out, in_2[6]);
  not not_8 (not_8_out, in_2[7]);
  and and_1 (and_1_out, 1'b1, 1'b1, in_2[0]);
  and and_2 (and_2_out, not_1_out, 1'b1, 1'b1);
  and and_3 (and_3_out, 1'b1, 1'b1, in_2[1]);
  and and_4 (and_4_out, not_2_out, 1'b1, 1'b1);
  and and_5 (and_5_out, 1'b1, 1'b1, in_2[2]);
  and and_6 (and_6_out, not_3_out, 1'b1, 1'b1);
  and and_7 (and_7_out, 1'b1, 1'b1, in_2[3]);
  and and_8 (and_8_out, not_4_out, 1'b1, 1'b1);
  and and_9 (and_9_out, 1'b1, 1'b1, in_2[4]);
  and and_10 (and_10_out, not_5_out, 1'b1, 1'b1);
  and and_11 (and_11_out, 1'b1, 1'b1, in_2[5]);
  and and_12 (and_12_out, not_6_out, 1'b1, 1'b1);
  and and_13 (and_13_out, 1'b1, 1'b1, in_2[6]);
  and and_14 (and_14_out, not_7_out, 1'b1, 1'b1);
  and and_15 (and_15_out, 1'b1, 1'b1, in_2[7]);
  and and_16 (and_16_out, not_8_out, 1'b1, 1'b1);
  S_R_Flip_Flop s_r_ff_1 (.S(and_1_out), .R(and_2_out), .clk(clock_bit), .Q(s_r_ff_1_q));  // open: reset, Qn, preset
  S_R_Flip_Flop s_r_ff_2 (.S(and_3_out), .R(and_4_out), .clk(clock_bit), .Q(s_r_ff_2_q));  // open: reset, Qn, preset
  S_R_Flip_Flop s_r_ff_3 (.S(and_5_out), .R(and_6_out), .clk(clock_bit), .Q(s_r_ff_3_q));  // open: reset, Qn, preset
  S_R_Flip_Flop s_r_ff_4 (.S(and_7_out), .R(and_8_out), .clk(clock_bit), .Q(s_r_ff_4_q));  // open: reset, Qn, preset
  S_R_Flip_Flop s_r_ff_5 (.S(and_9_out), .R(and_10_out), .clk(clock_bit), .Q(s_r_ff_5_q));  // open: reset, Qn, preset
  S_R_Flip_Flop s_r_ff_6 (.S(and_11_out), .R(and_12_out), .clk(clock_bit), .Q(s_r_ff_6_q));  // open: reset, Qn, preset
  S_R_Flip_Flop s_r_ff_7 (.S(and_13_out), .R(and_14_out), .clk(clock_bit), .Q(s_r_ff_7_q));  // open: reset, Qn, preset
  S_R_Flip_Flop s_r_ff_8 (.S(and_15_out), .R(and_16_out), .clk(clock_bit), .Q(s_r_ff_8_q));  // open: reset, Qn, preset
  and and_17 (out_3[0], s_r_ff_1_q, 1'b1, 1'b1);
  and and_18 (out_3[1], s_r_ff_2_q, 1'b1, 1'b1);
  and and_19 (out_3[2], s_r_ff_3_q, 1'b1, 1'b1);
  and and_20 (out_3[3], s_r_ff_4_q, 1'b1, 1'b1);
  and and_21 (out_3[4], s_r_ff_5_q, 1'b1, 1'b1);
  and and_22 (out_3[5], s_r_ff_6_q, 1'b1, 1'b1);
  and and_23 (out_3[6], s_r_ff_7_q, 1'b1, 1'b1);
  and and_24 (out_3[7], s_r_ff_8_q, 1'b1, 1'b1);

  // Notes on the sheet:
  //   address
  //   R/W, 1=W 0=R
endmodule

module A (
  input  clock_bit,
  input  [7:0] in_2,
  output [7:0] out_3
);

  wire and_1_out, and_2_out, and_3_out, and_4_out, and_5_out, and_6_out, and_7_out, and_8_out, and_9_out,
       and_10_out, and_11_out, and_12_out, and_13_out, and_14_out, and_15_out, and_16_out, not_1_out,
       not_2_out, not_3_out, not_4_out, not_5_out, not_6_out, not_7_out, not_8_out, s_r_ff_1_q, s_r_ff_2_q,
       s_r_ff_3_q, s_r_ff_4_q, s_r_ff_5_q, s_r_ff_6_q, s_r_ff_7_q, s_r_ff_8_q;

  not not_1 (not_1_out, in_2[0]);
  not not_2 (not_2_out, in_2[1]);
  not not_3 (not_3_out, in_2[2]);
  not not_4 (not_4_out, in_2[3]);
  not not_5 (not_5_out, in_2[4]);
  not not_6 (not_6_out, in_2[5]);
  not not_7 (not_7_out, in_2[6]);
  not not_8 (not_8_out, in_2[7]);
  and and_1 (and_1_out, 1'b1, 1'b1, in_2[0]);
  and and_2 (and_2_out, not_1_out, 1'b1, 1'b1);
  and and_3 (and_3_out, 1'b1, 1'b1, in_2[1]);
  and and_4 (and_4_out, not_2_out, 1'b1, 1'b1);
  and and_5 (and_5_out, 1'b1, 1'b1, in_2[2]);
  and and_6 (and_6_out, not_3_out, 1'b1, 1'b1);
  and and_7 (and_7_out, 1'b1, 1'b1, in_2[3]);
  and and_8 (and_8_out, not_4_out, 1'b1, 1'b1);
  and and_9 (and_9_out, 1'b1, 1'b1, in_2[4]);
  and and_10 (and_10_out, not_5_out, 1'b1, 1'b1);
  and and_11 (and_11_out, 1'b1, 1'b1, in_2[5]);
  and and_12 (and_12_out, not_6_out, 1'b1, 1'b1);
  and and_13 (and_13_out, 1'b1, 1'b1, in_2[6]);
  and and_14 (and_14_out, not_7_out, 1'b1, 1'b1);
  and and_15 (and_15_out, 1'b1, 1'b1, in_2[7]);
  and and_16 (and_16_out, not_8_out, 1'b1, 1'b1);
  S_R_Flip_Flop #(.trigger("falling")) s_r_ff_1 (
    .S(and_1_out), .R(and_2_out), .clk(clock_bit), .Q(s_r_ff_1_q));  // open: reset, Qn, preset
  S_R_Flip_Flop #(.trigger("falling")) s_r_ff_2 (
    .S(and_3_out), .R(and_4_out), .clk(clock_bit), .Q(s_r_ff_2_q));  // open: reset, Qn, preset
  S_R_Flip_Flop #(.trigger("falling")) s_r_ff_3 (
    .S(and_5_out), .R(and_6_out), .clk(clock_bit), .Q(s_r_ff_3_q));  // open: reset, Qn, preset
  S_R_Flip_Flop #(.trigger("falling")) s_r_ff_4 (
    .S(and_7_out), .R(and_8_out), .clk(clock_bit), .Q(s_r_ff_4_q));  // open: reset, Qn, preset
  S_R_Flip_Flop #(.trigger("falling")) s_r_ff_5 (
    .S(and_9_out), .R(and_10_out), .clk(clock_bit), .Q(s_r_ff_5_q));  // open: reset, Qn, preset
  S_R_Flip_Flop #(.trigger("falling")) s_r_ff_6 (
    .S(and_11_out), .R(and_12_out), .clk(clock_bit), .Q(s_r_ff_6_q));  // open: reset, Qn, preset
  S_R_Flip_Flop #(.trigger("falling")) s_r_ff_7 (
    .S(and_13_out), .R(and_14_out), .clk(clock_bit), .Q(s_r_ff_7_q));  // open: reset, Qn, preset
  S_R_Flip_Flop #(.trigger("falling")) s_r_ff_8 (
    .S(and_15_out), .R(and_16_out), .clk(clock_bit), .Q(s_r_ff_8_q));  // open: reset, Qn, preset
  and and_17 (out_3[0], s_r_ff_1_q, 1'b1, 1'b1);
  and and_18 (out_3[1], s_r_ff_2_q, 1'b1, 1'b1);
  and and_19 (out_3[2], s_r_ff_3_q, 1'b1, 1'b1);
  and and_20 (out_3[3], s_r_ff_4_q, 1'b1, 1'b1);
  and and_21 (out_3[4], s_r_ff_5_q, 1'b1, 1'b1);
  and and_22 (out_3[5], s_r_ff_6_q, 1'b1, 1'b1);
  and and_23 (out_3[6], s_r_ff_7_q, 1'b1, 1'b1);
  and and_24 (out_3[7], s_r_ff_8_q, 1'b1, 1'b1);

  // Notes on the sheet:
  //   address
  //   R/W, 1=W 0=R
endmodule

module StatusRegister (
  input  in_1,
  input  [2:0] in_2,
  output [2:0] out_3
);

  D_Flip_Flop #(.trigger("falling")) d_ff_1 (.D(in_2[0]), .clk(in_1), .Q(out_3[0]));  // open: Qn, preset, reset
  D_Flip_Flop #(.trigger("falling")) d_ff_2 (.D(in_2[1]), .clk(in_1), .Q(out_3[1]));  // open: Qn, preset, reset
  D_Flip_Flop #(.trigger("falling")) d_ff_3 (.D(in_2[2]), .clk(in_1), .Q(out_3[2]));  // open: Qn, preset, reset

  // Notes on the sheet:
  //   Falling Edge
endmodule

module D0 (
  input  clock_bit,
  input  [7:0] in_2,
  output [7:0] out_3
);

  wire and_1_out, and_2_out, and_3_out, and_4_out, and_5_out, and_6_out, and_7_out, and_8_out, and_9_out,
       and_10_out, and_11_out, and_12_out, and_13_out, and_14_out, and_15_out, and_16_out, not_1_out,
       not_2_out, not_3_out, not_4_out, not_5_out, not_6_out, not_7_out, not_8_out, s_r_ff_1_q, s_r_ff_2_q,
       s_r_ff_3_q, s_r_ff_4_q, s_r_ff_5_q, s_r_ff_6_q, s_r_ff_7_q, s_r_ff_8_q;

  not not_1 (not_1_out, in_2[0]);
  not not_2 (not_2_out, in_2[1]);
  not not_3 (not_3_out, in_2[2]);
  not not_4 (not_4_out, in_2[3]);
  not not_5 (not_5_out, in_2[4]);
  not not_6 (not_6_out, in_2[5]);
  not not_7 (not_7_out, in_2[6]);
  not not_8 (not_8_out, in_2[7]);
  and and_1 (and_1_out, 1'b1, 1'b1, in_2[0]);
  and and_2 (and_2_out, not_1_out, 1'b1, 1'b1);
  and and_3 (and_3_out, 1'b1, 1'b1, in_2[1]);
  and and_4 (and_4_out, not_2_out, 1'b1, 1'b1);
  and and_5 (and_5_out, 1'b1, 1'b1, in_2[2]);
  and and_6 (and_6_out, not_3_out, 1'b1, 1'b1);
  and and_7 (and_7_out, 1'b1, 1'b1, in_2[3]);
  and and_8 (and_8_out, not_4_out, 1'b1, 1'b1);
  and and_9 (and_9_out, 1'b1, 1'b1, in_2[4]);
  and and_10 (and_10_out, not_5_out, 1'b1, 1'b1);
  and and_11 (and_11_out, 1'b1, 1'b1, in_2[5]);
  and and_12 (and_12_out, not_6_out, 1'b1, 1'b1);
  and and_13 (and_13_out, 1'b1, 1'b1, in_2[6]);
  and and_14 (and_14_out, not_7_out, 1'b1, 1'b1);
  and and_15 (and_15_out, 1'b1, 1'b1, in_2[7]);
  and and_16 (and_16_out, not_8_out, 1'b1, 1'b1);
  S_R_Flip_Flop #(.trigger("falling")) s_r_ff_1 (
    .S(and_1_out), .R(and_2_out), .clk(clock_bit), .Q(s_r_ff_1_q));  // open: reset, Qn, preset
  S_R_Flip_Flop #(.trigger("falling")) s_r_ff_2 (
    .S(and_3_out), .R(and_4_out), .clk(clock_bit), .Q(s_r_ff_2_q));  // open: reset, Qn, preset
  S_R_Flip_Flop #(.trigger("falling")) s_r_ff_3 (
    .S(and_5_out), .R(and_6_out), .clk(clock_bit), .Q(s_r_ff_3_q));  // open: reset, Qn, preset
  S_R_Flip_Flop #(.trigger("falling")) s_r_ff_4 (
    .S(and_7_out), .R(and_8_out), .clk(clock_bit), .Q(s_r_ff_4_q));  // open: reset, Qn, preset
  S_R_Flip_Flop #(.trigger("falling")) s_r_ff_5 (
    .S(and_9_out), .R(and_10_out), .clk(clock_bit), .Q(s_r_ff_5_q));  // open: reset, Qn, preset
  S_R_Flip_Flop #(.trigger("falling")) s_r_ff_6 (
    .S(and_11_out), .R(and_12_out), .clk(clock_bit), .Q(s_r_ff_6_q));  // open: reset, Qn, preset
  S_R_Flip_Flop #(.trigger("falling")) s_r_ff_7 (
    .S(and_13_out), .R(and_14_out), .clk(clock_bit), .Q(s_r_ff_7_q));  // open: reset, Qn, preset
  S_R_Flip_Flop #(.trigger("falling")) s_r_ff_8 (
    .S(and_15_out), .R(and_16_out), .clk(clock_bit), .Q(s_r_ff_8_q));  // open: reset, Qn, preset
  and and_17 (out_3[0], s_r_ff_1_q, 1'b1, 1'b1);
  and and_18 (out_3[1], s_r_ff_2_q, 1'b1, 1'b1);
  and and_19 (out_3[2], s_r_ff_3_q, 1'b1, 1'b1);
  and and_20 (out_3[3], s_r_ff_4_q, 1'b1, 1'b1);
  and and_21 (out_3[4], s_r_ff_5_q, 1'b1, 1'b1);
  and and_22 (out_3[5], s_r_ff_6_q, 1'b1, 1'b1);
  and and_23 (out_3[6], s_r_ff_7_q, 1'b1, 1'b1);
  and and_24 (out_3[7], s_r_ff_8_q, 1'b1, 1'b1);

  // Notes on the sheet:
  //   address
  //   R/W, 1=W 0=R
endmodule

module D1 (
  input  clock_bit,
  input  [7:0] in_2,
  output [7:0] out_3
);

  wire and_1_out, and_2_out, and_3_out, and_4_out, and_5_out, and_6_out, and_7_out, and_8_out, and_9_out,
       and_10_out, and_11_out, and_12_out, and_13_out, and_14_out, and_15_out, and_16_out, not_1_out,
       not_2_out, not_3_out, not_4_out, not_5_out, not_6_out, not_7_out, not_8_out, s_r_ff_1_q, s_r_ff_2_q,
       s_r_ff_3_q, s_r_ff_4_q, s_r_ff_5_q, s_r_ff_6_q, s_r_ff_7_q, s_r_ff_8_q;

  not not_1 (not_1_out, in_2[0]);
  not not_2 (not_2_out, in_2[1]);
  not not_3 (not_3_out, in_2[2]);
  not not_4 (not_4_out, in_2[3]);
  not not_5 (not_5_out, in_2[4]);
  not not_6 (not_6_out, in_2[5]);
  not not_7 (not_7_out, in_2[6]);
  not not_8 (not_8_out, in_2[7]);
  and and_1 (and_1_out, 1'b1, 1'b1, in_2[0]);
  and and_2 (and_2_out, not_1_out, 1'b1, 1'b1);
  and and_3 (and_3_out, 1'b1, 1'b1, in_2[1]);
  and and_4 (and_4_out, not_2_out, 1'b1, 1'b1);
  and and_5 (and_5_out, 1'b1, 1'b1, in_2[2]);
  and and_6 (and_6_out, not_3_out, 1'b1, 1'b1);
  and and_7 (and_7_out, 1'b1, 1'b1, in_2[3]);
  and and_8 (and_8_out, not_4_out, 1'b1, 1'b1);
  and and_9 (and_9_out, 1'b1, 1'b1, in_2[4]);
  and and_10 (and_10_out, not_5_out, 1'b1, 1'b1);
  and and_11 (and_11_out, 1'b1, 1'b1, in_2[5]);
  and and_12 (and_12_out, not_6_out, 1'b1, 1'b1);
  and and_13 (and_13_out, 1'b1, 1'b1, in_2[6]);
  and and_14 (and_14_out, not_7_out, 1'b1, 1'b1);
  and and_15 (and_15_out, 1'b1, 1'b1, in_2[7]);
  and and_16 (and_16_out, not_8_out, 1'b1, 1'b1);
  S_R_Flip_Flop #(.trigger("falling")) s_r_ff_1 (
    .S(and_1_out), .R(and_2_out), .clk(clock_bit), .Q(s_r_ff_1_q));  // open: reset, Qn, preset
  S_R_Flip_Flop #(.trigger("falling")) s_r_ff_2 (
    .S(and_3_out), .R(and_4_out), .clk(clock_bit), .Q(s_r_ff_2_q));  // open: reset, Qn, preset
  S_R_Flip_Flop #(.trigger("falling")) s_r_ff_3 (
    .S(and_5_out), .R(and_6_out), .clk(clock_bit), .Q(s_r_ff_3_q));  // open: reset, Qn, preset
  S_R_Flip_Flop #(.trigger("falling")) s_r_ff_4 (
    .S(and_7_out), .R(and_8_out), .clk(clock_bit), .Q(s_r_ff_4_q));  // open: reset, Qn, preset
  S_R_Flip_Flop #(.trigger("falling")) s_r_ff_5 (
    .S(and_9_out), .R(and_10_out), .clk(clock_bit), .Q(s_r_ff_5_q));  // open: reset, Qn, preset
  S_R_Flip_Flop #(.trigger("falling")) s_r_ff_6 (
    .S(and_11_out), .R(and_12_out), .clk(clock_bit), .Q(s_r_ff_6_q));  // open: reset, Qn, preset
  S_R_Flip_Flop #(.trigger("falling")) s_r_ff_7 (
    .S(and_13_out), .R(and_14_out), .clk(clock_bit), .Q(s_r_ff_7_q));  // open: reset, Qn, preset
  S_R_Flip_Flop #(.trigger("falling")) s_r_ff_8 (
    .S(and_15_out), .R(and_16_out), .clk(clock_bit), .Q(s_r_ff_8_q));  // open: reset, Qn, preset
  and and_17 (out_3[0], s_r_ff_1_q, 1'b1, 1'b1);
  and and_18 (out_3[1], s_r_ff_2_q, 1'b1, 1'b1);
  and and_19 (out_3[2], s_r_ff_3_q, 1'b1, 1'b1);
  and and_20 (out_3[3], s_r_ff_4_q, 1'b1, 1'b1);
  and and_21 (out_3[4], s_r_ff_5_q, 1'b1, 1'b1);
  and and_22 (out_3[5], s_r_ff_6_q, 1'b1, 1'b1);
  and and_23 (out_3[6], s_r_ff_7_q, 1'b1, 1'b1);
  and and_24 (out_3[7], s_r_ff_8_q, 1'b1, 1'b1);

  // Notes on the sheet:
  //   address
  //   R/W, 1=W 0=R
endmodule

module NUMPAD (
  input  _0,
  input  _1,
  input  _2,
  input  _3,
  input  _4,
  input  _5,
  input  _6,
  input  _7,
  input  _8,
  input  _9,
  output [7:0] out_11
);

  or or_1 (out_11[0], _1, _3, _5, _7, _9);
  or or_2 (out_11[1], _7, _2, _3, _6);
  or or_3 (out_11[2], _4, _5, _7, _6);
  or or_4 (out_11[3], _8, _9);
  // Probe on {4'b0000, out_11[3:0]}

  assign out_11[7:4] = 4'b0000;
endmodule

module numpadbuffer (
  input  clock_bit,
  input  [7:0] in_2,
  output [7:0] out_3
);

  wire and_1_out, and_2_out, and_3_out, and_4_out, and_5_out, and_6_out, and_7_out, and_8_out, and_9_out,
       and_10_out, and_11_out, and_12_out, and_13_out, and_14_out, and_15_out, and_16_out, not_1_out,
       not_2_out, not_3_out, not_4_out, not_5_out, not_6_out, not_7_out, not_8_out, s_r_ff_1_q, s_r_ff_2_q,
       s_r_ff_3_q, s_r_ff_4_q, s_r_ff_5_q, s_r_ff_6_q, s_r_ff_7_q, s_r_ff_8_q;

  not not_1 (not_1_out, in_2[0]);
  not not_2 (not_2_out, in_2[1]);
  not not_3 (not_3_out, in_2[2]);
  not not_4 (not_4_out, in_2[3]);
  not not_5 (not_5_out, in_2[4]);
  not not_6 (not_6_out, in_2[5]);
  not not_7 (not_7_out, in_2[6]);
  not not_8 (not_8_out, in_2[7]);
  and and_1 (and_1_out, 1'b1, 1'b1, in_2[0]);
  and and_2 (and_2_out, not_1_out, 1'b1, 1'b1);
  and and_3 (and_3_out, 1'b1, 1'b1, in_2[1]);
  and and_4 (and_4_out, not_2_out, 1'b1, 1'b1);
  and and_5 (and_5_out, 1'b1, 1'b1, in_2[2]);
  and and_6 (and_6_out, not_3_out, 1'b1, 1'b1);
  and and_7 (and_7_out, 1'b1, 1'b1, in_2[3]);
  and and_8 (and_8_out, not_4_out, 1'b1, 1'b1);
  and and_9 (and_9_out, 1'b1, 1'b1, in_2[4]);
  and and_10 (and_10_out, not_5_out, 1'b1, 1'b1);
  and and_11 (and_11_out, 1'b1, 1'b1, in_2[5]);
  and and_12 (and_12_out, not_6_out, 1'b1, 1'b1);
  and and_13 (and_13_out, 1'b1, 1'b1, in_2[6]);
  and and_14 (and_14_out, not_7_out, 1'b1, 1'b1);
  and and_15 (and_15_out, 1'b1, 1'b1, in_2[7]);
  and and_16 (and_16_out, not_8_out, 1'b1, 1'b1);
  S_R_Flip_Flop #(.trigger("falling")) s_r_ff_1 (
    .S(and_1_out), .R(and_2_out), .clk(clock_bit), .Q(s_r_ff_1_q));  // open: reset, Qn, preset
  S_R_Flip_Flop #(.trigger("falling")) s_r_ff_2 (
    .S(and_3_out), .R(and_4_out), .clk(clock_bit), .Q(s_r_ff_2_q));  // open: reset, Qn, preset
  S_R_Flip_Flop #(.trigger("falling")) s_r_ff_3 (
    .S(and_5_out), .R(and_6_out), .clk(clock_bit), .Q(s_r_ff_3_q));  // open: reset, Qn, preset
  S_R_Flip_Flop #(.trigger("falling")) s_r_ff_4 (
    .S(and_7_out), .R(and_8_out), .clk(clock_bit), .Q(s_r_ff_4_q));  // open: reset, Qn, preset
  S_R_Flip_Flop #(.trigger("falling")) s_r_ff_5 (
    .S(and_9_out), .R(and_10_out), .clk(clock_bit), .Q(s_r_ff_5_q));  // open: reset, Qn, preset
  S_R_Flip_Flop #(.trigger("falling")) s_r_ff_6 (
    .S(and_11_out), .R(and_12_out), .clk(clock_bit), .Q(s_r_ff_6_q));  // open: reset, Qn, preset
  S_R_Flip_Flop #(.trigger("falling")) s_r_ff_7 (
    .S(and_13_out), .R(and_14_out), .clk(clock_bit), .Q(s_r_ff_7_q));  // open: reset, Qn, preset
  S_R_Flip_Flop #(.trigger("falling")) s_r_ff_8 (
    .S(and_15_out), .R(and_16_out), .clk(clock_bit), .Q(s_r_ff_8_q));  // open: reset, Qn, preset
  and and_17 (out_3[0], s_r_ff_1_q, 1'b1, 1'b1);
  and and_18 (out_3[1], s_r_ff_2_q, 1'b1, 1'b1);
  and and_19 (out_3[2], s_r_ff_3_q, 1'b1, 1'b1);
  and and_20 (out_3[3], s_r_ff_4_q, 1'b1, 1'b1);
  and and_21 (out_3[4], s_r_ff_5_q, 1'b1, 1'b1);
  and and_22 (out_3[5], s_r_ff_6_q, 1'b1, 1'b1);
  and and_23 (out_3[6], s_r_ff_7_q, 1'b1, 1'b1);
  and and_24 (out_3[7], s_r_ff_8_q, 1'b1, 1'b1);

  // Notes on the sheet:
  //   address
  //   R/W, 1=W 0=R
endmodule

module RWbit (
  input  clock_bit,
  input  in_2,
  output out_3
);

  wire and_1_out, and_2_out, not_1_out, s_r_ff_1_q;

  not not_1 (not_1_out, in_2);
  and and_1 (and_1_out, 1'b1, 1'b1, in_2);
  and and_2 (and_2_out, not_1_out, 1'b1, 1'b1);
  S_R_Flip_Flop s_r_ff_1 (.S(and_1_out), .R(and_2_out), .clk(clock_bit), .Q(s_r_ff_1_q));  // open: reset, Qn, preset
  and and_3 (out_3, s_r_ff_1_q, 1'b1, 1'b1);

  // Notes on the sheet:
  //   address
  //   R/W, 1=W 0=R
endmodule
module digi2 (
  input  i8,
  input  i7,
  input  i6,
  input  i5,
  input  i4,
  input  i3,
  input  i2,
  input  i1,
  output A,
  output B,
  output C,
  output D,
  output E,
  output F,
  output G
);

  wire and_1_out, and_2_out, and_3_out, and_4_out, and_5_out, and_6_out, and_7_out, and_8_out, and_9_out,
       and_10_out, and_11_out, and_12_out, and_13_out, and_14_out, and_15_out, and_16_out, and_17_out,
       and_18_out, and_19_out, and_20_out, and_21_out, and_22_out, and_23_out, and_24_out, and_25_out,
       and_26_out, and_27_out, and_28_out, and_29_out, and_30_out, and_31_out, and_32_out, and_33_out,
       and_34_out, and_35_out, and_36_out, and_37_out, and_38_out, and_39_out, and_40_out, and_41_out,
       and_42_out, and_43_out, and_44_out, and_45_out, and_46_out, and_47_out, and_48_out, and_49_out,
       and_50_out, and_51_out, and_52_out, and_53_out, and_54_out, and_55_out, and_56_out, and_57_out,
       and_58_out, and_59_out, and_60_out, and_61_out, and_62_out, and_63_out, and_64_out, and_65_out,
       and_66_out, and_67_out, and_68_out, and_69_out, and_70_out, and_71_out, and_72_out, and_73_out,
       and_74_out, and_75_out, and_76_out, and_77_out, and_78_out, and_79_out, and_80_out, and_81_out,
       and_82_out, and_83_out, and_84_out, and_85_out, and_86_out, and_87_out, and_88_out, and_89_out,
       and_90_out, and_91_out, and_92_out, and_93_out, and_94_out, and_95_out, and_96_out, and_97_out,
       and_98_out, and_99_out, and_100_out, and_101_out, and_102_out, and_103_out, and_104_out, and_105_out,
       and_106_out, and_107_out, and_108_out, and_109_out, and_110_out, and_111_out, and_112_out,
       and_113_out, and_114_out, and_115_out, and_116_out, and_117_out, and_118_out, and_119_out,
       and_120_out, and_121_out, and_122_out, not_1_out, not_2_out, not_3_out, not_4_out, not_5_out,
       not_6_out, not_7_out, not_8_out, not_9_out, not_10_out, not_11_out, not_12_out, not_13_out,
       not_14_out, not_15_out, not_16_out, not_17_out, not_18_out, not_19_out, not_20_out, not_21_out,
       not_22_out, not_23_out, not_24_out, not_25_out, not_26_out, not_27_out, not_28_out, not_29_out,
       not_30_out, not_31_out, not_32_out, not_33_out, not_34_out, not_35_out, not_36_out, not_37_out,
       not_38_out, not_39_out, not_40_out, not_41_out, not_42_out, not_43_out, not_44_out, not_45_out,
       not_46_out, not_47_out, not_48_out, not_49_out, not_50_out, not_51_out, not_52_out, not_53_out,
       not_54_out, not_55_out, not_56_out, not_57_out, not_58_out, not_59_out, not_60_out, not_61_out,
       not_62_out, not_63_out, not_64_out, not_65_out, not_66_out, not_67_out, not_68_out, not_69_out,
       not_70_out, not_71_out, not_72_out, not_73_out, not_74_out, not_75_out, not_76_out, not_77_out,
       not_78_out, not_79_out, not_80_out, not_81_out, not_82_out, not_83_out, not_84_out, not_85_out,
       not_86_out, not_87_out, not_88_out, not_89_out, not_90_out, not_91_out, not_92_out, not_93_out,
       not_94_out, not_95_out, not_96_out, not_97_out, not_98_out, not_99_out, not_100_out, not_101_out,
       not_102_out, not_103_out, not_104_out, not_105_out, not_106_out, not_107_out, not_108_out,
       not_109_out, not_110_out, not_111_out, not_112_out, not_113_out, not_114_out, not_115_out,
       not_116_out, not_117_out, not_118_out, not_119_out, not_120_out, not_121_out, not_122_out,
       not_123_out, not_124_out, not_125_out, not_126_out, not_127_out, not_128_out, not_129_out,
       not_130_out, not_131_out, not_132_out, not_133_out, not_134_out, not_135_out, not_136_out,
       not_137_out, not_138_out, not_139_out, not_140_out, not_141_out, not_142_out, not_143_out,
       not_144_out, not_145_out, not_146_out, not_147_out, not_148_out, not_149_out, not_150_out,
       not_151_out, not_152_out, not_153_out, not_154_out, not_155_out, not_156_out, not_157_out,
       not_158_out, not_159_out, not_160_out, not_161_out, not_162_out, not_163_out, not_164_out,
       not_165_out, not_166_out, not_167_out, not_168_out, not_169_out, not_170_out, not_171_out,
       not_172_out, not_173_out, not_174_out, not_175_out, not_176_out, not_177_out, not_178_out,
       not_179_out, not_180_out, not_181_out, not_182_out, not_183_out, not_184_out, not_185_out,
       not_186_out, not_187_out, not_188_out, not_189_out, not_190_out, not_191_out, not_192_out,
       not_193_out, not_194_out, not_195_out, not_196_out, not_197_out, not_198_out, not_199_out,
       not_200_out, not_201_out, not_202_out, not_203_out, not_204_out, not_205_out, not_206_out,
       not_207_out, not_208_out, not_209_out, not_210_out, not_211_out, not_212_out, not_213_out,
       not_214_out, not_215_out, not_216_out, not_217_out, not_218_out, not_219_out, not_220_out,
       not_221_out, not_222_out, not_223_out, not_224_out, not_225_out, not_226_out, not_227_out,
       not_228_out, not_229_out, not_230_out, not_231_out, not_232_out, not_233_out, not_234_out,
       not_235_out, not_236_out, not_237_out, not_238_out, not_239_out, not_240_out, not_241_out,
       not_242_out, not_243_out, not_244_out, not_245_out, not_246_out, not_247_out, not_248_out,
       not_249_out, not_250_out, not_251_out, not_252_out, not_253_out, not_254_out, not_255_out,
       not_256_out, not_257_out, not_258_out, not_259_out, not_260_out, not_261_out, not_262_out,
       not_263_out, not_264_out, not_265_out, not_266_out, not_267_out, not_268_out, not_269_out,
       not_270_out, not_271_out, not_272_out, not_273_out, not_274_out, not_275_out, not_276_out, not_277_out;

  not not_1 (not_1_out, i6);
  not not_2 (not_2_out, i5);
  not not_3 (not_3_out, i3);
  not not_4 (not_4_out, i2);
  not not_5 (not_5_out, i5);
  not not_6 (not_6_out, i4);
  not not_7 (not_7_out, i8);
  not not_8 (not_8_out, i7);
  not not_9 (not_9_out, i4);
  not not_10 (not_10_out, i7);
  not not_11 (not_11_out, i8);
  not not_12 (not_12_out, i7);
  not not_13 (not_13_out, i7);
  not not_14 (not_14_out, i8);
  not not_15 (not_15_out, i6);
  not not_16 (not_16_out, i6);
  not not_17 (not_17_out, i4);
  not not_18 (not_18_out, i3);
  not not_19 (not_19_out, i2);
  not not_20 (not_20_out, i5);
  not not_21 (not_21_out, i3);
  not not_22 (not_22_out, i5);
  not not_23 (not_23_out, i2);
  not not_24 (not_24_out, i5);
  not not_25 (not_25_out, i3);
  not not_26 (not_26_out, i7);
  not not_27 (not_27_out, i5);
  not not_28 (not_28_out, i8);
  not not_29 (not_29_out, i7);
  not not_30 (not_30_out, i5);
  not not_31 (not_31_out, i7);
  not not_32 (not_32_out, i6);
  not not_33 (not_33_out, i4);
  not not_34 (not_34_out, i3);
  not not_35 (not_35_out, i8);
  not not_36 (not_36_out, i6);
  not not_37 (not_37_out, i8);
  not not_38 (not_38_out, i6);
  not not_39 (not_39_out, i5);
  not not_40 (not_40_out, i5);
  not not_41 (not_41_out, i8);
  not not_42 (not_42_out, i6);
  not not_43 (not_43_out, i4);
  not not_44 (not_44_out, i3);
  not not_45 (not_45_out, i2);
  not not_46 (not_46_out, i8);
  not not_47 (not_47_out, i5);
  not not_48 (not_48_out, i6);
  not not_49 (not_49_out, i5);
  not not_50 (not_50_out, i6);
  not not_51 (not_51_out, i4);
  not not_52 (not_52_out, i2);
  not not_53 (not_53_out, i7);
  not not_54 (not_54_out, i4);
  not not_55 (not_55_out, i6);
  not not_56 (not_56_out, i3);
  not not_57 (not_57_out, i2);
  not not_58 (not_58_out, i8);
  not not_59 (not_59_out, i5);
  not not_60 (not_60_out, i8);
  not not_61 (not_61_out, i4);
  not not_62 (not_62_out, i3);
  not not_63 (not_63_out, i6);
  not not_64 (not_64_out, i5);
  not not_65 (not_65_out, i5);
  not not_66 (not_66_out, i5);
  not not_67 (not_67_out, i7);
  not not_68 (not_68_out, i7);
  not not_69 (not_69_out, i8);
  not not_70 (not_70_out, i6);
  not not_71 (not_71_out, i8);
  not not_72 (not_72_out, i4);
  not not_73 (not_73_out, i6);
  not not_74 (not_74_out, i5);
  not not_75 (not_75_out, i7);
  not not_76 (not_76_out, i4);
  not not_77 (not_77_out, i3);
  not not_78 (not_78_out, i7);
  not not_79 (not_79_out, i6);
  not not_80 (not_80_out, i5);
  not not_81 (not_81_out, i3);
  not not_82 (not_82_out, i2);
  not not_83 (not_83_out, i7);
  not not_84 (not_84_out, i5);
  not not_85 (not_85_out, i4);
  not not_86 (not_86_out, i8);
  not not_87 (not_87_out, i7);
  not not_88 (not_88_out, i4);
  not not_89 (not_89_out, i7);
  not not_90 (not_90_out, i4);
  not not_91 (not_91_out, i8);
  not not_92 (not_92_out, i3);
  not not_93 (not_93_out, i2);
  not not_94 (not_94_out, i7);
  not not_95 (not_95_out, i6);
  not not_96 (not_96_out, i7);
  not not_97 (not_97_out, i3);
  not not_98 (not_98_out, i7);
  not not_99 (not_99_out, i2);
  not not_100 (not_100_out, i8);
  not not_101 (not_101_out, i7);
  not not_102 (not_102_out, i4);
  not not_103 (not_103_out, i7);
  not not_104 (not_104_out, i4);
  not not_105 (not_105_out, i5);
  not not_106 (not_106_out, i4);
  not not_107 (not_107_out, i8);
  not not_108 (not_108_out, i8);
  not not_109 (not_109_out, i6);
  not not_110 (not_110_out, i4);
  not not_111 (not_111_out, i3);
  not not_112 (not_112_out, i8);
  not not_113 (not_113_out, i6);
  not not_114 (not_114_out, i4);
  not not_115 (not_115_out, i2);
  not not_116 (not_116_out, i8);
  not not_117 (not_117_out, i6);
  not not_118 (not_118_out, i4);
  not not_119 (not_119_out, i6);
  not not_120 (not_120_out, i4);
  not not_121 (not_121_out, i3);
  not not_122 (not_122_out, i2);
  not not_123 (not_123_out, i5);
  not not_124 (not_124_out, i2);
  not not_125 (not_125_out, i3);
  not not_126 (not_126_out, i7);
  not not_127 (not_127_out, i6);
  not not_128 (not_128_out, i3);
  not not_129 (not_129_out, i7);
  not not_130 (not_130_out, i3);
  not not_131 (not_131_out, i2);
  not not_132 (not_132_out, i5);
  not not_133 (not_133_out, i4);
  not not_134 (not_134_out, i5);
  not not_135 (not_135_out, i8);
  not not_136 (not_136_out, i6);
  not not_137 (not_137_out, i5);
  not not_138 (not_138_out, i4);
  not not_139 (not_139_out, i3);
  not not_140 (not_140_out, i7);
  not not_141 (not_141_out, i6);
  not not_142 (not_142_out, i5);
  not not_143 (not_143_out, i4);
  not not_144 (not_144_out, i3);
  not not_145 (not_145_out, i2);
  not not_146 (not_146_out, i8);
  not not_147 (not_147_out, i7);
  not not_148 (not_148_out, i6);
  not not_149 (not_149_out, i4);
  not not_150 (not_150_out, i8);
  not not_151 (not_151_out, i6);
  not not_152 (not_152_out, i4);
  not not_153 (not_153_out, i2);
  not not_154 (not_154_out, i8);
  not not_155 (not_155_out, i7);
  not not_156 (not_156_out, i6);
  not not_157 (not_157_out, i3);
  not not_158 (not_158_out, i2);
  not not_159 (not_159_out, i8);
  not not_160 (not_160_out, i7);
  not not_161 (not_161_out, i6);
  not not_162 (not_162_out, i3);
  not not_163 (not_163_out, i8);
  not not_164 (not_164_out, i7);
  not not_165 (not_165_out, i6);
  not not_166 (not_166_out, i2);
  not not_167 (not_167_out, i8);
  not not_168 (not_168_out, i6);
  not not_169 (not_169_out, i3);
  not not_170 (not_170_out, i2);
  not not_171 (not_171_out, i8);
  not not_172 (not_172_out, i8);
  not not_173 (not_173_out, i6);
  not not_174 (not_174_out, i4);
  not not_175 (not_175_out, i6);
  not not_176 (not_176_out, i4);
  not not_177 (not_177_out, i3);
  not not_178 (not_178_out, i2);
  not not_179 (not_179_out, i8);
  not not_180 (not_180_out, i5);
  not not_181 (not_181_out, i4);
  not not_182 (not_182_out, i8);
  not not_183 (not_183_out, i3);
  not not_184 (not_184_out, i8);
  not not_185 (not_185_out, i2);
  not not_186 (not_186_out, i5);
  not not_187 (not_187_out, i4);
  not not_188 (not_188_out, i3);
  not not_189 (not_189_out, i5);
  not not_190 (not_190_out, i4);
  not not_191 (not_191_out, i2);
  not not_192 (not_192_out, i7);
  not not_193 (not_193_out, i4);
  not not_194 (not_194_out, i7);
  not not_195 (not_195_out, i3);
  not not_196 (not_196_out, i2);
  not not_197 (not_197_out, i7);
  not not_198 (not_198_out, i2);
  not not_199 (not_199_out, i7);
  not not_200 (not_200_out, i3);
  not not_201 (not_201_out, i6);
  not not_202 (not_202_out, i5);
  not not_203 (not_203_out, i6);
  not not_204 (not_204_out, i8);
  not not_205 (not_205_out, i7);
  not not_206 (not_206_out, i6);
  not not_207 (not_207_out, i5);
  not not_208 (not_208_out, i4);
  not not_209 (not_209_out, i8);
  not not_210 (not_210_out, i7);
  not not_211 (not_211_out, i6);
  not not_212 (not_212_out, i5);
  not not_213 (not_213_out, i3);
  not not_214 (not_214_out, i2);
  not not_215 (not_215_out, i8);
  not not_216 (not_216_out, i7);
  not not_217 (not_217_out, i8);
  not not_218 (not_218_out, i5);
  not not_219 (not_219_out, i3);
  not not_220 (not_220_out, i8);
  not not_221 (not_221_out, i5);
  not not_222 (not_222_out, i2);
  not not_223 (not_223_out, i7);
  not not_224 (not_224_out, i3);
  not not_225 (not_225_out, i2);
  not not_226 (not_226_out, i8);
  not not_227 (not_227_out, i7);
  not not_228 (not_228_out, i8);
  not not_229 (not_229_out, i6);
  not not_230 (not_230_out, i4);
  not not_231 (not_231_out, i2);
  not not_232 (not_232_out, i8);
  not not_233 (not_233_out, i5);
  not not_234 (not_234_out, i4);
  not not_235 (not_235_out, i3);
  not not_236 (not_236_out, i6);
  not not_237 (not_237_out, i4);
  not not_238 (not_238_out, i3);
  not not_239 (not_239_out, i2);
  not not_240 (not_240_out, i8);
  not not_241 (not_241_out, i6);
  not not_242 (not_242_out, i8);
  not not_243 (not_243_out, i5);
  not not_244 (not_244_out, i4);
  not not_245 (not_245_out, i7);
  not not_246 (not_246_out, i6);
  not not_247 (not_247_out, i7);
  not not_248 (not_248_out, i6);
  not not_249 (not_249_out, i7);
  not not_250 (not_250_out, i7);
  not not_251 (not_251_out, i7);
  not not_252 (not_252_out, i5);
  not not_253 (not_253_out, i4);
  not not_254 (not_254_out, i6);
  not not_255 (not_255_out, i5);
  not not_256 (not_256_out, i7);
  not not_257 (not_257_out, i8);
  not not_258 (not_258_out, i7);
  not not_259 (not_259_out, i8);
  not not_260 (not_260_out, i7);
  not not_261 (not_261_out, i7);
  not not_262 (not_262_out, i5);
  not not_263 (not_263_out, i3);
  not not_264 (not_264_out, i2);
  not not_265 (not_265_out, i8);
  not not_266 (not_266_out, i6);
  not not_267 (not_267_out, i4);
  not not_268 (not_268_out, i2);
  not not_269 (not_269_out, i5);
  not not_270 (not_270_out, i4);
  not not_271 (not_271_out, i3);
  not not_272 (not_272_out, i8);
  not not_273 (not_273_out, i6);
  not not_274 (not_274_out, i7);
  not not_275 (not_275_out, i6);
  not not_276 (not_276_out, i5);
  not not_277 (not_277_out, i4);
  and and_1 (and_1_out, not_1_out, not_2_out, not_3_out, not_4_out);
  and and_2 (and_2_out, not_5_out, not_6_out);
  and and_3 (and_3_out, not_7_out, not_8_out, not_9_out, i3);
  and and_4 (and_4_out, not_10_out, i5, i3, i2);
  and and_5 (and_5_out, not_11_out, i5, i4);
  and and_6 (and_6_out, not_12_out, i5, i4);
  and and_7 (and_7_out, i5, i4, i3);
  and and_8 (and_8_out, not_13_out, i6, i5, i2);
  and and_9 (and_9_out, not_14_out, i7, not_15_out);
  and and_10 (and_10_out, i7, not_16_out, not_17_out, not_18_out, not_19_out);
  and and_11 (and_11_out, i7, not_20_out, not_21_out);
  and and_12 (and_12_out, i7, not_22_out, not_23_out);
  and and_13 (and_13_out, i8, not_24_out, not_25_out);
  and and_14 (and_14_out, i8, not_26_out, i6);
  and and_15 (and_15_out, i8, i6, i4, i2);
  and and_16 (and_16_out, i8, i7, not_27_out);
  and and_17 (and_17_out, not_28_out, not_29_out, not_30_out);
  and and_18 (and_18_out, not_31_out, not_32_out, not_33_out, not_34_out);
  and and_19 (and_19_out, not_35_out, not_36_out, i3, i2);
  and and_20 (and_20_out, not_37_out, not_38_out, i4);
  and and_21 (and_21_out, not_39_out, i4, i2);
  and and_22 (and_22_out, not_40_out, i4, i3);
  and and_23 (and_23_out, not_41_out, not_42_out, i5);
  and and_24 (and_24_out, i5, not_43_out, not_44_out, not_45_out);
  and and_25 (and_25_out, not_46_out, i7, i5);
  and and_26 (and_26_out, i7, i6, not_47_out);
  and and_27 (and_27_out, i8, not_48_out, not_49_out);
  and and_28 (and_28_out, i8, not_50_out, not_51_out, not_52_out);
  and and_29 (and_29_out, i8, not_53_out, i6, i5);
  and and_30 (and_30_out, i8, i6, i5, not_54_out);
  and and_31 (and_31_out, i8, i7, not_55_out);
  and and_32 (and_32_out, i8, i7, not_56_out, not_57_out);
  and and_33 (and_33_out, not_58_out, not_59_out);
  and and_34 (and_34_out, not_60_out, not_61_out, not_62_out);
  and and_35 (and_35_out, not_63_out, not_64_out, i2);
  and and_36 (and_36_out, not_65_out, i3, i2);
  and and_37 (and_37_out, not_66_out, i4);
  and and_38 (and_38_out, not_67_out, i4, i3, i2);
  and and_39 (and_39_out, not_68_out, i6);
  and and_40 (and_40_out, not_69_out, i7, not_70_out);
  and and_41 (and_41_out, not_71_out, i7, not_72_out);
  and and_42 (and_42_out, i7, not_73_out, not_74_out);
  and and_43 (and_43_out, i8, not_75_out, i3);
  and and_44 (and_44_out, i8, i5, not_76_out);
  and and_45 (and_45_out, i8, i5, not_77_out);
  and and_46 (and_46_out, i8, i6, i5);
  and and_47 (and_47_out, not_78_out, not_79_out, not_80_out, not_81_out, not_82_out);
  and and_48 (and_48_out, not_83_out, not_84_out, not_85_out);
  and and_49 (and_49_out, not_86_out, not_87_out, not_88_out, i3);
  and and_50 (and_50_out, not_89_out, not_90_out, i3, i2);
  and and_51 (and_51_out, not_91_out, i5, i4, not_92_out, not_93_out);
  and and_52 (and_52_out, not_94_out, not_95_out, i5, i4);
  and and_53 (and_53_out, not_96_out, i5, i4, not_97_out);
  and and_54 (and_54_out, not_98_out, i5, i4, not_99_out);
  and and_55 (and_55_out, not_100_out, not_101_out, i6, not_102_out, i2);
  and and_56 (and_56_out, not_103_out, i6, not_104_out, i3);
  and and_57 (and_57_out, i6, not_105_out, not_106_out, i3);
  and and_58 (and_58_out, not_107_out, i6, i5, i4);
  and and_59 (and_59_out, not_108_out, i7, not_109_out, not_110_out, not_111_out);
  and and_60 (and_60_out, not_112_out, i7, not_113_out, not_114_out, not_115_out);
  and and_61 (and_61_out, not_116_out, i7, not_117_out, i5, not_118_out);
  and and_62 (and_62_out, i7, not_119_out, i5, not_120_out, not_121_out, not_122_out);
  and and_63 (and_63_out, i7, i6, not_123_out, i4, not_124_out);
  and and_64 (and_64_out, i7, i6, i4, not_125_out, i2);
  and and_65 (and_65_out, i8, not_126_out, not_127_out, i4, not_128_out);
  and and_66 (and_66_out, i8, not_129_out, i4, not_130_out, not_131_out);
  and and_67 (and_67_out, i8, i6, not_132_out, not_133_out);
  and and_68 (and_68_out, i8, i7, not_134_out, i4);
  and and_69 (and_69_out, i8, i7, i4, i3);
  and and_70 (and_70_out, not_135_out, not_136_out, not_137_out, not_138_out, not_139_out);
  and and_71 (and_71_out, not_140_out, not_141_out, not_142_out, not_143_out, not_144_out, not_145_out);
  and and_72 (and_72_out, not_146_out, not_147_out, not_148_out, not_149_out, i3);
  and and_73 (and_73_out, not_150_out, not_151_out, not_152_out, i3, not_153_out);
  and and_74 (and_74_out, not_154_out, not_155_out, not_156_out, i4, not_157_out, not_158_out);
  and and_75 (and_75_out, not_159_out, not_160_out, not_161_out, i5, i4, not_162_out);
  and and_76 (and_76_out, not_163_out, not_164_out, not_165_out, i5, i4, not_166_out);
  and and_77 (and_77_out, not_167_out, not_168_out, i5, i4, not_169_out, not_170_out);
  and and_78 (and_78_out, not_171_out, i6, i5, i4, i3);
  and and_79 (and_79_out, not_172_out, i7, not_173_out, i5, not_174_out);
  and and_80 (and_80_out, i7, not_175_out, i5, not_176_out, not_177_out, not_178_out);
  and and_81 (and_81_out, not_179_out, i7, i6, not_180_out, not_181_out, i3);
  and and_82 (and_82_out, not_182_out, i7, i6, i4, not_183_out);
  and and_83 (and_83_out, not_184_out, i7, i6, i4, not_185_out);
  and and_84 (and_84_out, i8, i6, not_186_out, not_187_out, not_188_out);
  and and_85 (and_85_out, i8, i6, not_189_out, not_190_out, not_191_out);
  and and_86 (and_86_out, i8, not_192_out, i6, not_193_out, i3);
  and and_87 (and_87_out, i8, not_194_out, i6, i4, not_195_out, not_196_out);
  and and_88 (and_88_out, i8, not_197_out, i6, i5, i3, not_198_out);
  and and_89 (and_89_out, i8, not_199_out, i6, i5, i4, not_200_out);
  and and_90 (and_90_out, i8, i7, not_201_out, not_202_out, i4);
  and and_91 (and_91_out, i8, i7, not_203_out, i4, i3);
  and and_92 (and_92_out, not_204_out, not_205_out, not_206_out, not_207_out, not_208_out);
  and and_93 (and_93_out, not_209_out, not_210_out, not_211_out, not_212_out, not_213_out, not_214_out);
  and and_94 (and_94_out, not_215_out, not_216_out, i6, i4);
  and and_95 (and_95_out, not_217_out, i6, not_218_out, i4, not_219_out);
  and and_96 (and_96_out, not_220_out, i6, not_221_out, i4, not_222_out);
  and and_97 (and_97_out, not_223_out, i6, i4, not_224_out, not_225_out);
  and and_98 (and_98_out, not_226_out, not_227_out, i6, i5);
  and and_99 (and_99_out, not_228_out, i7, not_229_out, not_230_out, not_231_out);
  and and_100 (and_100_out, not_232_out, i7, not_233_out, not_234_out, not_235_out);
  and and_101 (and_101_out, i7, not_236_out, not_237_out, not_238_out, not_239_out);
  and and_102 (and_102_out, not_240_out, i7, not_241_out, i5);
  and and_103 (and_103_out, i7, not_243_out);
  and and_104 (and_104_out, i8, not_245_out, not_246_out, i4, i3);
  and and_105 (and_105_out, i8, not_247_out, not_248_out, i5);
  and and_106 (and_106_out, i8, not_249_out, i5, i3);
  and and_107 (and_107_out, i8, not_250_out, i5, i4);
  and and_108 (and_108_out, i8, not_251_out, i6, not_252_out, not_253_out);
  and and_109 (and_109_out, i8, i7, not_254_out, not_255_out);
  and and_110 (and_110_out, i8, i7, i6, i5);
  and and_111 (and_111_out, not_256_out, i5, i3);
  and and_112 (and_112_out, not_257_out, i5, i4);
  and and_113 (and_113_out, not_258_out, i5, i4);
  and and_114 (and_114_out, i5, i4, i3);
  and and_115 (and_115_out, not_259_out, not_260_out, i6);
  and and_116 (and_116_out, not_261_out, i6, not_262_out, not_263_out, not_264_out);
  and and_117 (and_117_out, not_265_out, i7, not_266_out, not_267_out, not_268_out);
  and and_118 (and_118_out, i7, not_269_out, not_270_out, not_271_out);
  and and_119 (and_119_out, not_272_out, i7, not_273_out, i5);
  and and_120 (and_120_out, i8, not_274_out, not_275_out);
  and and_121 (and_121_out, i8, not_276_out, not_277_out);
  and and_122 (and_122_out, i8, i7, i6);
  or or_1 (A, and_1_out, and_2_out, and_3_out, and_4_out, and_5_out, and_6_out, and_7_out, and_8_out, and_9_out, and_10_out, and_11_out, and_12_out, and_13_out, and_14_out, and_15_out, and_16_out);
  or or_2 (B, and_17_out, and_18_out, and_19_out, and_20_out, and_21_out, and_22_out, and_23_out, and_24_out, and_25_out, and_26_out, and_27_out, and_28_out, and_29_out, and_30_out, and_31_out, and_32_out);
  or or_3 (C, and_33_out, and_34_out, and_35_out, and_36_out, and_37_out, and_38_out, and_39_out, and_40_out, and_41_out, and_42_out, and_43_out, and_44_out, and_45_out, and_46_out);
  or or_4 (G, and_111_out, and_112_out, and_113_out, and_114_out, and_115_out, and_116_out, and_117_out, and_118_out, and_119_out, and_120_out, and_121_out, and_122_out);
  or or_5 (D, and_47_out, and_48_out, and_49_out, and_50_out, and_51_out, and_52_out, and_53_out, and_54_out, and_55_out, and_56_out, and_57_out, and_58_out, and_59_out, and_60_out, and_61_out, and_62_out, and_63_out, and_64_out, and_65_out, and_66_out, and_67_out, and_68_out, and_69_out);
  or or_6 (E, and_70_out, and_71_out, and_72_out, and_73_out, and_74_out, and_75_out, and_76_out, and_77_out, and_78_out, and_79_out, and_80_out, and_81_out, and_82_out, and_83_out, and_84_out, and_85_out, and_86_out, and_87_out, and_88_out, and_89_out, and_90_out, and_91_out);
  or or_7 (F, and_92_out, and_93_out, and_94_out, and_95_out, and_96_out, and_97_out, and_98_out, and_99_out, and_100_out, and_101_out, and_102_out, and_103_out, and_104_out, and_105_out, and_106_out, and_107_out, and_108_out, and_109_out, and_110_out);
endmodule

module digi1 (
  input  i8,
  input  i7,
  input  i6,
  input  i5,
  input  i4,
  input  i3,
  input  i2,
  input  i1,
  output A,
  output B,
  output C,
  output D,
  output E,
  output F,
  output G
);

  wire and_1_out, and_2_out, and_3_out, and_4_out, and_5_out, and_6_out, and_7_out, and_8_out, and_9_out,
       and_10_out, and_11_out, and_12_out, and_13_out, and_14_out, and_15_out, and_16_out, and_17_out,
       and_18_out, and_19_out, and_20_out, and_21_out, and_22_out, and_23_out, and_24_out, and_25_out,
       not_1_out, not_2_out, not_3_out, not_4_out, not_5_out, not_6_out, not_7_out, not_8_out, not_9_out,
       not_10_out, not_11_out, not_12_out, not_13_out, not_14_out, not_15_out, not_16_out, not_17_out,
       not_18_out, not_19_out, not_20_out, not_21_out, not_22_out, not_23_out, not_24_out, not_25_out,
       not_26_out, not_27_out, not_28_out, not_29_out, not_30_out, not_31_out, not_32_out, not_33_out,
       not_34_out, not_35_out, not_36_out, not_37_out, not_38_out, not_39_out, not_40_out, not_41_out,
       not_42_out, not_43_out;

  not not_1 (not_1_out, i8);
  not not_2 (not_2_out, i7);
  not not_3 (not_3_out, i8);
  not not_4 (not_4_out, i6);
  not not_5 (not_5_out, i8);
  not not_6 (not_6_out, i5);
  not not_7 (not_7_out, i4);
  not not_8 (not_8_out, i3);
  not not_9 (not_9_out, i6);
  not not_10 (not_10_out, i6);
  not not_11 (not_11_out, i6);
  not not_12 (not_12_out, i5);
  not not_13 (not_13_out, i4);
  not not_14 (not_14_out, i8);
  not not_15 (not_15_out, i7);
  not not_16 (not_16_out, i8);
  not not_17 (not_17_out, i6);
  not not_18 (not_18_out, i8);
  not not_19 (not_19_out, i5);
  not not_20 (not_20_out, i4);
  not not_21 (not_21_out, i3);
  not not_22 (not_22_out, i6);
  not not_23 (not_23_out, i6);
  not not_24 (not_24_out, i8);
  not not_25 (not_25_out, i7);
  not not_26 (not_26_out, i8);
  not not_27 (not_27_out, i6);
  not not_28 (not_28_out, i8);
  not not_29 (not_29_out, i5);
  not not_30 (not_30_out, i4);
  not not_31 (not_31_out, i3);
  not not_32 (not_32_out, i6);
  not not_33 (not_33_out, i6);
  not not_34 (not_34_out, i8);
  not not_35 (not_35_out, i7);
  not not_36 (not_36_out, i8);
  not not_37 (not_37_out, i6);
  not not_38 (not_38_out, i8);
  not not_39 (not_39_out, i5);
  not not_40 (not_40_out, i4);
  not not_41 (not_41_out, i3);
  and and_1 (and_1_out, i8, i7, i4);
  and and_2 (and_2_out, i8, i7, i5);
  and and_3 (and_3_out, i8, i7, i6);
  and and_4 (and_4_out, not_1_out, not_2_out);
  and and_5 (and_5_out, not_3_out, not_4_out);
  and and_6 (and_6_out, not_5_out, not_6_out, not_7_out, not_8_out);
  and and_7 (and_7_out, i7, not_9_out, i4);
  and and_8 (and_8_out, i7, not_10_out, i5);
  and and_9 (and_9_out, i8, i7, i6);
  not not_42 (not_42_out, i8);
  not not_43 (not_43_out, i7);
  and and_10 (and_10_out, not_11_out, not_12_out, not_13_out);
  and and_11 (and_11_out, not_14_out, not_15_out);
  and and_12 (and_12_out, not_16_out, not_17_out);
  and and_13 (and_13_out, not_18_out, not_19_out, not_20_out, not_21_out);
  and and_14 (and_14_out, i7, not_22_out, i4);
  and and_15 (and_15_out, i7, not_23_out, i5);
  and and_16 (and_16_out, i8, i7, i6);
  and and_17 (and_17_out, not_24_out, not_25_out);
  and and_18 (and_18_out, not_26_out, not_27_out);
  and and_19 (and_19_out, not_28_out, not_29_out, not_30_out, not_31_out);
  and and_20 (and_20_out, i7, not_32_out, i4);
  and and_21 (and_21_out, i7, not_33_out, i5);
  and and_22 (and_22_out, i8, i7, i6);
  and and_23 (and_23_out, not_34_out, not_35_out);
  and and_24 (and_24_out, not_36_out, not_37_out);
  and and_25 (and_25_out, not_38_out, not_39_out, not_40_out, not_41_out);
  or or_1 (G, and_1_out, and_2_out, and_3_out);
  or or_2 (A, and_4_out, and_5_out, and_6_out, and_7_out, and_8_out, and_9_out);
  or or_3 (C, not_42_out, not_43_out, and_10_out);
  or or_4 (D, and_11_out, and_12_out, and_13_out, and_14_out, and_15_out, and_16_out);
  or or_5 (E, and_17_out, and_18_out, and_19_out, and_20_out, and_21_out, and_22_out);
  or or_6 (F, and_23_out, and_24_out, and_25_out);

  assign B = 1'b1;
endmodule
module digi3 (
  input  i8,
  input  i7,
  input  i6,
  input  i5,
  input  i4,
  input  i3,
  input  i2,
  input  i1,
  output A,
  output B,
  output C,
  output D,
  output E,
  output F,
  output G
);

  wire and_1_out, and_2_out, and_3_out, and_4_out, and_5_out, and_6_out, and_7_out, and_8_out, and_9_out,
       and_10_out, and_11_out, and_12_out, and_13_out, and_14_out, and_15_out, and_16_out, and_17_out,
       and_18_out, and_19_out, and_20_out, and_21_out, and_22_out, and_23_out, and_24_out, and_25_out,
       and_26_out, and_27_out, and_28_out, and_29_out, and_30_out, and_31_out, and_32_out, and_33_out,
       and_34_out, and_35_out, and_36_out, and_37_out, and_38_out, and_39_out, and_40_out, and_41_out,
       and_42_out, and_43_out, and_44_out, and_45_out, and_46_out, and_47_out, and_48_out, and_49_out,
       and_50_out, and_51_out, and_52_out, and_53_out, and_54_out, and_55_out, and_56_out, and_57_out,
       and_58_out, and_59_out, and_60_out, and_61_out, and_62_out, and_63_out, and_64_out, and_65_out,
       and_66_out, and_67_out, and_68_out, and_69_out, and_70_out, and_71_out, and_72_out, and_73_out,
       and_74_out, and_75_out, and_76_out, and_77_out, and_78_out, and_79_out, and_80_out, and_81_out,
       and_82_out, and_83_out, and_84_out, and_85_out, and_86_out, and_87_out, and_88_out, and_89_out,
       and_90_out, and_91_out, and_92_out, and_93_out, and_94_out, and_95_out, and_96_out, and_97_out,
       and_98_out, and_99_out, and_100_out, and_101_out, and_102_out, and_103_out, and_104_out, and_105_out,
       and_106_out, and_107_out, and_108_out, and_109_out, and_110_out, and_111_out, and_112_out,
       and_113_out, and_114_out, and_115_out, and_116_out, and_117_out, and_118_out, and_119_out,
       and_120_out, and_121_out, and_122_out, and_123_out, and_124_out, and_125_out, and_126_out,
       and_127_out, and_128_out, and_129_out, and_130_out, and_131_out, and_132_out, and_133_out,
       and_134_out, and_135_out, and_136_out, and_137_out, and_138_out, and_139_out, and_140_out,
       and_141_out, and_142_out, and_143_out, and_144_out, and_145_out, and_146_out, and_147_out,
       and_148_out, and_149_out, and_150_out, and_151_out, and_152_out, and_153_out, and_154_out,
       and_155_out, and_156_out, and_157_out, and_158_out, and_159_out, and_160_out, and_161_out,
       and_162_out, and_163_out, and_164_out, and_165_out, and_166_out, and_167_out, and_168_out,
       and_169_out, and_170_out, and_171_out, and_172_out, and_173_out, and_174_out, and_175_out,
       and_176_out, and_177_out, and_178_out, and_179_out, and_180_out, and_181_out, and_182_out,
       and_183_out, and_184_out, and_185_out, and_186_out, and_187_out, and_188_out, and_189_out,
       and_190_out, and_191_out, and_192_out, and_193_out, and_194_out, and_195_out, and_196_out,
       and_197_out, and_198_out, and_199_out, and_200_out, and_201_out, and_202_out, and_203_out,
       and_204_out, and_205_out, and_206_out, and_207_out, and_208_out, and_209_out, and_210_out,
       and_211_out, and_212_out, and_213_out, and_214_out, and_215_out, and_216_out, and_217_out,
       and_218_out, and_219_out, and_220_out, and_221_out, and_222_out, and_223_out, and_224_out,
       and_225_out, and_226_out, and_227_out, and_228_out, and_229_out, and_230_out, and_231_out,
       and_232_out, and_233_out, and_234_out, and_235_out, and_236_out, and_237_out, and_238_out,
       and_239_out, and_240_out, and_241_out, and_242_out, and_243_out, and_244_out, and_245_out,
       and_246_out, and_247_out, and_248_out, and_249_out, and_250_out, and_251_out, and_252_out,
       and_253_out, and_254_out, and_255_out, and_256_out, and_257_out, and_258_out, and_259_out,
       and_260_out, and_261_out, and_262_out, and_263_out, and_264_out, and_265_out, and_266_out,
       and_267_out, and_268_out, and_269_out, and_270_out, and_271_out, and_272_out, and_273_out,
       and_274_out, and_275_out, and_276_out, and_277_out, and_278_out, and_279_out, and_280_out,
       and_281_out, and_282_out, and_283_out, and_284_out, and_285_out, and_286_out, and_287_out,
       and_288_out, and_289_out, and_290_out, and_291_out, and_292_out, and_293_out, and_294_out,
       and_295_out, and_296_out, and_297_out, and_298_out, and_299_out, and_300_out, and_301_out,
       and_302_out, and_303_out, and_304_out, and_305_out, and_306_out, and_307_out, and_308_out,
       and_309_out, and_310_out, and_311_out, and_312_out, and_313_out, and_314_out, and_315_out,
       and_316_out, and_317_out, and_318_out, and_319_out, and_320_out, and_321_out, and_322_out,
       and_323_out, and_324_out, and_325_out, and_326_out, and_327_out, and_328_out, and_329_out,
       and_330_out, and_331_out, and_332_out, and_333_out, and_334_out, and_335_out, and_336_out,
       and_337_out, and_338_out, and_339_out, and_340_out, and_341_out, and_342_out, and_343_out,
       and_344_out, and_345_out, and_346_out, and_347_out, and_348_out, and_349_out, and_350_out,
       and_351_out, and_352_out, and_353_out, and_354_out, and_355_out, and_356_out, and_357_out,
       and_358_out, and_359_out, and_360_out, and_361_out, and_362_out, and_363_out, and_364_out,
       and_365_out, and_366_out, and_367_out, and_368_out, and_369_out, and_370_out, and_371_out,
       and_372_out, and_373_out, and_374_out, and_375_out, and_376_out, and_377_out, and_378_out,
       and_379_out, and_380_out, not_1_out, not_2_out, not_3_out, not_4_out, not_5_out, not_6_out, not_7_out,
       not_8_out, not_9_out, not_10_out, not_11_out, not_12_out, not_13_out, not_14_out, not_15_out,
       not_16_out, not_17_out, not_18_out, not_19_out, not_20_out, not_21_out, not_22_out, not_23_out,
       not_24_out, not_25_out, not_26_out, not_27_out, not_28_out, not_29_out, not_30_out, not_31_out,
       not_32_out, not_33_out, not_34_out, not_35_out, not_36_out, not_37_out, not_38_out, not_39_out,
       not_40_out, not_41_out, not_42_out, not_43_out, not_44_out, not_45_out, not_46_out, not_47_out,
       not_48_out, not_49_out, not_50_out, not_51_out, not_52_out, not_53_out, not_54_out, not_55_out,
       not_56_out, not_57_out, not_58_out, not_59_out, not_60_out, not_61_out, not_62_out, not_63_out,
       not_64_out, not_65_out, not_66_out, not_67_out, not_68_out, not_69_out, not_70_out, not_71_out,
       not_72_out, not_73_out, not_74_out, not_75_out, not_76_out, not_77_out, not_78_out, not_79_out,
       not_80_out, not_81_out, not_82_out, not_83_out, not_84_out, not_85_out, not_86_out, not_87_out,
       not_88_out, not_89_out, not_90_out, not_91_out, not_92_out, not_93_out, not_94_out, not_95_out,
       not_96_out, not_97_out, not_98_out, not_99_out, not_100_out, not_101_out, not_102_out, not_103_out,
       not_104_out, not_105_out, not_106_out, not_107_out, not_108_out, not_109_out, not_110_out,
       not_111_out, not_112_out, not_113_out, not_114_out, not_115_out, not_116_out, not_117_out,
       not_118_out, not_119_out, not_120_out, not_121_out, not_122_out, not_123_out, not_124_out,
       not_125_out, not_126_out, not_127_out, not_128_out, not_129_out, not_130_out, not_131_out,
       not_132_out, not_133_out, not_134_out, not_135_out, not_136_out, not_137_out, not_138_out,
       not_139_out, not_140_out, not_141_out, not_142_out, not_143_out, not_144_out, not_145_out,
       not_146_out, not_147_out, not_148_out, not_149_out, not_150_out, not_151_out, not_152_out,
       not_153_out, not_154_out, not_155_out, not_156_out, not_157_out, not_158_out, not_159_out,
       not_160_out, not_161_out, not_162_out, not_163_out, not_164_out, not_165_out, not_166_out,
       not_167_out, not_168_out, not_169_out, not_170_out, not_171_out, not_172_out, not_173_out,
       not_174_out, not_175_out, not_176_out, not_177_out, not_178_out, not_179_out, not_180_out,
       not_181_out, not_182_out, not_183_out, not_184_out, not_185_out, not_186_out, not_187_out,
       not_188_out, not_189_out, not_190_out, not_191_out, not_192_out, not_193_out, not_194_out,
       not_195_out, not_196_out, not_197_out, not_198_out, not_199_out, not_200_out, not_201_out,
       not_202_out, not_203_out, not_204_out, not_205_out, not_206_out, not_207_out, not_208_out,
       not_209_out, not_210_out, not_211_out, not_212_out, not_213_out, not_214_out, not_215_out,
       not_216_out, not_217_out, not_218_out, not_219_out, not_220_out, not_221_out, not_222_out,
       not_223_out, not_224_out, not_225_out, not_226_out, not_227_out, not_228_out, not_229_out,
       not_230_out, not_231_out, not_232_out, not_233_out, not_234_out, not_235_out, not_236_out,
       not_237_out, not_238_out, not_239_out, not_240_out, not_241_out, not_242_out, not_243_out,
       not_244_out, not_245_out, not_246_out, not_247_out, not_248_out, not_249_out, not_250_out,
       not_251_out, not_252_out, not_253_out, not_254_out, not_255_out, not_256_out, not_257_out,
       not_258_out, not_259_out, not_260_out, not_261_out, not_262_out, not_263_out, not_264_out,
       not_265_out, not_266_out, not_267_out, not_268_out, not_269_out, not_270_out, not_271_out,
       not_272_out, not_273_out, not_274_out, not_275_out, not_276_out, not_277_out, not_278_out,
       not_279_out, not_280_out, not_281_out, not_282_out, not_283_out, not_284_out, not_285_out,
       not_286_out, not_287_out, not_288_out, not_289_out, not_290_out, not_291_out, not_292_out,
       not_293_out, not_294_out, not_295_out, not_296_out, not_297_out, not_298_out, not_299_out,
       not_300_out, not_301_out, not_302_out, not_303_out, not_304_out, not_305_out, not_306_out,
       not_307_out, not_308_out, not_309_out, not_310_out, not_311_out, not_312_out, not_313_out,
       not_314_out, not_315_out, not_316_out, not_317_out, not_318_out, not_319_out, not_320_out,
       not_321_out, not_322_out, not_323_out, not_324_out, not_325_out, not_326_out, not_327_out,
       not_328_out, not_329_out, not_330_out, not_331_out, not_332_out, not_333_out, not_334_out,
       not_335_out, not_336_out, not_337_out, not_338_out, not_339_out, not_340_out, not_341_out,
       not_342_out, not_343_out, not_344_out, not_345_out, not_346_out, not_347_out, not_348_out,
       not_349_out, not_350_out, not_351_out, not_352_out, not_353_out, not_354_out, not_355_out,
       not_356_out, not_357_out, not_358_out, not_359_out, not_360_out, not_361_out, not_362_out,
       not_363_out, not_364_out, not_365_out, not_366_out, not_367_out, not_368_out, not_369_out,
       not_370_out, not_371_out, not_372_out, not_373_out, not_374_out, not_375_out, not_376_out,
       not_377_out, not_378_out, not_379_out, not_380_out, not_381_out, not_382_out, not_383_out,
       not_384_out, not_385_out, not_386_out, not_387_out, not_388_out, not_389_out, not_390_out,
       not_391_out, not_392_out, not_393_out, not_394_out, not_395_out, not_396_out, not_397_out,
       not_398_out, not_399_out, not_400_out, not_401_out, not_402_out, not_403_out, not_404_out,
       not_405_out, not_406_out, not_407_out, not_408_out, not_409_out, not_410_out, not_411_out,
       not_412_out, not_413_out, not_414_out, not_415_out, not_416_out, not_417_out, not_418_out,
       not_419_out, not_420_out, not_421_out, not_422_out, not_423_out, not_424_out, not_425_out,
       not_426_out, not_427_out, not_428_out, not_429_out, not_430_out, not_431_out, not_432_out,
       not_433_out, not_434_out, not_435_out, not_436_out, not_437_out, not_438_out, not_439_out,
       not_440_out, not_441_out, not_442_out, not_443_out, not_444_out, not_445_out, not_446_out,
       not_447_out, not_448_out, not_449_out, not_450_out, not_451_out, not_452_out, not_453_out,
       not_454_out, not_455_out, not_456_out, not_457_out, not_458_out, not_459_out, not_460_out,
       not_461_out, not_462_out, not_463_out, not_464_out, not_465_out, not_466_out, not_467_out,
       not_468_out, not_469_out, not_470_out, not_471_out, not_472_out, not_473_out, not_474_out,
       not_475_out, not_476_out, not_477_out, not_478_out, not_479_out, not_480_out, not_481_out,
       not_482_out, not_483_out, not_484_out, not_485_out, not_486_out, not_487_out, not_488_out,
       not_489_out, not_490_out, not_491_out, not_492_out, not_493_out, not_494_out, not_495_out,
       not_496_out, not_497_out, not_498_out, not_499_out, not_500_out, not_501_out, not_502_out,
       not_503_out, not_504_out, not_505_out, not_506_out, not_507_out, not_508_out, not_509_out,
       not_510_out, not_511_out, not_512_out, not_513_out, not_514_out, not_515_out, not_516_out,
       not_517_out, not_518_out, not_519_out, not_520_out, not_521_out, not_522_out, not_523_out,
       not_524_out, not_525_out, not_526_out, not_527_out, not_528_out, not_529_out, not_530_out,
       not_531_out, not_532_out, not_533_out, not_534_out, not_535_out, not_536_out, not_537_out,
       not_538_out, not_539_out, not_540_out, not_541_out, not_542_out, not_543_out, not_544_out,
       not_545_out, not_546_out, not_547_out, not_548_out, not_549_out, not_550_out, not_551_out,
       not_552_out, not_553_out, not_554_out, not_555_out, not_556_out, not_557_out, not_558_out,
       not_559_out, not_560_out, not_561_out, not_562_out, not_563_out, not_564_out, not_565_out,
       not_566_out, not_567_out, not_568_out, not_569_out, not_570_out, not_571_out, not_572_out,
       not_573_out, not_574_out, not_575_out, not_576_out, not_577_out, not_578_out, not_579_out,
       not_580_out, not_581_out, not_582_out, not_583_out, not_584_out, not_585_out, not_586_out,
       not_587_out, not_588_out, not_589_out, not_590_out, not_591_out, not_592_out, not_593_out,
       not_594_out, not_595_out, not_596_out, not_597_out, not_598_out, not_599_out, not_600_out,
       not_601_out, not_602_out, not_603_out, not_604_out, not_605_out, not_606_out, not_607_out,
       not_608_out, not_609_out, not_610_out, not_611_out, not_612_out, not_613_out, not_614_out,
       not_615_out, not_616_out, not_617_out, not_618_out, not_619_out, not_620_out, not_621_out,
       not_622_out, not_623_out, not_624_out, not_625_out, not_626_out, not_627_out, not_628_out,
       not_629_out, not_630_out, not_631_out, not_632_out, not_633_out, not_634_out, not_635_out,
       not_636_out, not_637_out, not_638_out, not_639_out, not_640_out, not_641_out, not_642_out,
       not_643_out, not_644_out, not_645_out, not_646_out, not_647_out, not_648_out, not_649_out,
       not_650_out, not_651_out, not_652_out, not_653_out, not_654_out, not_655_out, not_656_out,
       not_657_out, not_658_out, not_659_out, not_660_out, not_661_out, not_662_out, not_663_out,
       not_664_out, not_665_out, not_666_out, not_667_out, not_668_out, not_669_out, not_670_out,
       not_671_out, not_672_out, not_673_out, not_674_out, not_675_out, not_676_out, not_677_out,
       not_678_out, not_679_out, not_680_out, not_681_out, not_682_out, not_683_out, not_684_out,
       not_685_out, not_686_out, not_687_out, not_688_out, not_689_out, not_690_out, not_691_out,
       not_692_out, not_693_out, not_694_out, not_695_out, not_696_out, not_697_out, not_698_out,
       not_699_out, not_700_out, not_701_out, not_702_out, not_703_out, not_704_out, not_705_out,
       not_706_out, not_707_out, not_708_out, not_709_out, not_710_out, not_711_out, not_712_out,
       not_713_out, not_714_out, not_715_out, not_716_out, not_717_out, not_718_out, not_719_out,
       not_720_out, not_721_out, not_722_out, not_723_out, not_724_out, not_725_out, not_726_out,
       not_727_out, not_728_out, not_729_out, not_730_out, not_731_out, not_732_out, not_733_out,
       not_734_out, not_735_out, not_736_out, not_737_out, not_738_out, not_739_out, not_740_out,
       not_741_out, not_742_out, not_743_out, not_744_out, not_745_out, not_746_out, not_747_out,
       not_748_out, not_749_out, not_750_out, not_751_out, not_752_out, not_753_out, not_754_out,
       not_755_out, not_756_out, not_757_out, not_758_out, not_759_out, not_760_out, not_761_out,
       not_762_out, not_763_out, not_764_out, not_765_out, not_766_out, not_767_out, not_768_out,
       not_769_out, not_770_out, not_771_out, not_772_out, not_773_out, not_774_out, not_775_out,
       not_776_out, not_777_out, not_778_out, not_779_out, not_780_out, not_781_out, not_782_out,
       not_783_out, not_784_out, not_785_out, not_786_out, not_787_out, not_788_out, not_789_out,
       not_790_out, not_791_out, not_792_out, not_793_out, not_794_out, not_795_out, not_796_out,
       not_797_out, not_798_out, not_799_out, not_800_out, not_801_out, not_802_out, not_803_out,
       not_804_out, not_805_out, not_806_out, not_807_out, not_808_out, not_809_out, not_810_out,
       not_811_out, not_812_out, not_813_out, not_814_out, not_815_out, not_816_out, not_817_out,
       not_818_out, not_819_out, not_820_out, not_821_out, not_822_out, not_823_out, not_824_out,
       not_825_out, not_826_out, not_827_out, not_828_out, not_829_out, not_830_out, not_831_out,
       not_832_out, not_833_out, not_834_out, not_835_out, not_836_out, not_837_out, not_838_out,
       not_839_out, not_840_out, not_841_out, not_842_out, not_843_out, not_844_out, not_845_out,
       not_846_out, not_847_out, not_848_out, not_849_out, not_850_out, not_851_out, not_852_out,
       not_853_out, not_854_out, not_855_out, not_856_out, not_857_out, not_858_out, not_859_out,
       not_860_out, not_861_out, not_862_out, not_863_out, not_864_out, not_865_out, not_866_out,
       not_867_out, not_868_out, not_869_out, not_870_out, not_871_out, not_872_out, not_873_out,
       not_874_out, not_875_out, not_876_out, not_877_out, not_878_out, not_879_out, not_880_out,
       not_881_out, not_882_out, not_883_out, not_884_out, not_885_out, not_886_out, not_887_out,
       not_888_out, not_889_out, not_890_out, not_891_out, not_892_out, not_893_out, not_894_out,
       not_895_out, not_896_out, not_897_out, not_898_out, not_899_out, not_900_out, not_901_out,
       not_902_out, not_903_out, not_904_out, not_905_out, not_906_out, not_907_out, not_908_out,
       not_909_out, not_910_out, not_911_out, not_912_out, not_913_out, not_914_out, not_915_out,
       not_916_out, not_917_out, not_918_out, not_919_out, not_920_out, not_921_out, not_922_out,
       not_923_out, not_924_out, not_925_out, not_926_out, not_927_out, not_928_out, not_929_out,
       not_930_out, not_931_out, not_932_out, not_933_out, not_934_out, not_935_out, not_936_out,
       not_937_out, not_938_out, not_939_out, not_940_out, not_941_out, not_942_out, not_943_out,
       not_944_out, not_945_out, not_946_out, not_947_out, not_948_out, not_949_out, not_950_out,
       not_951_out, not_952_out, not_953_out, not_954_out, not_955_out, not_956_out, not_957_out,
       not_958_out, not_959_out, not_960_out, not_961_out, not_962_out, not_963_out, not_964_out,
       not_965_out, not_966_out, not_967_out, not_968_out, not_969_out, not_970_out, not_971_out,
       not_972_out, not_973_out, not_974_out, not_975_out, not_976_out, not_977_out, not_978_out,
       not_979_out, not_980_out, not_981_out, not_982_out, not_983_out, not_984_out, not_985_out,
       not_986_out, not_987_out, not_988_out, not_989_out, not_990_out, not_991_out, not_992_out,
       not_993_out, not_994_out, not_995_out, not_996_out, not_997_out, not_998_out, not_999_out,
       not_1000_out, not_1001_out, not_1002_out, not_1003_out, not_1004_out, not_1005_out, not_1006_out,
       not_1007_out, not_1008_out, not_1009_out, not_1010_out, not_1011_out, not_1012_out, not_1013_out,
       not_1014_out, not_1015_out, not_1016_out, not_1017_out, not_1018_out, not_1019_out, not_1020_out,
       not_1021_out, not_1022_out, not_1023_out, not_1024_out, not_1025_out, not_1026_out, not_1027_out,
       not_1028_out, not_1029_out, not_1030_out, not_1031_out, not_1032_out, not_1033_out, not_1034_out,
       not_1035_out, not_1036_out, not_1037_out, not_1038_out, not_1039_out, not_1040_out, not_1041_out,
       not_1042_out, not_1043_out, not_1044_out, not_1045_out, not_1046_out, not_1047_out, not_1048_out,
       not_1049_out, not_1050_out, not_1051_out, not_1052_out, not_1053_out, not_1054_out, not_1055_out,
       not_1056_out, not_1057_out, not_1058_out, not_1059_out, not_1060_out, not_1061_out, not_1062_out,
       not_1063_out, not_1064_out, not_1065_out, not_1066_out, not_1067_out, not_1068_out, not_1069_out,
       not_1070_out, not_1071_out, not_1072_out, not_1073_out, not_1074_out, not_1075_out, not_1076_out,
       not_1077_out, not_1078_out, not_1079_out, not_1080_out, not_1081_out, not_1082_out, not_1083_out,
       not_1084_out, not_1085_out, not_1086_out, not_1087_out, not_1088_out, not_1089_out, not_1090_out,
       not_1091_out, not_1092_out, not_1093_out, not_1094_out, not_1095_out, not_1096_out, not_1097_out,
       not_1098_out, not_1099_out, not_1100_out, not_1101_out, not_1102_out, not_1103_out, not_1104_out,
       not_1105_out, not_1106_out, not_1107_out, not_1108_out, not_1109_out, not_1110_out, not_1111_out,
       not_1112_out, not_1113_out, not_1114_out, not_1115_out, not_1116_out, not_1117_out, not_1118_out,
       not_1119_out, or_1_out, or_2_out, or_3_out, or_4_out, or_5_out, or_6_out, or_7_out, or_9_out,
       or_10_out, or_11_out, or_13_out, or_14_out, or_15_out, or_16_out;

  not not_1 (not_1_out, i7);
  not not_2 (not_2_out, i6);
  not not_3 (not_3_out, i5);
  not not_4 (not_4_out, i3);
  not not_5 (not_5_out, i1);
  not not_6 (not_6_out, i7);
  not not_7 (not_7_out, i5);
  not not_8 (not_8_out, i3);
  not not_9 (not_9_out, i2);
  not not_10 (not_10_out, i1);
  not not_11 (not_11_out, i8);
  not not_12 (not_12_out, i7);
  not not_13 (not_13_out, i6);
  not not_14 (not_14_out, i4);
  not not_15 (not_15_out, i8);
  not not_16 (not_16_out, i6);
  not not_17 (not_17_out, i4);
  not not_18 (not_18_out, i1);
  not not_19 (not_19_out, i8);
  not not_20 (not_20_out, i7);
  not not_21 (not_21_out, i5);
  not not_22 (not_22_out, i7);
  not not_23 (not_23_out, i5);
  not not_24 (not_24_out, i8);
  not not_25 (not_25_out, i6);
  not not_26 (not_26_out, i5);
  not not_27 (not_27_out, i2);
  not not_28 (not_28_out, i8);
  not not_29 (not_29_out, i6);
  not not_30 (not_30_out, i2);
  not not_31 (not_31_out, i8);
  not not_32 (not_32_out, i7);
  not not_33 (not_33_out, i4);
  not not_34 (not_34_out, i3);
  not not_35 (not_35_out, i1);
  not not_36 (not_36_out, i7);
  not not_37 (not_37_out, i6);
  not not_38 (not_38_out, i3);
  not not_39 (not_39_out, i8);
  not not_40 (not_40_out, i6);
  not not_41 (not_41_out, i4);
  not not_42 (not_42_out, i7);
  not not_43 (not_43_out, i6);
  not not_44 (not_44_out, i4);
  not not_45 (not_45_out, i3);
  not not_46 (not_46_out, i7);
  not not_47 (not_47_out, i6);
  not not_48 (not_48_out, i1);
  not not_49 (not_49_out, i7);
  not not_50 (not_50_out, i2);
  not not_51 (not_51_out, i1);
  not not_52 (not_52_out, i8);
  not not_53 (not_53_out, i3);
  not not_54 (not_54_out, i1);
  not not_55 (not_55_out, i8);
  not not_56 (not_56_out, i7);
  not not_57 (not_57_out, i4);
  not not_58 (not_58_out, i2);
  not not_59 (not_59_out, i8);
  not not_60 (not_60_out, i4);
  not not_61 (not_61_out, i2);
  not not_62 (not_62_out, i1);
  not not_63 (not_63_out, i8);
  not not_64 (not_64_out, i5);
  not not_65 (not_65_out, i4);
  not not_66 (not_66_out, i8);
  not not_67 (not_67_out, i7);
  not not_68 (not_68_out, i5);
  not not_69 (not_69_out, i4);
  not not_70 (not_70_out, i7);
  not not_71 (not_71_out, i5);
  not not_72 (not_72_out, i8);
  not not_73 (not_73_out, i3);
  not not_74 (not_74_out, i8);
  not not_75 (not_75_out, i1);
  not not_76 (not_76_out, i8);
  not not_77 (not_77_out, i4);
  not not_78 (not_78_out, i2);
  not not_79 (not_79_out, i7);
  not not_80 (not_80_out, i4);
  not not_81 (not_81_out, i3);
  not not_82 (not_82_out, i1);
  not not_83 (not_83_out, i7);
  not not_84 (not_84_out, i3);
  not not_85 (not_85_out, i1);
  not not_86 (not_86_out, i8);
  not not_87 (not_87_out, i4);
  not not_88 (not_88_out, i8);
  not not_89 (not_89_out, i7);
  not not_90 (not_90_out, i3);
  not not_91 (not_91_out, i8);
  not not_92 (not_92_out, i8);
  not not_93 (not_93_out, i5);
  not not_94 (not_94_out, i3);
  not not_95 (not_95_out, i5);
  not not_96 (not_96_out, i3);
  not not_97 (not_97_out, i8);
  not not_98 (not_98_out, i5);
  not not_99 (not_99_out, i1);
  not not_100 (not_100_out, i6);
  not not_101 (not_101_out, i5);
  not not_102 (not_102_out, i2);
  not not_103 (not_103_out, i5);
  not not_104 (not_104_out, i1);
  not not_105 (not_105_out, i8);
  not not_106 (not_106_out, i6);
  not not_107 (not_107_out, i2);
  not not_108 (not_108_out, i8);
  not not_109 (not_109_out, i6);
  not not_110 (not_110_out, i5);
  not not_111 (not_111_out, i8);
  not not_112 (not_112_out, i5);
  not not_113 (not_113_out, i2);
  not not_114 (not_114_out, i3);
  not not_115 (not_115_out, i2);
  not not_116 (not_116_out, i1);
  not not_117 (not_117_out, i4);
  not not_118 (not_118_out, i8);
  not not_119 (not_119_out, i5);
  not not_120 (not_120_out, i4);
  not not_121 (not_121_out, i1);
  not not_122 (not_122_out, i5);
  not not_123 (not_123_out, i3);
  not not_124 (not_124_out, i5);
  not not_125 (not_125_out, i1);
  not not_126 (not_126_out, i8);
  not not_127 (not_127_out, i4);
  not not_128 (not_128_out, i8);
  not not_129 (not_129_out, i4);
  not not_130 (not_130_out, i7);
  not not_131 (not_131_out, i6);
  not not_132 (not_132_out, i5);
  not not_133 (not_133_out, i3);
  not not_134 (not_134_out, i2);
  not not_135 (not_135_out, i7);
  not not_136 (not_136_out, i6);
  not not_137 (not_137_out, i5);
  not not_138 (not_138_out, i2);
  not not_139 (not_139_out, i1);
  not not_140 (not_140_out, i7);
  not not_141 (not_141_out, i5);
  not not_142 (not_142_out, i3);
  not not_143 (not_143_out, i1);
  not not_144 (not_144_out, i6);
  not not_145 (not_145_out, i5);
  not not_146 (not_146_out, i4);
  not not_147 (not_147_out, i2);
  not not_148 (not_148_out, i6);
  not not_149 (not_149_out, i5);
  not not_150 (not_150_out, i3);
  not not_151 (not_151_out, i2);
  not not_152 (not_152_out, i1);
  not not_153 (not_153_out, i6);
  not not_154 (not_154_out, i5);
  not not_155 (not_155_out, i6);
  not not_156 (not_156_out, i7);
  not not_157 (not_157_out, i3);
  not not_158 (not_158_out, i7);
  not not_159 (not_159_out, i6);
  not not_160 (not_160_out, i2);
  not not_161 (not_161_out, i7);
  not not_162 (not_162_out, i1);
  not not_163 (not_163_out, i6);
  not not_164 (not_164_out, i2);
  not not_165 (not_165_out, i1);
  not not_166 (not_166_out, i4);
  not not_167 (not_167_out, i3);
  not not_168 (not_168_out, i4);
  not not_169 (not_169_out, i1);
  not not_170 (not_170_out, i5);
  not not_171 (not_171_out, i2);
  not not_172 (not_172_out, i2);
  not not_173 (not_173_out, i4);
  not not_174 (not_174_out, i6);
  not not_175 (not_175_out, i4);
  not not_176 (not_176_out, i2);
  not not_177 (not_177_out, i6);
  not not_178 (not_178_out, i5);
  not not_179 (not_179_out, i6);
  not not_180 (not_180_out, i6);
  not not_181 (not_181_out, i3);
  not not_182 (not_182_out, i2);
  not not_183 (not_183_out, i3);
  not not_184 (not_184_out, i1);
  not not_185 (not_185_out, i5);
  not not_186 (not_186_out, i2);
  not not_187 (not_187_out, i2);
  not not_188 (not_188_out, i5);
  not not_189 (not_189_out, i8);
  not not_190 (not_190_out, i7);
  not not_191 (not_191_out, i5);
  not not_192 (not_192_out, i3);
  not not_193 (not_193_out, i2);
  not not_194 (not_194_out, i7);
  not not_195 (not_195_out, i5);
  not not_196 (not_196_out, i4);
  not not_197 (not_197_out, i3);
  not not_198 (not_198_out, i1);
  not not_199 (not_199_out, i7);
  not not_200 (not_200_out, i6);
  not not_201 (not_201_out, i5);
  not not_202 (not_202_out, i3);
  not not_203 (not_203_out, i8);
  not not_204 (not_204_out, i6);
  not not_205 (not_205_out, i4);
  not not_206 (not_206_out, i7);
  not not_207 (not_207_out, i6);
  not not_208 (not_208_out, i5);
  not not_209 (not_209_out, i2);
  not not_210 (not_210_out, i1);
  not not_211 (not_211_out, i8);
  not not_212 (not_212_out, i6);
  not not_213 (not_213_out, i5);
  not not_214 (not_214_out, i2);
  not not_215 (not_215_out, i8);
  not not_216 (not_216_out, i6);
  not not_217 (not_217_out, i5);
  not not_218 (not_218_out, i1);
  not not_219 (not_219_out, i8);
  not not_220 (not_220_out, i7);
  not not_221 (not_221_out, i4);
  not not_222 (not_222_out, i3);
  not not_223 (not_223_out, i8);
  not not_224 (not_224_out, i7);
  not not_225 (not_225_out, i4);
  not not_226 (not_226_out, i3);
  not not_227 (not_227_out, i7);
  not not_228 (not_228_out, i4);
  not not_229 (not_229_out, i3);
  not not_230 (not_230_out, i8);
  not not_231 (not_231_out, i7);
  not not_232 (not_232_out, i6);
  not not_233 (not_233_out, i7);
  not not_234 (not_234_out, i6);
  not not_235 (not_235_out, i3);
  not not_236 (not_236_out, i2);
  not not_237 (not_237_out, i1);
  not not_238 (not_238_out, i8);
  not not_239 (not_239_out, i3);
  not not_240 (not_240_out, i8);
  not not_241 (not_241_out, i7);
  not not_242 (not_242_out, i8);
  not not_243 (not_243_out, i4);
  not not_244 (not_244_out, i2);
  not not_245 (not_245_out, i8);
  not not_246 (not_246_out, i4);
  not not_247 (not_247_out, i1);
  not not_248 (not_248_out, i8);
  not not_249 (not_249_out, i5);
  not not_250 (not_250_out, i4);
  not not_251 (not_251_out, i8);
  not not_252 (not_252_out, i5);
  not not_253 (not_253_out, i2);
  not not_254 (not_254_out, i1);
  not not_255 (not_255_out, i8);
  not not_256 (not_256_out, i7);
  not not_257 (not_257_out, i3);
  not not_258 (not_258_out, i8);
  not not_259 (not_259_out, i8);
  not not_260 (not_260_out, i7);
  not not_261 (not_261_out, i4);
  not not_262 (not_262_out, i3);
  not not_263 (not_263_out, i7);
  not not_264 (not_264_out, i4);
  not not_265 (not_265_out, i3);
  not not_266 (not_266_out, i7);
  not not_267 (not_267_out, i4);
  not not_268 (not_268_out, i3);
  not not_269 (not_269_out, i7);
  not not_270 (not_270_out, i3);
  not not_271 (not_271_out, i7);
  not not_272 (not_272_out, i1);
  not not_273 (not_273_out, i8);
  not not_274 (not_274_out, i3);
  not not_275 (not_275_out, i6);
  not not_276 (not_276_out, i5);
  not not_277 (not_277_out, i3);
  not not_278 (not_278_out, i2);
  not not_279 (not_279_out, i1);
  not not_280 (not_280_out, i8);
  not not_281 (not_281_out, i5);
  not not_282 (not_282_out, i4);
  not not_283 (not_283_out, i5);
  not not_284 (not_284_out, i4);
  not not_285 (not_285_out, i5);
  not not_286 (not_286_out, i8);
  not not_287 (not_287_out, i6);
  not not_288 (not_288_out, i3);
  not not_289 (not_289_out, i6);
  not not_290 (not_290_out, i2);
  not not_291 (not_291_out, i1);
  not not_292 (not_292_out, i8);
  not not_293 (not_293_out, i6);
  not not_294 (not_294_out, i2);
  not not_295 (not_295_out, i8);
  not not_296 (not_296_out, i6);
  not not_297 (not_297_out, i1);
  not not_298 (not_298_out, i2);
  not not_299 (not_299_out, i1);
  not not_300 (not_300_out, i8);
  not not_301 (not_301_out, i5);
  not not_302 (not_302_out, i4);
  not not_303 (not_303_out, i8);
  not not_304 (not_304_out, i4);
  not not_305 (not_305_out, i5);
  not not_306 (not_306_out, i5);
  not not_307 (not_307_out, i3);
  not not_308 (not_308_out, i1);
  not not_309 (not_309_out, i7);
  not not_310 (not_310_out, i6);
  not not_311 (not_311_out, i5);
  not not_312 (not_312_out, i2);
  not not_313 (not_313_out, i6);
  not not_314 (not_314_out, i5);
  not not_315 (not_315_out, i4);
  not not_316 (not_316_out, i1);
  not not_317 (not_317_out, i7);
  not not_318 (not_318_out, i6);
  not not_319 (not_319_out, i1);
  not not_320 (not_320_out, i6);
  not not_321 (not_321_out, i5);
  not not_322 (not_322_out, i7);
  not not_323 (not_323_out, i5);
  not not_324 (not_324_out, i1);
  not not_325 (not_325_out, i6);
  not not_326 (not_326_out, i4);
  not not_327 (not_327_out, i2);
  not not_328 (not_328_out, i1);
  not not_329 (not_329_out, i7);
  not not_330 (not_330_out, i6);
  not not_331 (not_331_out, i2);
  not not_332 (not_332_out, i6);
  not not_333 (not_333_out, i1);
  not not_334 (not_334_out, i7);
  not not_335 (not_335_out, i5);
  not not_336 (not_336_out, i3);
  not not_337 (not_337_out, i5);
  not not_338 (not_338_out, i4);
  not not_339 (not_339_out, i2);
  not not_340 (not_340_out, i1);
  not not_341 (not_341_out, i4);
  not not_342 (not_342_out, i5);
  not not_343 (not_343_out, i2);
  not not_344 (not_344_out, i2);
  not not_345 (not_345_out, i1);
  not not_346 (not_346_out, i6);
  not not_347 (not_347_out, i5);
  not not_348 (not_348_out, i3);
  not not_349 (not_349_out, i2);
  not not_350 (not_350_out, i6);
  not not_351 (not_351_out, i5);
  not not_352 (not_352_out, i2);
  not not_353 (not_353_out, i1);
  not not_354 (not_354_out, i5);
  not not_355 (not_355_out, i3);
  not not_356 (not_356_out, i1);
  not not_357 (not_357_out, i3);
  not not_358 (not_358_out, i6);
  not not_359 (not_359_out, i1);
  not not_360 (not_360_out, i6);
  not not_361 (not_361_out, i2);
  not not_362 (not_362_out, i6);
  not not_363 (not_363_out, i2);
  not not_364 (not_364_out, i1);
  not not_365 (not_365_out, i2);
  not not_366 (not_366_out, i1);
  not not_367 (not_367_out, i8);
  not not_368 (not_368_out, i6);
  not not_369 (not_369_out, i4);
  not not_370 (not_370_out, i2);
  not not_371 (not_371_out, i7);
  not not_372 (not_372_out, i6);
  not not_373 (not_373_out, i5);
  not not_374 (not_374_out, i3);
  not not_375 (not_375_out, i2);
  not not_376 (not_376_out, i8);
  not not_377 (not_377_out, i7);
  not not_378 (not_378_out, i5);
  not not_379 (not_379_out, i4);
  not not_380 (not_380_out, i8);
  not not_381 (not_381_out, i6);
  not not_382 (not_382_out, i8);
  not not_383 (not_383_out, i7);
  not not_384 (not_384_out, i3);
  not not_385 (not_385_out, i7);
  not not_386 (not_386_out, i4);
  not not_387 (not_387_out, i3);
  not not_388 (not_388_out, i7);
  not not_389 (not_389_out, i3);
  not not_390 (not_390_out, i7);
  not not_391 (not_391_out, i6);
  not not_392 (not_392_out, i2);
  not not_393 (not_393_out, i8);
  not not_394 (not_394_out, i7);
  not not_395 (not_395_out, i4);
  not not_396 (not_396_out, i7);
  not not_397 (not_397_out, i5);
  not not_398 (not_398_out, i8);
  not not_399 (not_399_out, i2);
  not not_400 (not_400_out, i7);
  not not_401 (not_401_out, i3);
  not not_402 (not_402_out, i8);
  not not_403 (not_403_out, i4);
  not not_404 (not_404_out, i8);
  not not_405 (not_405_out, i5);
  not not_406 (not_406_out, i4);
  not not_407 (not_407_out, i3);
  not not_408 (not_408_out, i6);
  not not_409 (not_409_out, i5);
  not not_410 (not_410_out, i5);
  not not_411 (not_411_out, i2);
  not not_412 (not_412_out, i6);
  not not_413 (not_413_out, i3);
  not not_414 (not_414_out, i2);
  not not_415 (not_415_out, i8);
  not not_416 (not_416_out, i4);
  not not_417 (not_417_out, i8);
  not not_418 (not_418_out, i5);
  not not_419 (not_419_out, i6);
  not not_420 (not_420_out, i4);
  not not_421 (not_421_out, i7);
  not not_422 (not_422_out, i5);
  not not_423 (not_423_out, i3);
  not not_424 (not_424_out, i6);
  not not_425 (not_425_out, i5);
  not not_426 (not_426_out, i2);
  not not_427 (not_427_out, i7);
  not not_428 (not_428_out, i4);
  not not_429 (not_429_out, i2);
  not not_430 (not_430_out, i5);
  not not_431 (not_431_out, i6);
  not not_432 (not_432_out, i2);
  not not_433 (not_433_out, i3);
  not not_434 (not_434_out, i5);
  not not_435 (not_435_out, i7);
  not not_436 (not_436_out, i6);
  not not_437 (not_437_out, i5);
  not not_438 (not_438_out, i3);
  not not_439 (not_439_out, i1);
  not not_440 (not_440_out, i8);
  not not_441 (not_441_out, i7);
  not not_442 (not_442_out, i6);
  not not_443 (not_443_out, i5);
  not not_444 (not_444_out, i4);
  not not_445 (not_445_out, i3);
  not not_446 (not_446_out, i8);
  not not_447 (not_447_out, i6);
  not not_448 (not_448_out, i4);
  not not_449 (not_449_out, i1);
  not not_450 (not_450_out, i7);
  not not_451 (not_451_out, i6);
  not not_452 (not_452_out, i4);
  not not_453 (not_453_out, i3);
  not not_454 (not_454_out, i1);
  not not_455 (not_455_out, i7);
  not not_456 (not_456_out, i6);
  not not_457 (not_457_out, i5);
  not not_458 (not_458_out, i4);
  not not_459 (not_459_out, i2);
  not not_460 (not_460_out, i8);
  not not_461 (not_461_out, i6);
  not not_462 (not_462_out, i5);
  not not_463 (not_463_out, i2);
  not not_464 (not_464_out, i1);
  not not_465 (not_465_out, i8);
  not not_466 (not_466_out, i7);
  not not_467 (not_467_out, i6);
  not not_468 (not_468_out, i5);
  not not_469 (not_469_out, i8);
  not not_470 (not_470_out, i7);
  not not_471 (not_471_out, i5);
  not not_472 (not_472_out, i2);
  not not_473 (not_473_out, i8);
  not not_474 (not_474_out, i7);
  not not_475 (not_475_out, i4);
  not not_476 (not_476_out, i3);
  not not_477 (not_477_out, i1);
  not not_478 (not_478_out, i7);
  not not_479 (not_479_out, i6);
  not not_480 (not_480_out, i1);
  not not_481 (not_481_out, i7);
  not not_482 (not_482_out, i2);
  not not_483 (not_483_out, i1);
  not not_484 (not_484_out, i8);
  not not_485 (not_485_out, i7);
  not not_486 (not_486_out, i6);
  not not_487 (not_487_out, i4);
  not not_488 (not_488_out, i7);
  not not_489 (not_489_out, i6);
  not not_490 (not_490_out, i3);
  not not_491 (not_491_out, i2);
  not not_492 (not_492_out, i8);
  not not_493 (not_493_out, i3);
  not not_494 (not_494_out, i1);
  not not_495 (not_495_out, i8);
  not not_496 (not_496_out, i4);
  not not_497 (not_497_out, i2);
  not not_498 (not_498_out, i1);
  not not_499 (not_499_out, i8);
  not not_500 (not_500_out, i7);
  not not_501 (not_501_out, i5);
  not not_502 (not_502_out, i4);
  not not_503 (not_503_out, i3);
  not not_504 (not_504_out, i8);
  not not_505 (not_505_out, i5);
  not not_506 (not_506_out, i4);
  not not_507 (not_507_out, i1);
  not not_508 (not_508_out, i8);
  not not_509 (not_509_out, i7);
  not not_510 (not_510_out, i3);
  not not_511 (not_511_out, i1);
  not not_512 (not_512_out, i8);
  not not_513 (not_513_out, i7);
  not not_514 (not_514_out, i5);
  not not_515 (not_515_out, i3);
  not not_516 (not_516_out, i8);
  not not_517 (not_517_out, i1);
  not not_518 (not_518_out, i7);
  not not_519 (not_519_out, i4);
  not not_520 (not_520_out, i3);
  not not_521 (not_521_out, i1);
  not not_522 (not_522_out, i7);
  not not_523 (not_523_out, i3);
  not not_524 (not_524_out, i1);
  not not_525 (not_525_out, i8);
  not not_526 (not_526_out, i7);
  not not_527 (not_527_out, i4);
  not not_528 (not_528_out, i7);
  not not_529 (not_529_out, i4);
  not not_530 (not_530_out, i8);
  not not_531 (not_531_out, i7);
  not not_532 (not_532_out, i6);
  not not_533 (not_533_out, i5);
  not not_534 (not_534_out, i4);
  not not_535 (not_535_out, i3);
  not not_536 (not_536_out, i2);
  not not_537 (not_537_out, i8);
  not not_538 (not_538_out, i5);
  not not_539 (not_539_out, i1);
  not not_540 (not_540_out, i5);
  not not_541 (not_541_out, i1);
  not not_542 (not_542_out, i8);
  not not_543 (not_543_out, i6);
  not not_544 (not_544_out, i5);
  not not_545 (not_545_out, i3);
  not not_546 (not_546_out, i8);
  not not_547 (not_547_out, i5);
  not not_548 (not_548_out, i3);
  not not_549 (not_549_out, i2);
  not not_550 (not_550_out, i3);
  not not_551 (not_551_out, i2);
  not not_552 (not_552_out, i1);
  not not_553 (not_553_out, i8);
  not not_554 (not_554_out, i6);
  not not_555 (not_555_out, i4);
  not not_556 (not_556_out, i3);
  not not_557 (not_557_out, i6);
  not not_558 (not_558_out, i4);
  not not_559 (not_559_out, i2);
  not not_560 (not_560_out, i8);
  not not_561 (not_561_out, i6);
  not not_562 (not_562_out, i2);
  not not_563 (not_563_out, i8);
  not not_564 (not_564_out, i6);
  not not_565 (not_565_out, i8);
  not not_566 (not_566_out, i2);
  not not_567 (not_567_out, i8);
  not not_568 (not_568_out, i5);
  not not_569 (not_569_out, i4);
  not not_570 (not_570_out, i1);
  not not_571 (not_571_out, i8);
  not not_572 (not_572_out, i4);
  not not_573 (not_573_out, i1);
  not not_574 (not_574_out, i5);
  not not_575 (not_575_out, i1);
  not not_576 (not_576_out, i8);
  not not_577 (not_577_out, i5);
  not not_578 (not_578_out, i4);
  not not_579 (not_579_out, i8);
  not not_580 (not_580_out, i4);
  not not_581 (not_581_out, i3);
  not not_582 (not_582_out, i4);
  not not_583 (not_583_out, i3);
  not not_584 (not_584_out, i8);
  not not_585 (not_585_out, i3);
  not not_586 (not_586_out, i7);
  not not_587 (not_587_out, i5);
  not not_588 (not_588_out, i3);
  not not_589 (not_589_out, i1);
  not not_590 (not_590_out, i6);
  not not_591 (not_591_out, i5);
  not not_592 (not_592_out, i4);
  not not_593 (not_593_out, i2);
  not not_594 (not_594_out, i1);
  not not_595 (not_595_out, i6);
  not not_596 (not_596_out, i5);
  not not_597 (not_597_out, i3);
  not not_598 (not_598_out, i2);
  not not_599 (not_599_out, i1);
  not not_600 (not_600_out, i7);
  not not_601 (not_601_out, i6);
  not not_602 (not_602_out, i5);
  not not_603 (not_603_out, i7);
  not not_604 (not_604_out, i6);
  not not_605 (not_605_out, i2);
  not not_606 (not_606_out, i1);
  not not_607 (not_607_out, i6);
  not not_608 (not_608_out, i5);
  not not_609 (not_609_out, i1);
  not not_610 (not_610_out, i7);
  not not_611 (not_611_out, i6);
  not not_612 (not_612_out, i3);
  not not_613 (not_613_out, i2);
  not not_614 (not_614_out, i7);
  not not_615 (not_615_out, i1);
  not not_616 (not_616_out, i7);
  not not_617 (not_617_out, i6);
  not not_618 (not_618_out, i3);
  not not_619 (not_619_out, i7);
  not not_620 (not_620_out, i3);
  not not_621 (not_621_out, i2);
  not not_622 (not_622_out, i7);
  not not_623 (not_623_out, i5);
  not not_624 (not_624_out, i4);
  not not_625 (not_625_out, i3);
  not not_626 (not_626_out, i4);
  not not_627 (not_627_out, i1);
  not not_628 (not_628_out, i7);
  not not_629 (not_629_out, i5);
  not not_630 (not_630_out, i2);
  not not_631 (not_631_out, i5);
  not not_632 (not_632_out, i2);
  not not_633 (not_633_out, i1);
  not not_634 (not_634_out, i7);
  not not_635 (not_635_out, i5);
  not not_636 (not_636_out, i6);
  not not_637 (not_637_out, i5);
  not not_638 (not_638_out, i3);
  not not_639 (not_639_out, i6);
  not not_640 (not_640_out, i1);
  not not_641 (not_641_out, i6);
  not not_642 (not_642_out, i5);
  not not_643 (not_643_out, i2);
  not not_644 (not_644_out, i6);
  not not_645 (not_645_out, i2);
  not not_646 (not_646_out, i1);
  not not_647 (not_647_out, i3);
  not not_648 (not_648_out, i1);
  not not_649 (not_649_out, i6);
  not not_650 (not_650_out, i5);
  not not_651 (not_651_out, i3);
  not not_652 (not_652_out, i2);
  not not_653 (not_653_out, i2);
  not not_654 (not_654_out, i1);
  not not_655 (not_655_out, i5);
  not not_656 (not_656_out, i3);
  not not_657 (not_657_out, i2);
  not not_658 (not_658_out, i7);
  not not_659 (not_659_out, i6);
  not not_660 (not_660_out, i5);
  not not_661 (not_661_out, i3);
  not not_662 (not_662_out, i1);
  not not_663 (not_663_out, i8);
  not not_664 (not_664_out, i6);
  not not_665 (not_665_out, i4);
  not not_666 (not_666_out, i1);
  not not_667 (not_667_out, i7);
  not not_668 (not_668_out, i6);
  not not_669 (not_669_out, i4);
  not not_670 (not_670_out, i3);
  not not_671 (not_671_out, i1);
  not not_672 (not_672_out, i8);
  not not_673 (not_673_out, i6);
  not not_674 (not_674_out, i5);
  not not_675 (not_675_out, i2);
  not not_676 (not_676_out, i1);
  not not_677 (not_677_out, i8);
  not not_678 (not_678_out, i7);
  not not_679 (not_679_out, i4);
  not not_680 (not_680_out, i3);
  not not_681 (not_681_out, i1);
  not not_682 (not_682_out, i7);
  not not_683 (not_683_out, i6);
  not not_684 (not_684_out, i1);
  not not_685 (not_685_out, i7);
  not not_686 (not_686_out, i2);
  not not_687 (not_687_out, i1);
  not not_688 (not_688_out, i8);
  not not_689 (not_689_out, i3);
  not not_690 (not_690_out, i1);
  not not_691 (not_691_out, i8);
  not not_692 (not_692_out, i4);
  not not_693 (not_693_out, i2);
  not not_694 (not_694_out, i1);
  not not_695 (not_695_out, i8);
  not not_696 (not_696_out, i5);
  not not_697 (not_697_out, i4);
  not not_698 (not_698_out, i1);
  not not_699 (not_699_out, i8);
  not not_700 (not_700_out, i7);
  not not_701 (not_701_out, i3);
  not not_702 (not_702_out, i1);
  not not_703 (not_703_out, i8);
  not not_704 (not_704_out, i1);
  not not_705 (not_705_out, i7);
  not not_706 (not_706_out, i4);
  not not_707 (not_707_out, i3);
  not not_708 (not_708_out, i1);
  not not_709 (not_709_out, i7);
  not not_710 (not_710_out, i3);
  not not_711 (not_711_out, i1);
  not not_712 (not_712_out, i8);
  not not_713 (not_713_out, i5);
  not not_714 (not_714_out, i1);
  not not_715 (not_715_out, i5);
  not not_716 (not_716_out, i1);
  not not_717 (not_717_out, i8);
  not not_718 (not_718_out, i6);
  not not_719 (not_719_out, i2);
  not not_720 (not_720_out, i1);
  not not_721 (not_721_out, i3);
  not not_722 (not_722_out, i2);
  not not_723 (not_723_out, i1);
  not not_724 (not_724_out, i8);
  not not_725 (not_725_out, i5);
  not not_726 (not_726_out, i4);
  not not_727 (not_727_out, i1);
  not not_728 (not_728_out, i8);
  not not_729 (not_729_out, i4);
  not not_730 (not_730_out, i1);
  not not_731 (not_731_out, i5);
  not not_732 (not_732_out, i1);
  not not_733 (not_733_out, i7);
  not not_734 (not_734_out, i5);
  not not_735 (not_735_out, i3);
  not not_736 (not_736_out, i1);
  not not_737 (not_737_out, i6);
  not not_738 (not_738_out, i5);
  not not_739 (not_739_out, i4);
  not not_740 (not_740_out, i2);
  not not_741 (not_741_out, i1);
  not not_742 (not_742_out, i6);
  not not_743 (not_743_out, i5);
  not not_744 (not_744_out, i3);
  not not_745 (not_745_out, i2);
  not not_746 (not_746_out, i1);
  not not_747 (not_747_out, i7);
  not not_748 (not_748_out, i6);
  not not_749 (not_749_out, i2);
  not not_750 (not_750_out, i1);
  not not_751 (not_751_out, i6);
  not not_752 (not_752_out, i5);
  not not_753 (not_753_out, i1);
  not not_754 (not_754_out, i7);
  not not_755 (not_755_out, i1);
  not not_756 (not_756_out, i4);
  not not_757 (not_757_out, i1);
  not not_758 (not_758_out, i5);
  not not_759 (not_759_out, i2);
  not not_760 (not_760_out, i1);
  not not_761 (not_761_out, i6);
  not not_762 (not_762_out, i1);
  not not_763 (not_763_out, i6);
  not not_764 (not_764_out, i2);
  not not_765 (not_765_out, i1);
  not not_766 (not_766_out, i3);
  not not_767 (not_767_out, i1);
  not not_768 (not_768_out, i2);
  not not_769 (not_769_out, i1);
  not not_770 (not_770_out, i8);
  not not_771 (not_771_out, i6);
  not not_772 (not_772_out, i4);
  not not_773 (not_773_out, i2);
  not not_774 (not_774_out, i1);
  not not_775 (not_775_out, i8);
  not not_776 (not_776_out, i7);
  not not_777 (not_777_out, i5);
  not not_778 (not_778_out, i4);
  not not_779 (not_779_out, i1);
  not not_780 (not_780_out, i8);
  not not_781 (not_781_out, i6);
  not not_782 (not_782_out, i5);
  not not_783 (not_783_out, i4);
  not not_784 (not_784_out, i2);
  not not_785 (not_785_out, i8);
  not not_786 (not_786_out, i7);
  not not_787 (not_787_out, i6);
  not not_788 (not_788_out, i3);
  not not_789 (not_789_out, i2);
  not not_790 (not_790_out, i8);
  not not_791 (not_791_out, i6);
  not not_792 (not_792_out, i1);
  not not_793 (not_793_out, i8);
  not not_794 (not_794_out, i6);
  not not_795 (not_795_out, i5);
  not not_796 (not_796_out, i8);
  not not_797 (not_797_out, i7);
  not not_798 (not_798_out, i6);
  not not_799 (not_799_out, i4);
  not not_800 (not_800_out, i3);
  not not_801 (not_801_out, i7);
  not not_802 (not_802_out, i6);
  not not_803 (not_803_out, i2);
  not not_804 (not_804_out, i1);
  not not_805 (not_805_out, i8);
  not not_806 (not_806_out, i7);
  not not_807 (not_807_out, i6);
  not not_808 (not_808_out, i2);
  not not_809 (not_809_out, i8);
  not not_810 (not_810_out, i6);
  not not_811 (not_811_out, i3);
  not not_812 (not_812_out, i2);
  not not_813 (not_813_out, i8);
  not not_814 (not_814_out, i5);
  not not_815 (not_815_out, i4);
  not not_816 (not_816_out, i3);
  not not_817 (not_817_out, i8);
  not not_818 (not_818_out, i7);
  not not_819 (not_819_out, i4);
  not not_820 (not_820_out, i7);
  not not_821 (not_821_out, i5);
  not not_822 (not_822_out, i1);
  not not_823 (not_823_out, i8);
  not not_824 (not_824_out, i2);
  not not_825 (not_825_out, i1);
  not not_826 (not_826_out, i8);
  not not_827 (not_827_out, i5);
  not not_828 (not_828_out, i2);
  not not_829 (not_829_out, i8);
  not not_830 (not_830_out, i7);
  not not_831 (not_831_out, i4);
  not not_832 (not_832_out, i3);
  not not_833 (not_833_out, i2);
  not not_834 (not_834_out, i7);
  not not_835 (not_835_out, i3);
  not not_836 (not_836_out, i1);
  not not_837 (not_837_out, i8);
  not not_838 (not_838_out, i7);
  not not_839 (not_839_out, i3);
  not not_840 (not_840_out, i8);
  not not_841 (not_841_out, i6);
  not not_842 (not_842_out, i5);
  not not_843 (not_843_out, i4);
  not not_844 (not_844_out, i2);
  not not_845 (not_845_out, i8);
  not not_846 (not_846_out, i5);
  not not_847 (not_847_out, i4);
  not not_848 (not_848_out, i2);
  not not_849 (not_849_out, i1);
  not not_850 (not_850_out, i5);
  not not_851 (not_851_out, i4);
  not not_852 (not_852_out, i3);
  not not_853 (not_853_out, i1);
  not not_854 (not_854_out, i8);
  not not_855 (not_855_out, i6);
  not not_856 (not_856_out, i4);
  not not_857 (not_857_out, i2);
  not not_858 (not_858_out, i6);
  not not_859 (not_859_out, i5);
  not not_860 (not_860_out, i1);
  not not_861 (not_861_out, i8);
  not not_862 (not_862_out, i6);
  not not_863 (not_863_out, i5);
  not not_864 (not_864_out, i8);
  not not_865 (not_865_out, i6);
  not not_866 (not_866_out, i8);
  not not_867 (not_867_out, i4);
  not not_868 (not_868_out, i1);
  not not_869 (not_869_out, i8);
  not not_870 (not_870_out, i5);
  not not_871 (not_871_out, i2);
  not not_872 (not_872_out, i8);
  not not_873 (not_873_out, i5);
  not not_874 (not_874_out, i1);
  not not_875 (not_875_out, i8);
  not not_876 (not_876_out, i2);
  not not_877 (not_877_out, i8);
  not not_878 (not_878_out, i4);
  not not_879 (not_879_out, i1);
  not not_880 (not_880_out, i7);
  not not_881 (not_881_out, i6);
  not not_882 (not_882_out, i4);
  not not_883 (not_883_out, i3);
  not not_884 (not_884_out, i2);
  not not_885 (not_885_out, i6);
  not not_886 (not_886_out, i4);
  not not_887 (not_887_out, i1);
  not not_888 (not_888_out, i6);
  not not_889 (not_889_out, i5);
  not not_890 (not_890_out, i4);
  not not_891 (not_891_out, i6);
  not not_892 (not_892_out, i5);
  not not_893 (not_893_out, i2);
  not not_894 (not_894_out, i1);
  not not_895 (not_895_out, i7);
  not not_896 (not_896_out, i6);
  not not_897 (not_897_out, i3);
  not not_898 (not_898_out, i7);
  not not_899 (not_899_out, i6);
  not not_900 (not_900_out, i4);
  not not_901 (not_901_out, i2);
  not not_902 (not_902_out, i6);
  not not_903 (not_903_out, i4);
  not not_904 (not_904_out, i3);
  not not_905 (not_905_out, i2);
  not not_906 (not_906_out, i7);
  not not_907 (not_907_out, i6);
  not not_908 (not_908_out, i6);
  not not_909 (not_909_out, i3);
  not not_910 (not_910_out, i4);
  not not_911 (not_911_out, i2);
  not not_912 (not_912_out, i1);
  not not_913 (not_913_out, i5);
  not not_914 (not_914_out, i4);
  not not_915 (not_915_out, i2);
  not not_916 (not_916_out, i7);
  not not_917 (not_917_out, i3);
  not not_918 (not_918_out, i2);
  not not_919 (not_919_out, i1);
  not not_920 (not_920_out, i5);
  not not_921 (not_921_out, i7);
  not not_922 (not_922_out, i4);
  not not_923 (not_923_out, i3);
  not not_924 (not_924_out, i7);
  not not_925 (not_925_out, i2);
  not not_926 (not_926_out, i3);
  not not_927 (not_927_out, i2);
  not not_928 (not_928_out, i6);
  not not_929 (not_929_out, i5);
  not not_930 (not_930_out, i4);
  not not_931 (not_931_out, i5);
  not not_932 (not_932_out, i1);
  not not_933 (not_933_out, i6);
  not not_934 (not_934_out, i4);
  not not_935 (not_935_out, i6);
  not not_936 (not_936_out, i2);
  not not_937 (not_937_out, i1);
  not not_938 (not_938_out, i6);
  not not_939 (not_939_out, i5);
  not not_940 (not_940_out, i2);
  not not_941 (not_941_out, i5);
  not not_942 (not_942_out, i4);
  not not_943 (not_943_out, i2);
  not not_944 (not_944_out, i4);
  not not_945 (not_945_out, i2);
  not not_946 (not_946_out, i5);
  not not_947 (not_947_out, i8);
  not not_948 (not_948_out, i7);
  not not_949 (not_949_out, i6);
  not not_950 (not_950_out, i4);
  not not_951 (not_951_out, i3);
  not not_952 (not_952_out, i7);
  not not_953 (not_953_out, i6);
  not not_954 (not_954_out, i5);
  not not_955 (not_955_out, i4);
  not not_956 (not_956_out, i2);
  not not_957 (not_957_out, i7);
  not not_958 (not_958_out, i5);
  not not_959 (not_959_out, i1);
  not not_960 (not_960_out, i8);
  not not_961 (not_961_out, i6);
  not not_962 (not_962_out, i3);
  not not_963 (not_963_out, i2);
  not not_964 (not_964_out, i8);
  not not_965 (not_965_out, i6);
  not not_966 (not_966_out, i2);
  not not_967 (not_967_out, i1);
  not not_968 (not_968_out, i8);
  not not_969 (not_969_out, i7);
  not not_970 (not_970_out, i6);
  not not_971 (not_971_out, i5);
  not not_972 (not_972_out, i8);
  not not_973 (not_973_out, i7);
  not not_974 (not_974_out, i5);
  not not_975 (not_975_out, i2);
  not not_976 (not_976_out, i7);
  not not_977 (not_977_out, i6);
  not not_978 (not_978_out, i3);
  not not_979 (not_979_out, i1);
  not not_980 (not_980_out, i7);
  not not_981 (not_981_out, i3);
  not not_982 (not_982_out, i2);
  not not_983 (not_983_out, i1);
  not not_984 (not_984_out, i8);
  not not_985 (not_985_out, i6);
  not not_986 (not_986_out, i4);
  not not_987 (not_987_out, i3);
  not not_988 (not_988_out, i8);
  not not_989 (not_989_out, i6);
  not not_990 (not_990_out, i4);
  not not_991 (not_991_out, i1);
  not not_992 (not_992_out, i8);
  not not_993 (not_993_out, i7);
  not not_994 (not_994_out, i4);
  not not_995 (not_995_out, i8);
  not not_996 (not_996_out, i6);
  not not_997 (not_997_out, i2);
  not not_998 (not_998_out, i8);
  not not_999 (not_999_out, i7);
  not not_1000 (not_1000_out, i4);
  not not_1001 (not_1001_out, i3);
  not not_1002 (not_1002_out, i2);
  not not_1003 (not_1003_out, i8);
  not not_1004 (not_1004_out, i7);
  not not_1005 (not_1005_out, i5);
  not not_1006 (not_1006_out, i3);
  not not_1007 (not_1007_out, i8);
  not not_1008 (not_1008_out, i5);
  not not_1009 (not_1009_out, i4);
  not not_1010 (not_1010_out, i7);
  not not_1011 (not_1011_out, i5);
  not not_1012 (not_1012_out, i4);
  not not_1013 (not_1013_out, i3);
  not not_1014 (not_1014_out, i7);
  not not_1015 (not_1015_out, i5);
  not not_1016 (not_1016_out, i1);
  not not_1017 (not_1017_out, i8);
  not not_1018 (not_1018_out, i7);
  not not_1019 (not_1019_out, i4);
  not not_1020 (not_1020_out, i7);
  not not_1021 (not_1021_out, i4);
  not not_1022 (not_1022_out, i8);
  not not_1023 (not_1023_out, i7);
  not not_1024 (not_1024_out, i8);
  not not_1025 (not_1025_out, i3);
  not not_1026 (not_1026_out, i8);
  not not_1027 (not_1027_out, i6);
  not not_1028 (not_1028_out, i5);
  not not_1029 (not_1029_out, i4);
  not not_1030 (not_1030_out, i2);
  not not_1031 (not_1031_out, i5);
  not not_1032 (not_1032_out, i3);
  not not_1033 (not_1033_out, i1);
  not not_1034 (not_1034_out, i8);
  not not_1035 (not_1035_out, i6);
  not not_1036 (not_1036_out, i5);
  not not_1037 (not_1037_out, i8);
  not not_1038 (not_1038_out, i6);
  not not_1039 (not_1039_out, i8);
  not not_1040 (not_1040_out, i6);
  not not_1041 (not_1041_out, i2);
  not not_1042 (not_1042_out, i8);
  not not_1043 (not_1043_out, i2);
  not not_1044 (not_1044_out, i5);
  not not_1045 (not_1045_out, i3);
  not not_1046 (not_1046_out, i1);
  not not_1047 (not_1047_out, i8);
  not not_1048 (not_1048_out, i4);
  not not_1049 (not_1049_out, i8);
  not not_1050 (not_1050_out, i5);
  not not_1051 (not_1051_out, i2);
  not not_1052 (not_1052_out, i8);
  not not_1053 (not_1053_out, i4);
  not not_1054 (not_1054_out, i3);
  not not_1055 (not_1055_out, i1);
  not not_1056 (not_1056_out, i7);
  not not_1057 (not_1057_out, i6);
  not not_1058 (not_1058_out, i3);
  not not_1059 (not_1059_out, i2);
  not not_1060 (not_1060_out, i1);
  not not_1061 (not_1061_out, i6);
  not not_1062 (not_1062_out, i4);
  not not_1063 (not_1063_out, i3);
  not not_1064 (not_1064_out, i2);
  not not_1065 (not_1065_out, i6);
  not not_1066 (not_1066_out, i4);
  not not_1067 (not_1067_out, i2);
  not not_1068 (not_1068_out, i1);
  not not_1069 (not_1069_out, i7);
  not not_1070 (not_1070_out, i6);
  not not_1071 (not_1071_out, i5);
  not not_1072 (not_1072_out, i7);
  not not_1073 (not_1073_out, i6);
  not not_1074 (not_1074_out, i7);
  not not_1075 (not_1075_out, i6);
  not not_1076 (not_1076_out, i3);
  not not_1077 (not_1077_out, i2);
  not not_1078 (not_1078_out, i7);
  not not_1079 (not_1079_out, i6);
  not not_1080 (not_1080_out, i2);
  not not_1081 (not_1081_out, i1);
  not not_1082 (not_1082_out, i7);
  not not_1083 (not_1083_out, i3);
  not not_1084 (not_1084_out, i1);
  not not_1085 (not_1085_out, i6);
  not not_1086 (not_1086_out, i4);
  not not_1087 (not_1087_out, i2);
  not not_1088 (not_1088_out, i6);
  not not_1089 (not_1089_out, i3);
  not not_1090 (not_1090_out, i2);
  not not_1091 (not_1091_out, i1);
  not not_1092 (not_1092_out, i6);
  not not_1093 (not_1093_out, i7);
  not not_1094 (not_1094_out, i5);
  not not_1095 (not_1095_out, i2);
  not not_1096 (not_1096_out, i7);
  not not_1097 (not_1097_out, i2);
  not not_1098 (not_1098_out, i3);
  not not_1099 (not_1099_out, i2);
  not not_1100 (not_1100_out, i7);
  not not_1101 (not_1101_out, i5);
  not not_1102 (not_1102_out, i4);
  not not_1103 (not_1103_out, i3);
  not not_1104 (not_1104_out, i2);
  not not_1105 (not_1105_out, i6);
  not not_1106 (not_1106_out, i5);
  not not_1107 (not_1107_out, i3);
  not not_1108 (not_1108_out, i6);
  not not_1109 (not_1109_out, i4);
  not not_1110 (not_1110_out, i6);
  not not_1111 (not_1111_out, i5);
  not not_1112 (not_1112_out, i2);
  not not_1113 (not_1113_out, i5);
  not not_1114 (not_1114_out, i1);
  not not_1115 (not_1115_out, i5);
  not not_1116 (not_1116_out, i4);
  not not_1117 (not_1117_out, i2);
  not not_1118 (not_1118_out, i5);
  not not_1119 (not_1119_out, i2);
  and and_1 (and_1_out, not_1_out, not_2_out, not_3_out, not_4_out, not_5_out);
  and and_2 (and_2_out, not_6_out, not_7_out, not_8_out, not_9_out, not_10_out);
  and and_3 (and_3_out, not_11_out, not_12_out, not_13_out, not_14_out, i2);
  and and_4 (and_4_out, not_15_out, not_16_out, not_17_out, i2, not_18_out);
  and and_5 (and_5_out, not_19_out, not_20_out, not_21_out, i3, i1);
  and and_6 (and_6_out, not_22_out, not_23_out, i3, i2, i1);
  and and_7 (and_7_out, not_24_out, not_25_out, not_26_out, i4, not_27_out);
  and and_8 (and_8_out, not_28_out, not_29_out, i4, not_30_out, i1);
  and and_9 (and_9_out, not_31_out, not_32_out, i5, not_33_out, not_34_out, not_35_out);
  and and_10 (and_10_out, not_36_out, not_37_out, i5, not_38_out, i1);
  and and_11 (and_11_out, not_39_out, not_40_out, i5, not_41_out, i2);
  and and_12 (and_12_out, not_42_out, not_43_out, i5, not_44_out, not_45_out, i2);
  and and_13 (and_13_out, not_46_out, not_47_out, i5, i3, not_48_out);
  and and_14 (and_14_out, not_49_out, i5, i3, not_50_out, not_51_out);
  and and_15 (and_15_out, not_52_out, i5, i4, not_53_out, i2, not_54_out);
  and and_16 (and_16_out, not_55_out, not_56_out, i6, not_57_out, not_58_out);
  and and_17 (and_17_out, not_59_out, i6, not_60_out, not_61_out, not_62_out);
  and and_18 (and_18_out, not_63_out, i6, not_64_out, not_65_out, i2, i1);
  and and_19 (and_19_out, not_66_out, not_67_out, i6, not_68_out, not_69_out, i3);
  and and_20 (and_20_out, not_70_out, i6, not_71_out, i3, i1);
  and and_21 (and_21_out, not_72_out, i6, i4, not_73_out, i2);
  and and_22 (and_22_out, not_74_out, i6, i4, i2, not_75_out);
  and and_23 (and_23_out, not_76_out, i6, i5, not_77_out, not_78_out);
  and and_24 (and_24_out, not_79_out, i6, i5, not_80_out, not_81_out, not_82_out);
  and and_25 (and_25_out, not_83_out, i6, i5, not_84_out, i2, not_85_out);
  and and_26 (and_26_out, not_86_out, i6, i5, not_87_out, i3, i1);
  and and_27 (and_27_out, not_88_out, not_89_out, i6, i5, i4, not_90_out);
  and and_28 (and_28_out, not_91_out, i6, i5, i4, i2);
  and and_29 (and_29_out, not_92_out, i7, not_93_out, not_94_out, i1);
  and and_30 (and_30_out, i7, not_95_out, not_96_out, i2, i1);
  and and_31 (and_31_out, not_97_out, i7, not_98_out, i3, not_99_out);
  and and_32 (and_32_out, i7, not_100_out, not_101_out, i3, not_102_out, i1);
  and and_33 (and_33_out, i7, not_103_out, i3, i2, not_104_out);
  and and_34 (and_34_out, not_105_out, i7, not_106_out, i4, not_107_out);
  and and_35 (and_35_out, not_108_out, i7, not_109_out, not_110_out, i4, i1);
  and and_36 (and_36_out, not_111_out, i7, not_112_out, i4, not_113_out, i1);
  and and_37 (and_37_out, i7, i5, not_114_out, not_115_out, not_116_out);
  and and_38 (and_38_out, i7, i5, not_117_out, i3, i1);
  and and_39 (and_39_out, i7, i5, i3, i2, i1);
  and and_40 (and_40_out, not_118_out, i7, i6, not_119_out, not_120_out, not_121_out);
  and and_41 (and_41_out, i7, i6, not_122_out, not_123_out, i1);
  and and_42 (and_42_out, i7, i6, not_124_out, i3, not_125_out);
  and and_43 (and_43_out, not_126_out, i7, i6, i5, not_127_out, i1);
  and and_44 (and_44_out, not_128_out, i7, i6, i5, not_129_out, i3);
  and and_45 (and_45_out, i7, i6, i5, i3, i1);
  and and_46 (and_46_out, i8, not_130_out, not_131_out, not_132_out, not_133_out, not_134_out);
  and and_47 (and_47_out, i8, not_135_out, not_136_out, not_137_out, not_138_out, not_139_out);
  and and_48 (and_48_out, i8, not_140_out, not_141_out, not_142_out, not_143_out);
  and and_49 (and_49_out, i8, not_144_out, not_145_out, not_146_out, not_147_out);
  and and_50 (and_50_out, i8, not_148_out, not_149_out, not_150_out, not_151_out, not_152_out);
  and and_51 (and_51_out, i8, not_153_out, not_154_out, i4, i2);
  and and_52 (and_52_out, i8, not_155_out, i4, i2, i1);
  and and_53 (and_53_out, i8, not_156_out, i5, not_157_out, i1);
  and and_54 (and_54_out, i8, not_158_out, not_159_out, i5, i3, not_160_out);
  and and_55 (and_55_out, i8, not_161_out, i5, i3, not_162_out);
  and and_56 (and_56_out, i8, not_163_out, i5, i4, not_164_out, not_165_out);
  and and_57 (and_57_out, i8, i6, not_166_out, not_167_out, i2);
  and and_58 (and_58_out, i8, i6, not_168_out, i2, not_169_out);
  and and_59 (and_59_out, i8, i6, not_170_out, i4, not_171_out);
  and and_60 (and_60_out, i8, i6, i4, not_172_out, i1);
  and and_61 (and_61_out, i8, i6, i5, not_173_out, i2);
  and and_62 (and_62_out, i8, i7, not_174_out, not_175_out, not_176_out);
  and and_63 (and_63_out, i8, i7, not_177_out, not_178_out, i2, i1);
  and and_64 (and_64_out, i8, i7, not_179_out, i4, i2);
  and and_65 (and_65_out, i8, i7, not_180_out, i5, not_181_out, not_182_out);
  and and_66 (and_66_out, i8, i7, i5, not_183_out, not_184_out);
  and and_67 (and_67_out, i8, i7, i6, not_185_out, not_186_out, i1);
  and and_68 (and_68_out, i8, i7, i6, i4, not_187_out);
  and and_69 (and_69_out, i8, i7, i6, not_188_out, i4, i1);
  and and_70 (and_70_out, not_189_out, not_190_out, not_191_out, not_192_out, not_193_out);
  and and_71 (and_71_out, not_194_out, not_195_out, not_196_out, not_197_out, not_198_out);
  and and_72 (and_72_out, not_199_out, not_200_out, not_201_out, not_202_out, i2);
  and and_73 (and_73_out, not_203_out, not_204_out, not_205_out, i2, i1);
  and and_74 (and_74_out, not_206_out, not_207_out, not_208_out, i3, not_209_out, not_210_out);
  and and_75 (and_75_out, not_211_out, not_212_out, not_213_out, i4, not_214_out, i1);
  and and_76 (and_76_out, not_215_out, not_216_out, not_217_out, i4, i2, not_218_out);
  and and_77 (and_77_out, not_219_out, not_220_out, i5, not_221_out, not_222_out, i1);
  and and_78 (and_78_out, not_223_out, not_224_out, i5, not_225_out, not_226_out, i2);
  and and_79 (and_79_out, not_227_out, i5, not_228_out, not_229_out, i2, i1);
  and and_80 (and_80_out, not_230_out, not_231_out, not_232_out, i5, i3);
  and and_81 (and_81_out, not_233_out, not_234_out, i5, i4, not_235_out, not_236_out, not_237_out);
  and and_82 (and_82_out, not_238_out, i5, i4, not_239_out, i2, i1);
  and and_83 (and_83_out, not_240_out, not_241_out, i5, i4, i3);
  and and_84 (and_84_out, not_242_out, i6, not_243_out, not_244_out, i1);
  and and_85 (and_85_out, not_245_out, i6, not_246_out, i2, not_247_out);
  and and_86 (and_86_out, not_248_out, i6, not_249_out, not_250_out, i3, i1);
  and and_87 (and_87_out, not_251_out, i6, not_252_out, i4, not_253_out, not_254_out);
  and and_88 (and_88_out, not_255_out, not_256_out, i6, i4, not_257_out, i2);
  and and_89 (and_89_out, not_258_out, i6, i4, i2, i1);
  and and_90 (and_90_out, not_259_out, not_260_out, i6, i5, not_261_out, not_262_out);
  and and_91 (and_91_out, not_263_out, i6, i5, not_264_out, not_265_out, i1);
  and and_92 (and_92_out, not_266_out, i6, i5, not_267_out, not_268_out, i2);
  and and_93 (and_93_out, not_269_out, i6, i5, not_270_out, i2, i1);
  and and_94 (and_94_out, not_271_out, i6, i5, i3, not_272_out);
  and and_95 (and_95_out, not_273_out, i6, i5, i4, not_274_out, i1);
  and and_96 (and_96_out, i7, not_275_out, not_276_out, not_277_out, not_278_out, not_279_out);
  and and_97 (and_97_out, not_280_out, i7, not_281_out, not_282_out, i3);
  and and_98 (and_98_out, i7, not_283_out, not_284_out, i3, i1);
  and and_99 (and_99_out, i7, not_285_out, i3, i2, i1);
  and and_100 (and_100_out, not_286_out, i7, not_287_out, i5, not_288_out);
  and and_101 (and_101_out, i7, not_289_out, i5, i3, not_290_out, not_291_out);
  and and_102 (and_102_out, not_292_out, i7, not_293_out, i5, i4, not_294_out);
  and and_103 (and_103_out, not_295_out, i7, not_296_out, i5, i4, not_297_out);
  and and_104 (and_104_out, i7, i5, i4, i3, not_298_out, not_299_out);
  and and_105 (and_105_out, not_300_out, i7, i6, not_301_out, not_302_out, i1);
  and and_106 (and_106_out, not_303_out, i7, i6, not_304_out, i3, i1);
  and and_107 (and_107_out, i7, i6, not_305_out, i3, i1);
  and and_108 (and_108_out, i7, i6, not_306_out, i3, i2);
  and and_109 (and_109_out, i7, i6, i5, not_307_out, not_308_out);
  and and_110 (and_110_out, i8, not_309_out, not_310_out, not_311_out, not_312_out, i1);
  and and_111 (and_111_out, i8, not_313_out, not_314_out, not_315_out, i2, not_316_out);
  and and_112 (and_112_out, i8, not_317_out, not_318_out, i3, i2, not_319_out);
  and and_113 (and_113_out, i8, not_320_out, not_321_out, i4, i2, i1);
  and and_114 (and_114_out, i8, not_322_out, not_323_out, i4, i3, not_324_out);
  and and_115 (and_115_out, i8, not_325_out, i5, not_326_out, not_327_out, not_328_out);
  and and_116 (and_116_out, i8, not_329_out, i5, i3, i1);
  and and_117 (and_117_out, i8, not_330_out, i5, i4, not_331_out, i1);
  and and_118 (and_118_out, i8, not_332_out, i5, i4, i2, not_333_out);
  and and_119 (and_119_out, i8, not_334_out, i6, not_335_out, not_336_out);
  and and_120 (and_120_out, i8, i6, not_337_out, not_338_out, not_339_out, not_340_out);
  and and_121 (and_121_out, i8, i6, not_341_out, i2, i1);
  and and_122 (and_122_out, i8, i6, not_342_out, i4, not_343_out, i1);
  and and_123 (and_123_out, i8, i6, i5, i4, not_344_out, not_345_out);
  and and_124 (and_124_out, i8, i7, not_346_out, not_347_out, not_348_out, not_349_out);
  and and_125 (and_125_out, i8, i7, not_350_out, not_351_out, i4, not_352_out, not_353_out);
  and and_126 (and_126_out, i8, i7, not_354_out, i4, not_355_out, not_356_out);
  and and_127 (and_127_out, i8, i7, i5, not_357_out, i1);
  and and_128 (and_128_out, i8, i7, not_358_out, i5, i2, not_359_out);
  and and_129 (and_129_out, i8, i7, not_360_out, i5, i3, not_361_out);
  and and_130 (and_130_out, i8, i7, not_362_out, i5, i4, i2);
  and and_131 (and_131_out, i8, i7, i6, i5, not_363_out, not_364_out);
  and and_132 (and_132_out, i8, i7, i6, i5, i4, not_365_out);
  and and_133 (and_133_out, i8, i7, i6, i5, i4, not_366_out);
  and and_134 (and_134_out, not_367_out, not_368_out, not_369_out, not_370_out);
  and and_135 (and_135_out, not_371_out, not_372_out, not_373_out, not_374_out, not_375_out);
  and and_136 (and_136_out, not_376_out, not_377_out, not_378_out, not_379_out, i3);
  and and_137 (and_137_out, not_380_out, not_381_out, i4, i2);
  and and_138 (and_138_out, not_382_out, not_383_out, i5, not_384_out);
  and and_139 (and_139_out, not_385_out, i5, not_386_out, not_387_out);
  and and_140 (and_140_out, not_388_out, i5, not_389_out, i2);
  and and_141 (and_141_out, not_390_out, not_391_out, i5, i3, not_392_out);
  and and_142 (and_142_out, not_393_out, not_394_out, i6, not_395_out, i2);
  and and_143 (and_143_out, not_396_out, i6, not_397_out, i3, i2);
  and and_144 (and_144_out, not_398_out, i6, i4, not_399_out);
  and and_145 (and_145_out, not_400_out, i6, i5, not_401_out);
  and and_146 (and_146_out, not_402_out, i6, i5, not_403_out, i2);
  and and_147 (and_147_out, not_404_out, i7, not_405_out, not_406_out, not_407_out);
  and and_148 (and_148_out, i7, not_408_out, not_409_out, i3);
  and and_149 (and_149_out, i7, not_410_out, i3, not_411_out);
  and and_150 (and_150_out, i7, not_412_out, i5, not_413_out, not_414_out);
  and and_151 (and_151_out, not_415_out, i7, i5, not_416_out, i3);
  and and_152 (and_152_out, not_417_out, i7, i6, not_418_out, i4);
  and and_153 (and_153_out, i7, i6, i5, i3, i2);
  and and_154 (and_154_out, i8, not_419_out, not_420_out, i2);
  and and_155 (and_155_out, i8, not_421_out, not_422_out, i4, not_423_out);
  and and_156 (and_156_out, i8, not_424_out, not_425_out, i4, not_426_out);
  and and_157 (and_157_out, i8, not_427_out, i5, i4, i3);
  and and_158 (and_158_out, i8, i6, not_428_out, not_429_out);
  and and_159 (and_159_out, i8, i6, i4, i2);
  and and_160 (and_160_out, i8, i7, not_430_out, i3);
  and and_161 (and_161_out, i8, i7, not_431_out, i4, not_432_out);
  and and_162 (and_162_out, i8, i7, i5, i4, not_433_out);
  and and_163 (and_163_out, i8, i7, i6, not_434_out, i2);
  and and_164 (and_164_out, not_435_out, not_436_out, not_437_out, not_438_out, not_439_out);
  and and_165 (and_165_out, not_440_out, not_441_out, not_442_out, not_443_out, not_444_out, not_445_out, i2);
  and and_166 (and_166_out, not_446_out, not_447_out, not_448_out, i2, not_449_out);
  and and_167 (and_167_out, not_450_out, not_451_out, not_452_out, not_453_out, i2, not_454_out);
  and and_168 (and_168_out, not_455_out, not_456_out, not_457_out, not_458_out, i3, not_459_out, i1);
  and and_169 (and_169_out, not_460_out, not_461_out, not_462_out, i4, not_463_out, not_464_out);
  and and_170 (and_170_out, not_465_out, not_466_out, not_467_out, not_468_out, i4, i3, i1);
  and and_171 (and_171_out, not_469_out, not_470_out, not_471_out, i4, i3, not_472_out, i1);
  and and_172 (and_172_out, not_473_out, not_474_out, i5, not_475_out, not_476_out, not_477_out);
  and and_173 (and_173_out, not_478_out, not_479_out, i5, i3, not_480_out);
  and and_174 (and_174_out, not_481_out, i5, i3, not_482_out, not_483_out);
  and and_175 (and_175_out, not_484_out, not_485_out, not_486_out, i5, not_487_out, i3, i2);
  and and_176 (and_176_out, not_488_out, not_489_out, i5, i4, not_490_out, not_491_out, i1);
  and and_177 (and_177_out, not_492_out, i5, i4, not_493_out, i2, not_494_out);
  and and_178 (and_178_out, not_495_out, i6, not_496_out, not_497_out, not_498_out);
  and and_179 (and_179_out, not_499_out, not_500_out, i6, not_501_out, not_502_out, not_503_out, i1);
  and and_180 (and_180_out, not_504_out, i6, not_505_out, not_506_out, i3, not_507_out);
  and and_181 (and_181_out, not_508_out, not_509_out, i6, i4, not_510_out, not_511_out);
  and and_182 (and_182_out, not_512_out, not_513_out, i6, not_514_out, i4, not_515_out, i2);
  and and_183 (and_183_out, not_516_out, i6, i4, i2, not_517_out);
  and and_184 (and_184_out, not_518_out, i6, i5, not_519_out, not_520_out, not_521_out);
  and and_185 (and_185_out, not_522_out, i6, i5, not_523_out, i2, not_524_out);
  and and_186 (and_186_out, not_525_out, not_526_out, i6, i5, not_527_out, i3, i1);
  and and_187 (and_187_out, not_528_out, i6, i5, not_529_out, i3, i2, i1);
  and and_188 (and_188_out, not_530_out, not_531_out, i6, i5, i4, i3, i2);
  and and_189 (and_189_out, i7, not_532_out, not_533_out, not_534_out, not_535_out, not_536_out, i1);
  and and_190 (and_190_out, not_537_out, i7, not_538_out, i3, not_539_out);
  and and_191 (and_191_out, i7, not_540_out, i3, i2, not_541_out);
  and and_192 (and_192_out, not_542_out, i7, not_543_out, not_544_out, i4, not_545_out, i1);
  and and_193 (and_193_out, not_546_out, i7, not_547_out, i4, not_548_out, not_549_out, i1);
  and and_194 (and_194_out, i7, i5, not_550_out, not_551_out, not_552_out);
  and and_195 (and_195_out, not_553_out, i7, not_554_out, i5, not_555_out, not_556_out, i2);
  and and_196 (and_196_out, i7, not_557_out, i5, not_558_out, i3, not_559_out, i1);
  and and_197 (and_197_out, not_560_out, i7, not_561_out, i5, i4, i3, not_562_out);
  and and_198 (and_198_out, not_563_out, i7, not_564_out, i5, i4, i3, i1);
  and and_199 (and_199_out, not_565_out, i7, i5, i4, i3, not_566_out, i1);
  and and_200 (and_200_out, not_567_out, i7, i6, not_568_out, not_569_out, not_570_out);
  and and_201 (and_201_out, not_571_out, i7, i6, not_572_out, i3, not_573_out);
  and and_202 (and_202_out, i7, i6, not_574_out, i3, not_575_out);
  and and_203 (and_203_out, not_576_out, i7, i6, not_577_out, not_578_out, i3, i2);
  and and_204 (and_204_out, not_579_out, i7, i6, i5, not_580_out, not_581_out, i1);
  and and_205 (and_205_out, i7, i6, i5, not_582_out, not_583_out, i2, i1);
  and and_206 (and_206_out, not_584_out, i7, i6, i5, i4, not_585_out, i2);
  and and_207 (and_207_out, i8, not_586_out, not_587_out, not_588_out, not_589_out);
  and and_208 (and_208_out, i8, not_590_out, not_591_out, not_592_out, not_593_out, not_594_out);
  and and_209 (and_209_out, i8, not_595_out, not_596_out, not_597_out, not_598_out, not_599_out);
  and and_210 (and_210_out, i8, not_600_out, not_601_out, not_602_out, i3, i2, i1);
  and and_211 (and_211_out, i8, not_603_out, not_604_out, i4, not_605_out, not_606_out);
  and and_212 (and_212_out, i8, not_607_out, not_608_out, i4, i2, not_609_out);
  and and_213 (and_213_out, i8, not_610_out, not_611_out, i5, not_612_out, not_613_out, i1);
  and and_214 (and_214_out, i8, not_614_out, i5, i3, not_615_out);
  and and_215 (and_215_out, i8, not_616_out, not_617_out, i5, i4, not_618_out, i1);
  and and_216 (and_216_out, i8, not_619_out, i5, i4, not_620_out, not_621_out, i1);
  and and_217 (and_217_out, i8, not_622_out, i6, not_623_out, not_624_out, not_625_out, i2);
  and and_218 (and_218_out, i8, i6, not_626_out, i2, not_627_out);
  and and_219 (and_219_out, i8, not_628_out, i6, not_629_out, i3, not_630_out, i1);
  and and_220 (and_220_out, i8, i6, not_631_out, i4, not_632_out, not_633_out);
  and and_221 (and_221_out, i8, not_634_out, i6, not_635_out, i4, i3, i1);
  and and_222 (and_222_out, i8, i7, not_636_out, not_637_out, not_638_out, i2, i1);
  and and_223 (and_223_out, i8, i7, not_639_out, i4, i2, not_640_out);
  and and_224 (and_224_out, i8, i7, not_641_out, not_642_out, i4, i3, not_643_out, i1);
  and and_225 (and_225_out, i8, i7, not_644_out, i5, not_645_out, not_646_out);
  and and_226 (and_226_out, i8, i7, i5, not_647_out, not_648_out);
  and and_227 (and_227_out, i8, i7, not_649_out, i5, i3, i2, i1);
  and and_228 (and_228_out, i8, i7, i6, not_650_out, not_651_out, not_652_out, i1);
  and and_229 (and_229_out, i8, i7, i6, i4, not_653_out, not_654_out);
  and and_230 (and_230_out, i8, i7, i6, not_655_out, i4, not_656_out, i1);
  and and_231 (and_231_out, i8, i7, i6, i5, i3, not_657_out, i1);
  and and_232 (and_232_out, i8, i7, i6, i5, i4, i3, i1);
  and and_233 (and_233_out, not_658_out, not_659_out, not_660_out, not_661_out, not_662_out);
  and and_234 (and_234_out, not_663_out, not_664_out, not_665_out, i2, not_666_out);
  and and_235 (and_235_out, not_667_out, not_668_out, not_669_out, not_670_out, i2, not_671_out);
  and and_236 (and_236_out, not_672_out, not_673_out, not_674_out, i4, not_675_out, not_676_out);
  and and_237 (and_237_out, not_677_out, not_678_out, i5, not_679_out, not_680_out, not_681_out);
  and and_238 (and_238_out, not_682_out, not_683_out, i5, i3, not_684_out);
  and and_239 (and_239_out, not_685_out, i5, i3, not_686_out, not_687_out);
  and and_240 (and_240_out, not_688_out, i5, i4, not_689_out, i2, not_690_out);
  and and_241 (and_241_out, not_691_out, i6, not_692_out, not_693_out, not_694_out);
  and and_242 (and_242_out, not_695_out, i6, not_696_out, not_697_out, i3, not_698_out);
  and and_243 (and_243_out, not_699_out, not_700_out, i6, i4, not_701_out, not_702_out);
  and and_244 (and_244_out, not_703_out, i6, i4, i2, not_704_out);
  and and_245 (and_245_out, not_705_out, i6, i5, not_706_out, not_707_out, not_708_out);
  and and_246 (and_246_out, not_709_out, i6, i5, not_710_out, i2, not_711_out);
  and and_247 (and_247_out, not_712_out, i7, not_713_out, i3, not_714_out);
  and and_248 (and_248_out, i7, not_715_out, i3, i2, not_716_out);
  and and_249 (and_249_out, not_717_out, i7, not_718_out, i4, not_719_out, not_720_out);
  and and_250 (and_250_out, i7, i5, not_721_out, not_722_out, not_723_out);
  and and_251 (and_251_out, not_724_out, i7, i6, not_725_out, not_726_out, not_727_out);
  and and_252 (and_252_out, not_728_out, i7, i6, not_729_out, i3, not_730_out);
  and and_253 (and_253_out, i7, i6, not_731_out, i3, not_732_out);
  and and_254 (and_254_out, i8, not_733_out, not_734_out, not_735_out, not_736_out);
  and and_255 (and_255_out, i8, not_737_out, not_738_out, not_739_out, not_740_out, not_741_out);
  and and_256 (and_256_out, i8, not_742_out, not_743_out, not_744_out, not_745_out, not_746_out);
  and and_257 (and_257_out, i8, not_747_out, not_748_out, i4, not_749_out, not_750_out);
  and and_258 (and_258_out, i8, not_751_out, not_752_out, i4, i2, not_753_out);
  and and_259 (and_259_out, i8, not_754_out, i5, i3, not_755_out);
  and and_260 (and_260_out, i8, i6, not_756_out, i2, not_757_out);
  and and_261 (and_261_out, i8, i6, not_758_out, i4, not_759_out, not_760_out);
  and and_262 (and_262_out, i8, i7, not_761_out, i4, i2, not_762_out);
  and and_263 (and_263_out, i8, i7, not_763_out, i5, not_764_out, not_765_out);
  and and_264 (and_264_out, i8, i7, i5, not_766_out, not_767_out);
  and and_265 (and_265_out, i8, i7, i6, i4, not_768_out, not_769_out);
  and and_266 (and_266_out, not_770_out, not_771_out, not_772_out, not_773_out, not_774_out);
  and and_267 (and_267_out, not_775_out, not_776_out, not_777_out, not_778_out, i3, not_779_out);
  and and_268 (and_268_out, not_780_out, not_781_out, not_782_out, not_783_out, i3, not_784_out);
  and and_269 (and_269_out, not_785_out, not_786_out, not_787_out, i4, not_788_out, not_789_out);
  and and_270 (and_270_out, not_790_out, not_791_out, i4, i2, not_792_out);
  and and_271 (and_271_out, not_793_out, not_794_out, not_795_out, i4, i3, i2);
  and and_272 (and_272_out, not_796_out, not_797_out, not_798_out, i5, not_799_out, not_800_out, i2);
  and and_273 (and_273_out, not_801_out, not_802_out, i5, i3, not_803_out, not_804_out);
  and and_274 (and_274_out, not_805_out, not_806_out, not_807_out, i5, i4, not_808_out);
  and and_275 (and_275_out, not_809_out, not_810_out, i5, i4, not_811_out, not_812_out);
  and and_276 (and_276_out, not_813_out, i6, not_814_out, not_815_out, not_816_out, i2);
  and and_277 (and_277_out, not_817_out, not_818_out, i6, not_819_out, i3, i2);
  and and_278 (and_278_out, not_820_out, i6, not_821_out, i3, i2, not_822_out);
  and and_279 (and_279_out, not_823_out, i6, i4, not_824_out, not_825_out);
  and and_280 (and_280_out, not_826_out, i6, not_827_out, i4, i3, not_828_out);
  and and_281 (and_281_out, not_829_out, not_830_out, i6, i5, not_831_out, not_832_out, not_833_out);
  and and_282 (and_282_out, not_834_out, i6, i5, not_835_out, not_836_out);
  and and_283 (and_283_out, not_837_out, not_838_out, i6, i5, i4, not_839_out, i2);
  and and_284 (and_284_out, not_840_out, i7, not_841_out, not_842_out, not_843_out, not_844_out);
  and and_285 (and_285_out, not_845_out, i7, not_846_out, not_847_out, not_848_out, not_849_out);
  and and_286 (and_286_out, i7, not_850_out, not_851_out, not_852_out, i2, not_853_out);
  and and_287 (and_287_out, not_854_out, i7, not_855_out, not_856_out, i3, not_857_out);
  and and_288 (and_288_out, i7, not_858_out, not_859_out, i3, not_860_out);
  and and_289 (and_289_out, not_861_out, i7, not_862_out, not_863_out, i4, i2);
  and and_290 (and_290_out, not_864_out, i7, not_865_out, i4, i3, i2);
  and and_291 (and_291_out, not_866_out, i7, i5, not_867_out, i3, not_868_out);
  and and_292 (and_292_out, not_869_out, i7, i6, not_870_out, i4, not_871_out);
  and and_293 (and_293_out, not_872_out, i7, i6, not_873_out, i4, not_874_out);
  and and_294 (and_294_out, not_875_out, i7, i6, i4, i3, not_876_out);
  and and_295 (and_295_out, not_877_out, i7, i6, i5, not_878_out, i2);
  and and_296 (and_296_out, i7, i6, i5, i3, i2, not_879_out);
  and and_297 (and_297_out, i8, not_880_out, not_881_out, not_882_out, not_883_out, not_884_out);
  and and_298 (and_298_out, i8, not_885_out, not_886_out, i2, not_887_out);
  and and_299 (and_299_out, i8, not_888_out, not_889_out, not_890_out, i3, i2);
  and and_300 (and_300_out, i8, not_891_out, not_892_out, i4, not_893_out, not_894_out);
  and and_301 (and_301_out, i8, not_895_out, not_896_out, i4, not_897_out, i2);
  and and_302 (and_302_out, i8, not_898_out, not_899_out, i5, not_900_out, not_901_out);
  and and_303 (and_303_out, i8, not_902_out, i5, not_903_out, not_904_out, not_905_out);
  and and_304 (and_304_out, i8, not_906_out, not_907_out, i5, i4, i2);
  and and_305 (and_305_out, i8, not_908_out, i5, i4, not_909_out, i2);
  and and_306 (and_306_out, i8, i6, not_910_out, not_911_out, not_912_out);
  and and_307 (and_307_out, i8, i6, not_913_out, not_914_out, i3, not_915_out);
  and and_308 (and_308_out, i8, not_916_out, i6, i4, not_917_out, not_918_out);
  and and_309 (and_309_out, i8, i6, i4, i2, not_919_out);
  and and_310 (and_310_out, i8, i6, not_920_out, i4, i3, i2);
  and and_311 (and_311_out, i8, not_921_out, i6, i5, not_922_out, not_923_out, i2);
  and and_312 (and_312_out, i8, not_924_out, i6, i5, i4, not_925_out);
  and and_313 (and_313_out, i8, i6, i5, i4, not_926_out, not_927_out);
  and and_314 (and_314_out, i8, i7, not_928_out, not_929_out, not_930_out, i2);
  and and_315 (and_315_out, i8, i7, not_931_out, i3, not_932_out);
  and and_316 (and_316_out, i8, i7, not_933_out, not_934_out, i3, i2);
  and and_317 (and_317_out, i8, i7, not_935_out, i4, not_936_out, not_937_out);
  and and_318 (and_318_out, i8, i7, not_938_out, not_939_out, i4, i3, not_940_out);
  and and_319 (and_319_out, i8, i7, i6, not_941_out, not_942_out, not_943_out);
  and and_320 (and_320_out, i8, i7, i6, not_944_out, i3, not_945_out);
  and and_321 (and_321_out, i8, i7, i6, not_946_out, i4, i2);
  and and_322 (and_322_out, i8, i7, i6, i4, i3, i2);
  and and_323 (and_323_out, not_947_out, not_948_out, not_949_out, not_950_out, not_951_out, i2);
  and and_324 (and_324_out, not_952_out, not_953_out, not_954_out, not_955_out, i3, not_956_out);
  and and_325 (and_325_out, not_957_out, not_958_out, i3, i2, not_959_out);
  and and_326 (and_326_out, not_960_out, not_961_out, i4, not_962_out, not_963_out);
  and and_327 (and_327_out, not_964_out, not_965_out, i4, not_966_out, not_967_out);
  and and_328 (and_328_out, not_968_out, not_969_out, not_970_out, not_971_out, i4, i3);
  and and_329 (and_329_out, not_972_out, not_973_out, not_974_out, i4, i3, not_975_out);
  and and_330 (and_330_out, not_976_out, not_977_out, i5, not_978_out, not_979_out);
  and and_331 (and_331_out, not_980_out, i5, not_981_out, not_982_out, not_983_out);
  and and_332 (and_332_out, not_984_out, not_985_out, i5, not_986_out, not_987_out, i2);
  and and_333 (and_333_out, not_988_out, not_989_out, i5, not_990_out, i2, not_991_out);
  and and_334 (and_334_out, not_992_out, not_993_out, i5, not_994_out, i3, i2);
  and and_335 (and_335_out, not_995_out, not_996_out, i5, i4, not_997_out);
  and and_336 (and_336_out, not_998_out, not_999_out, i6, not_1000_out, not_1001_out, not_1002_out);
  and and_337 (and_337_out, not_1003_out, not_1004_out, i6, not_1005_out, not_1006_out, i2);
  and and_338 (and_338_out, not_1007_out, i6, not_1008_out, not_1009_out, i2);
  and and_339 (and_339_out, not_1010_out, i6, not_1011_out, not_1012_out, not_1013_out, i2);
  and and_340 (and_340_out, not_1014_out, i6, not_1015_out, i3, not_1016_out);
  and and_341 (and_341_out, not_1017_out, not_1018_out, i6, i5, not_1019_out, i3);
  and and_342 (and_342_out, not_1020_out, i6, i5, not_1021_out, i3, i2);
  and and_343 (and_343_out, not_1022_out, not_1023_out, i6, i5, i4, i2);
  and and_344 (and_344_out, not_1024_out, i6, i5, i4, not_1025_out, i2);
  and and_345 (and_345_out, not_1026_out, i7, not_1027_out, not_1028_out, not_1029_out, not_1030_out);
  and and_346 (and_346_out, i7, not_1031_out, not_1032_out, i2, not_1033_out);
  and and_347 (and_347_out, not_1034_out, i7, not_1035_out, not_1036_out, i4, i2);
  and and_348 (and_348_out, not_1037_out, i7, not_1038_out, i4, i3, i2);
  and and_349 (and_349_out, not_1039_out, i7, not_1040_out, i5, i3, not_1041_out);
  and and_350 (and_350_out, not_1042_out, i7, i5, i4, i3, not_1043_out);
  and and_351 (and_351_out, i7, i6, not_1044_out, not_1045_out, not_1046_out);
  and and_352 (and_352_out, not_1047_out, i7, i6, not_1048_out, i2);
  and and_353 (and_353_out, not_1049_out, i7, i6, not_1050_out, i4, not_1051_out);
  and and_354 (and_354_out, not_1052_out, i7, i6, i5, not_1053_out, not_1054_out);
  and and_355 (and_355_out, i7, i6, i5, i3, not_1055_out);
  and and_356 (and_356_out, i8, not_1056_out, not_1057_out, not_1058_out, not_1059_out, not_1060_out);
  and and_357 (and_357_out, i8, not_1061_out, not_1062_out, not_1063_out, not_1064_out);
  and and_358 (and_358_out, i8, not_1065_out, not_1066_out, not_1067_out, not_1068_out);
  and and_359 (and_359_out, i8, not_1069_out, not_1070_out, not_1071_out, i3, i2);
  and and_360 (and_360_out, i8, not_1072_out, not_1073_out, i4, i2);
  and and_361 (and_361_out, i8, not_1074_out, not_1075_out, i5, not_1076_out, not_1077_out);
  and and_362 (and_362_out, i8, not_1078_out, not_1079_out, i5, not_1080_out, not_1081_out);
  and and_363 (and_363_out, i8, not_1082_out, i5, not_1083_out, not_1084_out);
  and and_364 (and_364_out, i8, not_1085_out, i5, not_1086_out, not_1087_out);
  and and_365 (and_365_out, i8, not_1088_out, i5, not_1089_out, not_1090_out, not_1091_out);
  and and_366 (and_366_out, i8, not_1092_out, i5, i4, i2);
  and and_367 (and_367_out, i8, not_1093_out, i6, not_1094_out, i3, not_1095_out);
  and and_368 (and_368_out, i8, not_1096_out, i6, i4, not_1097_out);
  and and_369 (and_369_out, i8, i6, i4, not_1098_out, not_1099_out);
  and and_370 (and_370_out, i8, not_1100_out, i6, not_1101_out, i4, i3);
  and and_371 (and_371_out, i8, i6, i5, not_1102_out, not_1103_out, i2);
  and and_372 (and_372_out, i8, i6, i5, i4, not_1104_out);
  and and_373 (and_373_out, i8, i7, not_1105_out, not_1106_out, not_1107_out, i2);
  and and_374 (and_374_out, i8, i7, not_1108_out, not_1109_out, i3, i2);
  and and_375 (and_375_out, i8, i7, not_1110_out, not_1111_out, i4, i3, not_1112_out);
  and and_376 (and_376_out, i8, i7, not_1113_out, i4, i3, not_1114_out);
  and and_377 (and_377_out, i8, i7, i6, not_1115_out, not_1116_out, not_1117_out);
  and and_378 (and_378_out, i8, i7, i6, not_1118_out, i4, i2);
  and and_379 (and_379_out, i8, i7, i6, i5, i3, not_1119_out);
  and and_380 (and_380_out, i8, i7, i6, i5, i4, i3);
  or or_1 (or_1_out, and_233_out, and_234_out, and_235_out, and_236_out, and_237_out, and_238_out, and_239_out, and_240_out, and_241_out, and_242_out, and_243_out, and_244_out, and_245_out, and_246_out, and_247_out, and_248_out, and_249_out);
  or or_2 (or_2_out, and_250_out, and_251_out, and_252_out, and_253_out, and_254_out, and_255_out, and_256_out, and_257_out, and_258_out, and_259_out, and_260_out, and_261_out, and_262_out, and_263_out, and_264_out, and_265_out);
  or or_3 (or_3_out, and_1_out, and_2_out, and_3_out, and_4_out, and_5_out, and_6_out, and_7_out, and_8_out, and_9_out, and_10_out, and_11_out, and_12_out, and_13_out, and_14_out, and_15_out, and_16_out, and_17_out, and_18_out, and_19_out, and_20_out, and_21_out, and_22_out, and_23_out);
  or or_4 (or_4_out, and_24_out, and_25_out, and_26_out, and_27_out, and_28_out, and_29_out, and_30_out, and_31_out, and_32_out, and_33_out, and_34_out, and_35_out, and_36_out, and_37_out, and_38_out, and_39_out, and_40_out, and_41_out, and_42_out, and_43_out, and_44_out, and_45_out, and_46_out);
  or or_5 (or_5_out, and_47_out, and_48_out, and_49_out, and_50_out, and_51_out, and_52_out, and_53_out, and_54_out, and_55_out, and_56_out, and_57_out, and_58_out, and_59_out, and_60_out, and_61_out, and_62_out, and_63_out, and_64_out, and_65_out, and_66_out, and_67_out, and_68_out, and_69_out);
  or or_6 (or_6_out, and_70_out, and_71_out, and_72_out, and_73_out, and_74_out, and_75_out, and_76_out, and_77_out, and_78_out, and_79_out, and_80_out, and_81_out, and_82_out, and_83_out, and_84_out, and_85_out, and_86_out, and_87_out, and_88_out, and_89_out, and_90_out, and_91_out, and_92_out, and_93_out, and_94_out, and_95_out, and_96_out, and_97_out, and_98_out, and_99_out, and_100_out, and_101_out);
  or or_7 (or_7_out, and_102_out, and_103_out, and_104_out, and_105_out, and_106_out, and_107_out, and_108_out, and_109_out, and_110_out, and_111_out, and_112_out, and_113_out, and_114_out, and_115_out, and_116_out, and_117_out, and_118_out, and_119_out, and_120_out, and_121_out, and_122_out, and_123_out, and_124_out, and_125_out, and_126_out, and_127_out, and_128_out, and_129_out, and_130_out, and_131_out, and_132_out, and_133_out);
  or or_8 (C, and_134_out, and_135_out, i1, and_136_out, and_137_out, and_138_out, and_139_out, and_140_out, and_141_out, and_142_out, and_143_out, and_144_out, and_145_out, and_146_out, and_147_out, and_148_out, and_149_out, and_150_out, and_151_out, and_152_out, and_153_out, and_154_out, and_155_out, and_156_out, and_157_out, and_158_out, and_159_out, and_160_out, and_161_out, and_162_out, and_163_out);
  or or_9 (or_9_out, and_164_out, and_165_out, and_166_out, and_167_out, and_168_out, and_169_out, and_170_out, and_171_out, and_172_out, and_173_out, and_174_out, and_175_out, and_176_out, and_177_out, and_178_out, and_179_out, and_180_out, and_181_out, and_182_out, and_183_out, and_184_out, and_185_out, and_186_out);
  or or_10 (or_10_out, and_187_out, and_188_out, and_189_out, and_190_out, and_191_out, and_192_out, and_193_out, and_194_out, and_195_out, and_196_out, and_197_out, and_198_out, and_199_out, and_200_out, and_201_out, and_202_out, and_203_out, and_204_out, and_205_out, and_206_out, and_207_out, and_208_out, and_209_out);
  or or_11 (or_11_out, and_210_out, and_211_out, and_212_out, and_213_out, and_214_out, and_215_out, and_216_out, and_217_out, and_218_out, and_219_out, and_220_out, and_221_out, and_222_out, and_223_out, and_224_out, and_225_out, and_226_out, and_227_out, and_228_out, and_229_out, and_230_out, and_231_out, and_232_out);
  or or_12 (E, or_1_out, or_2_out);
  or or_13 (or_13_out, and_266_out, and_267_out, and_268_out, and_269_out, and_270_out, and_271_out, and_272_out, and_273_out, and_274_out, and_275_out, and_276_out, and_277_out, and_278_out, and_279_out, and_280_out, and_281_out, and_282_out, and_283_out, and_284_out, and_285_out, and_286_out, and_287_out, and_288_out, and_289_out, and_290_out, and_291_out, and_292_out, and_293_out, and_294_out);
  or or_14 (or_14_out, and_295_out, and_296_out, and_297_out, and_298_out, and_299_out, and_300_out, and_301_out, and_302_out, and_303_out, and_304_out, and_305_out, and_306_out, and_307_out, and_308_out, and_309_out, and_310_out, and_311_out, and_312_out, and_313_out, and_314_out, and_315_out, and_316_out, and_317_out, and_318_out, and_319_out, and_320_out, and_321_out, and_322_out);
  or or_15 (or_15_out, and_323_out, and_324_out, and_325_out, and_326_out, and_327_out, and_328_out, and_329_out, and_330_out, and_331_out, and_332_out, and_333_out, and_334_out, and_335_out, and_336_out, and_337_out, and_338_out, and_339_out, and_340_out, and_341_out, and_342_out, and_343_out, and_344_out, and_345_out, and_346_out, and_347_out, and_348_out, and_349_out, and_350_out, and_351_out);
  or or_16 (or_16_out, and_352_out, and_353_out, and_354_out, and_355_out, and_356_out, and_357_out, and_358_out, and_359_out, and_360_out, and_361_out, and_362_out, and_363_out, and_364_out, and_365_out, and_366_out, and_367_out, and_368_out, and_369_out, and_370_out, and_371_out, and_372_out, and_373_out, and_374_out, and_375_out, and_376_out, and_377_out, and_378_out, and_379_out, and_380_out);
  or or_17 (A, or_3_out, or_4_out, or_5_out);
  or or_18 (B, or_6_out, or_7_out);
  or or_19 (D, or_9_out, or_10_out, or_11_out);
  or or_20 (F, or_13_out, or_14_out);
  or or_21 (G, or_15_out, or_16_out);
endmodule

module dispbyte (
  input  clock_bit,
  input  [7:0] in_2,
  output [7:0] out_3
);

  wire and_1_out, and_2_out, and_3_out, and_4_out, and_5_out, and_6_out, and_7_out, and_8_out, and_9_out,
       and_10_out, and_11_out, and_12_out, and_13_out, and_14_out, and_15_out, and_16_out, not_1_out,
       not_2_out, not_3_out, not_4_out, not_5_out, not_6_out, not_7_out, not_8_out, s_r_ff_1_q, s_r_ff_2_q,
       s_r_ff_3_q, s_r_ff_4_q, s_r_ff_5_q, s_r_ff_6_q, s_r_ff_7_q, s_r_ff_8_q;

  not not_1 (not_1_out, in_2[0]);
  not not_2 (not_2_out, in_2[1]);
  not not_3 (not_3_out, in_2[2]);
  not not_4 (not_4_out, in_2[3]);
  not not_5 (not_5_out, in_2[4]);
  not not_6 (not_6_out, in_2[5]);
  not not_7 (not_7_out, in_2[6]);
  not not_8 (not_8_out, in_2[7]);
  and and_1 (and_1_out, 1'b1, 1'b1, in_2[0]);
  and and_2 (and_2_out, not_1_out, 1'b1, 1'b1);
  and and_3 (and_3_out, 1'b1, 1'b1, in_2[1]);
  and and_4 (and_4_out, not_2_out, 1'b1, 1'b1);
  and and_5 (and_5_out, 1'b1, 1'b1, in_2[2]);
  and and_6 (and_6_out, not_3_out, 1'b1, 1'b1);
  and and_7 (and_7_out, 1'b1, 1'b1, in_2[3]);
  and and_8 (and_8_out, not_4_out, 1'b1, 1'b1);
  and and_9 (and_9_out, 1'b1, 1'b1, in_2[4]);
  and and_10 (and_10_out, not_5_out, 1'b1, 1'b1);
  and and_11 (and_11_out, 1'b1, 1'b1, in_2[5]);
  and and_12 (and_12_out, not_6_out, 1'b1, 1'b1);
  and and_13 (and_13_out, 1'b1, 1'b1, in_2[6]);
  and and_14 (and_14_out, not_7_out, 1'b1, 1'b1);
  and and_15 (and_15_out, 1'b1, 1'b1, in_2[7]);
  and and_16 (and_16_out, not_8_out, 1'b1, 1'b1);
  S_R_Flip_Flop s_r_ff_1 (.S(and_1_out), .R(and_2_out), .clk(clock_bit), .Q(s_r_ff_1_q));  // open: reset, Qn, preset
  S_R_Flip_Flop s_r_ff_2 (.S(and_3_out), .R(and_4_out), .clk(clock_bit), .Q(s_r_ff_2_q));  // open: reset, Qn, preset
  S_R_Flip_Flop s_r_ff_3 (.S(and_5_out), .R(and_6_out), .clk(clock_bit), .Q(s_r_ff_3_q));  // open: reset, Qn, preset
  S_R_Flip_Flop s_r_ff_4 (.S(and_7_out), .R(and_8_out), .clk(clock_bit), .Q(s_r_ff_4_q));  // open: reset, Qn, preset
  S_R_Flip_Flop s_r_ff_5 (.S(and_9_out), .R(and_10_out), .clk(clock_bit), .Q(s_r_ff_5_q));  // open: reset, Qn, preset
  S_R_Flip_Flop s_r_ff_6 (.S(and_11_out), .R(and_12_out), .clk(clock_bit), .Q(s_r_ff_6_q));  // open: reset, Qn, preset
  S_R_Flip_Flop s_r_ff_7 (.S(and_13_out), .R(and_14_out), .clk(clock_bit), .Q(s_r_ff_7_q));  // open: reset, Qn, preset
  S_R_Flip_Flop s_r_ff_8 (.S(and_15_out), .R(and_16_out), .clk(clock_bit), .Q(s_r_ff_8_q));  // open: reset, Qn, preset
  and and_17 (out_3[0], s_r_ff_1_q, 1'b1, 1'b1);
  and and_18 (out_3[1], s_r_ff_2_q, 1'b1, 1'b1);
  and and_19 (out_3[2], s_r_ff_3_q, 1'b1, 1'b1);
  and and_20 (out_3[3], s_r_ff_4_q, 1'b1, 1'b1);
  and and_21 (out_3[4], s_r_ff_5_q, 1'b1, 1'b1);
  and and_22 (out_3[5], s_r_ff_6_q, 1'b1, 1'b1);
  and and_23 (out_3[6], s_r_ff_7_q, 1'b1, 1'b1);
  and and_24 (out_3[7], s_r_ff_8_q, 1'b1, 1'b1);

  // Notes on the sheet:
  //   address
  //   R/W, 1=W 0=R
endmodule
